// Logisim project cpuv2.circ as structural Verilog: 1 circuit, main circuit main
module main (
  output [7:0] data_bus,
  output [15:0] address_bus,
  output clk_pin
);

  wire adder_1_cout, ALU_ADD, ALU_ADO, ALU_CMP, ALU_NAND, ALU_NOR, ALU_SBO, ALU_SUB, and_1_out, and_2_out,
       and_3_out, and_4_out, and_5_out, and_6_out, and_7_out, and_9_out, and_10_out, and_11_out, and_14_out,
       and_15_out, and_16_out, and_17_out, and_18_out, and_19_out, and_20_out, and_21_out, and_22_out,
       and_23_out, and_24_out, and_25_out, and_26_out, and_27_out, and_28_out, and_29_out, and_30_out,
       and_31_out, and_32_out, and_33_out, and_34_out, and_35_out, and_36_out, and_37_out, and_38_out,
       and_39_out, and_40_out, and_41_out, and_42_out, and_43_out, and_44_out, and_45_out, and_46_out,
       and_47_out, and_48_out, and_49_out, and_50_out, and_51_out, and_52_out, and_53_out, and_54_out,
       and_55_out, and_56_out, and_57_out, and_58_out, and_59_out, and_61_out, and_62_out, and_63_out,
       and_64_out, and_65_out, and_66_out, and_67_out, and_68_out, and_69_out, and_70_out, and_71_out,
       and_72_out, and_73_out, and_74_out, and_75_out, and_76_out, and_77_out, and_78_out, and_79_out,
       and_80_out, and_81_out, and_82_out, and_83_out, and_84_out, and_85_out, and_86_out, and_87_out,
       and_88_out, and_89_out, and_90_out, and_91_out, and_92_out, and_93_out, and_94_out, and_95_out,
       and_96_out, and_97_out, and_98_out, and_99_out, and_100_out, and_101_out, and_102_out, and_103_out,
       and_104_out, and_105_out, and_106_out, and_107_out, and_108_out, and_109_out, and_110_out,
       and_111_out, and_112_out, and_113_out, and_114_out, and_115_out, and_116_out, and_117_out,
       and_118_out, and_119_out, and_120_out, and_121_out, and_122_out, and_123_out, and_124_out,
       and_125_out, and_126_out, and_127_out, and_128_out, and_129_out, and_130_out, and_131_out,
       and_132_out, and_133_out, and_134_out, and_135_out, and_136_out, and_137_out, and_138_out,
       and_139_out, and_140_out, and_141_out, and_142_out, and_143_out, and_144_out, and_145_out,
       and_146_out, and_147_out, and_148_out, and_149_out, and_150_out, and_151_out, and_152_out,
       and_153_out, and_154_out, and_155_out, and_156_out, and_157_out, and_158_out, and_159_out,
       and_160_out, and_161_out, and_162_out, and_163_out, and_164_out, and_165_out, and_166_out,
       and_167_out, and_168_out, and_169_out, and_170_out, and_171_out, and_172_out, and_173_out,
       and_174_out, and_175_out, and_176_out, and_177_out, and_178_out, and_179_out, and_180_out,
       and_181_out, and_182_out, and_183_out, and_184_out, and_185_out, and_186_out, and_187_out,
       and_188_out, and_189_out, and_190_out, and_191_out, and_192_out, and_193_out, and_194_out,
       and_195_out, and_196_out, and_197_out, and_198_out, and_199_out, and_200_out, and_201_out,
       and_202_out, and_203_out, and_204_out, and_205_out, and_206_out, and_207_out, and_208_out,
       buffer_7_out, button_2_out, CLEAR_FG, clock_1_out, comparator_1_eq, comparator_2_eq, COND_INVERT,
       counter_1_carry, d_ff_1_q, d_ff_2_q, d_ff_3_q, d_ff_4_q, d_ff_5_q, d_ff_6_q, d_ff_8_qn, halt, INT0,
       INT1, INT2, INT3, INT4, INT5, INT6, INT7, INT_DISABLE, INT_LOCK, INT_RET_TO_ADDR, INT_TRIGGER, IO_IN,
       IO_OUT, memory_read, memory_write, multiplexer_1_out, nand_1_out, nand_2_out, nand_3_out, nand_4_out,
       nand_5_out, nand_6_out, nand_7_out, nand_8_out, nor_1_out, nor_2_out, nor_3_out, nor_4_out, nor_5_out,
       nor_6_out, nor_7_out, nor_8_out, not_1_out, not_2_out, not_3_out, not_4_out, not_5_out, not_6_out,
       not_7_out, not_8_out, not_9_out, not_10_out, not_11_out, not_12_out, not_13_out, not_14_out,
       not_15_out, not_16_out, not_17_out, not_18_out, not_19_out, not_20_out, not_21_out, not_22_out,
       not_23_out, not_24_out, not_25_out, not_26_out, not_27_out, not_28_out, not_29_out, not_30_out,
       not_31_out, not_32_out, not_33_out, not_34_out, not_35_out, not_36_out, not_37_out, not_38_out,
       not_39_out, not_40_out, not_41_out, not_42_out, not_43_out, not_44_out, not_45_out, not_46_out,
       not_47_out, not_48_out, not_49_out, not_50_out, not_51_out, not_52_out, not_53_out, not_54_out,
       not_55_out, not_56_out, not_57_out, not_58_out, not_59_out, not_60_out, not_61_out, not_62_out,
       not_63_out, not_64_out, not_65_out, not_66_out, not_67_out, not_68_out, not_69_out, not_70_out,
       not_71_out, not_72_out, not_73_out, not_74_out, not_75_out, not_76_out, not_77_out, not_78_out,
       not_79_out, not_80_out, not_81_out, not_82_out, not_83_out, not_84_out, not_85_out, not_86_out,
       not_87_out, not_88_out, not_89_out, not_90_out, not_91_out, not_92_out, not_93_out, not_94_out,
       not_95_out, not_96_out, not_97_out, not_98_out, not_99_out, not_100_out, not_101_out, not_102_out,
       not_103_out, not_104_out, not_105_out, not_106_out, not_107_out, not_108_out, not_109_out,
       not_110_out, not_111_out, not_112_out, not_113_out, not_114_out, or_1_out, or_2_out, or_3_out,
       or_4_out, or_5_out, or_6_out, or_7_out, or_8_out, or_9_out, or_10_out, or_11_out, or_12_out,
       or_13_out, or_14_out, or_15_out, or_16_out, or_17_out, or_18_out, or_19_out, or_20_out, or_21_out,
       or_22_out, or_23_out, or_24_out, or_25_out, or_27_out, or_28_out, or_29_out, or_30_out, or_31_out,
       or_32_out, or_33_out, or_34_out, or_35_out, or_36_out, or_37_out, or_40_out, or_41_out, or_42_out,
       or_43_out, or_44_out, or_45_out, or_46_out, or_47_out, or_48_out, or_49_out, or_50_out, or_51_out,
       or_52_out, or_53_out, or_54_out, or_55_out, or_58_out, or_59_out, or_60_out, or_61_out, or_62_out,
       or_63_out, or_64_out, or_65_out, or_66_out, or_67_out, or_68_out, or_69_out, or_70_out, or_71_out,
       or_72_out, pc_count, PC_FLUSH, PC_FLUSH_COND, pc_load, pc_out_address_bus, pull_resistor_1_node,
       pull_resistor_26_node, pull_resistor_82_node, pull_resistor_83_node, pull_resistor_84_node,
       pull_resistor_85_node, PUT_A_ADDR, PUT_ALUOUT_DB, PUT_B_ADDR, PUT_DB_FG, PUT_FG_DB, PUT_IADR_ADDR,
       PUT_IIMM_DB, PUT_IR0_DB, PUT_IR1_DB, PUT_SP_ADDR, reset, s_r_ff_2_qn, s_r_ff_3_q, s_r_ff_4_q,
       s_r_ff_5_q, s_r_ff_6_q, s_r_ff_7_q, s_r_ff_8_q, s_r_ff_9_q, s_r_ff_10_q, SAVE_ADDR_A, SAVE_ADDR_B,
       SAVE_ADDR_SP, SAVE_DB_ALUA, SAVE_DB_ALUB, SAVE_DB_IR0, SAVE_DB_IR1, SAVE_IH, SAVE_PCB, SAVE_PCB_IF_EQ,
       SAVE_PCB_IF_OF, SAVE_PCB_IF_Z, SP_DOWN, SP_UP, subtractor_1_bout, tout, transistor_1_out,
       transistor_2_out, transistor_3_out, transistor_4_out, transistor_5_out, transistor_6_out,
       transistor_7_out, transistor_8_out, transistor_9_out, transistor_10_out, transistor_11_out,
       transistor_12_out, transistor_13_out, transistor_14_out, transistor_15_out, transistor_112_out,
       transistor_161_out, transistor_162_out, transistor_163_out, transistor_164_out, transistor_165_out,
       transistor_166_out, transistor_167_out, transistor_168_out, transistor_169_out, transistor_170_out,
       transistor_171_out, transistor_172_out, transistor_173_out, transistor_174_out, transistor_175_out,
       transistor_185_out, transistor_186_out, transistor_187_out, transistor_188_out, transistor_189_out,
       transistor_190_out, transistor_191_out, transistor_192_out, transistor_193_out, transistor_194_out,
       transistor_195_out, transistor_196_out, transistor_197_out, transistor_198_out, transistor_199_out,
       transistor_201_out, transistor_202_out, transistor_203_out, transistor_204_out, transistor_205_out,
       transistor_206_out, transistor_207_out, transistor_208_out, transistor_209_out, transistor_210_out,
       transistor_211_out, transistor_212_out, transistor_213_out, transistor_214_out, transistor_215_out,
       transistor_241_out, transistor_242_out, transistor_243_out, transistor_244_out, transistor_245_out,
       transistor_246_out, transistor_247_out, transistor_248_out, transistor_249_out, transistor_250_out,
       transistor_251_out, transistor_252_out, transistor_253_out, transistor_254_out, transistor_255_out,
       transistor_301_out, transistor_302_out, transistor_303_out, transistor_304_out, transistor_305_out,
       transistor_306_out, transistor_307_out, transistor_308_out, transistor_333_out, transistor_334_out,
       transistor_335_out, transistor_336_out, transistor_337_out, transistor_338_out, transistor_339_out,
       transistor_340_out, xnor_1_out, xnor_2_out, xnor_3_out, xnor_4_out, xnor_5_out, xnor_6_out,
       xnor_7_out, xnor_8_out, xnor_9_out, xnor_10_out, xnor_11_out, xnor_12_out, xnor_13_out, xnor_14_out,
       xnor_15_out, xnor_16_out, xnor_17_out, xnor_18_out, xnor_19_out, xnor_20_out, xnor_21_out,
       xnor_22_out, xnor_23_out, xnor_24_out, xnor_25_out, xnor_26_out, xnor_27_out, xnor_28_out,
       xnor_29_out, xnor_30_out, xnor_31_out, xnor_32_out, xnor_33_out, xnor_34_out, xnor_35_out,
       xnor_36_out, xnor_37_out, xnor_38_out, xnor_39_out, xnor_40_out, xnor_41_out, xnor_42_out,
       xnor_43_out, xnor_44_out, xnor_45_out, xnor_46_out, xnor_47_out, xnor_48_out, xnor_49_out,
       xnor_50_out, xnor_51_out, xnor_52_out, xnor_53_out, xnor_54_out, xnor_55_out, xnor_56_out,
       xnor_57_out, xnor_58_out, xnor_59_out, xnor_60_out, xnor_61_out, xnor_62_out, xnor_63_out,
       xnor_64_out, xnor_65_out, xnor_66_out, xnor_67_out, xnor_68_out, xnor_69_out, xnor_70_out,
       xnor_71_out, xnor_72_out, xnor_73_out, xnor_74_out, xnor_75_out, xnor_76_out, xnor_77_out,
       xnor_78_out, xnor_79_out, xnor_80_out, xor_1_out, xor_2_out, xor_3_out, xor_4_out, xor_5_out,
       xor_6_out, xor_7_out, xor_8_out, xor_9_out, xor_10_out, xor_11_out, xor_12_out, xor_13_out, xor_14_out;
  wire [2:0] counter_1_q;
  wire [3:0] fg, instruction_reg0, instruction_reg1;
  wire [7:0] adder_1_out, alua_q, alub_q, aluout_q, i0_q, i2_q, or_38_out, or_39_out, or_56_out, or_57_out,
       pull_resistor_27_node, pull_resistor_103_node, pull_resistor_111_node, pull_resistor_121_node,
       pull_resistor_129_node, r0_q, r1_q, r2_q, r3_q, r4_q, r5_q, r6_q, r7_q, r8_q, r9_q, r10_q, r11_q,
       r12_q, r13_q, r14_q, r15_q, ram_1_dout, register_2_q, register_4_q, register_5_q, register_6_q,
       register_7_q, rom_1_data, s_r_ff_11_q, subtractor_1_out, tcnt_q, tpsc_q, transistor_233_out;
  wire [15:0] controlled_buffer_1_out, ih, pc_q, register_1_q, register_3_q, sp_q;
  wire [31:0] MC1_data, MC2_data;

  Pull_Resistor pull_resistor_1 (.node(pull_resistor_1_node));
  // Switch switch_1: pin names not known; wires that end beside it: 1'b1, pull_resistor_1_node, reset
  Pull_Resistor pull_resistor_2 (.node(address_bus[0]));
  Pull_Resistor pull_resistor_3 (.node(address_bus[1]));
  Pull_Resistor pull_resistor_4 (.node(address_bus[2]));
  Pull_Resistor pull_resistor_5 (.node(address_bus[3]));
  Pull_Resistor pull_resistor_6 (.node(address_bus[4]));
  Pull_Resistor pull_resistor_7 (.node(address_bus[5]));
  Pull_Resistor pull_resistor_8 (.node(address_bus[6]));
  Pull_Resistor pull_resistor_9 (.node(address_bus[7]));
  Pull_Resistor pull_resistor_10 (.node(address_bus[8]));
  Pull_Resistor pull_resistor_11 (.node(address_bus[9]));
  Pull_Resistor pull_resistor_12 (.node(address_bus[10]));
  Pull_Resistor pull_resistor_13 (.node(address_bus[11]));
  Pull_Resistor pull_resistor_14 (.node(address_bus[12]));
  Pull_Resistor pull_resistor_15 (.node(address_bus[13]));
  Pull_Resistor pull_resistor_16 (.node(address_bus[14]));
  Pull_Resistor pull_resistor_17 (.node(address_bus[15]));
  Pull_Resistor pull_resistor_18 (.node(data_bus[0]));
  Pull_Resistor pull_resistor_19 (.node(data_bus[1]));
  Pull_Resistor pull_resistor_20 (.node(data_bus[2]));
  Pull_Resistor pull_resistor_21 (.node(data_bus[3]));
  Pull_Resistor pull_resistor_22 (.node(data_bus[4]));
  Pull_Resistor pull_resistor_23 (.node(data_bus[5]));
  Pull_Resistor pull_resistor_24 (.node(data_bus[6]));
  Pull_Resistor pull_resistor_25 (.node(data_bus[7]));
  Register #(.trigger("falling"), .width(16)) register_1 (
    .D(address_bus), .en(SAVE_PCB), .clk(clk_pin), .Q(register_1_q), .clr(reset));
  not not_1 (not_1_out, INT_DISABLE);
  Button button_1 (.out(reset));
  Button button_2 (.out(button_2_out));
  Clock clock_1 (.out(clock_1_out));
  and and_1 (and_1_out, clock_1_out, pull_resistor_1_node);
  or or_1 (or_1_out, d_ff_5_q, reset);
  not not_2 (not_2_out, d_ff_4_q);
  ROM #(.addrWidth(15)) rom_1 (.addr(address_bus[14:0]), .data(rom_1_data));
  RAM #(.addrWidth(15), .enables("line"), .trigger("falling")) ram_1 (
    .addr(address_bus[14:0]), .we(and_7_out), .clk(and_9_out), .din(data_bus), .dout(ram_1_dout));
  or or_2 (or_2_out, PC_FLUSH, pc_count, INT_LOCK);
  assign controlled_buffer_1_out = not_3_out ? register_1_q : 16'bz;  // Controlled_Buffer controlled_buffer_1
  not not_3 (not_3_out, and_2_out);
  and and_2 (and_2_out, INT_TRIGGER, not_1_out);
  and and_3 (and_3_out, clk_pin, or_3_out);
  not not_4 (not_4_out, d_ff_4_q);
  or or_3 (or_3_out, not_4_out, or_7_out);
  Counter #(.max('h7), .width(3)) counter_1 (
    .clr(xor_3_out), .up(1'b1), .clk(and_4_out), .carry(counter_1_carry), .Q(counter_1_q));  // open: load, count, D
  and and_4 (and_4_out, clk_pin, d_ff_4_q);
  Counter #(.max('hffff), .width(16)) pc (
    .clr(reset), .load(or_4_out), .up(1'b1), .clk(or_2_out), .D(controlled_buffer_1_out), .carry(halt),
    .Q(pc_q));  // open: count
  or or_4 (or_4_out, PC_FLUSH, INT_LOCK);
  assign controlled_buffer_1_out = and_2_out ? ih : 16'bz;  // Controlled_Buffer controlled_buffer_2
  or or_5 (or_5_out, button_2_out, and_1_out);
  D_Flip_Flop d_ff_1 (.D(1'b1), .clk(and_3_out), .Q(d_ff_1_q), .reset(or_1_out));  // open: Qn, preset
  or or_6 (or_6_out, or_1_out, reset);
  or or_7 (or_7_out, transistor_112_out, counter_1_carry);
  not not_5 (not_5_out, address_bus[15]);
  not not_6 (not_6_out, fg[3]);
  D_Flip_Flop d_ff_2 (.D(d_ff_1_q), .clk(and_3_out), .Q(d_ff_2_q), .reset(or_1_out));  // open: Qn, preset
  xor xor_1 (xor_1_out, d_ff_1_q, d_ff_2_q);
  Register #(.trigger("falling")) i0 (.D(data_bus), .en(xor_1_out), .clk(clk_pin), .Q(i0_q), .clr(or_6_out));
  and and_5 (and_5_out, not_5_out, memory_read);
  and and_6 (and_6_out, address_bus[15], memory_read);
  and and_7 (and_7_out, address_bus[15], memory_write);
  and and_8 (clk_pin, or_5_out, not_6_out);
  D_Flip_Flop d_ff_3 (.D(d_ff_2_q), .clk(and_3_out), .Q(d_ff_3_q), .reset(or_1_out));  // open: Qn, preset
  xor xor_2 (xor_2_out, d_ff_2_q, d_ff_3_q);
  Register #(.trigger("falling")) i1 (
    .D(data_bus), .en(xor_2_out), .clk(clk_pin), .Q({instruction_reg1, instruction_reg0}), .clr(or_6_out));
  not not_7 (not_7_out, PUT_IIMM_DB);
  xnor xnor_1 (xnor_1_out, address_bus[0], 1'b1);
  Transistor transistor_1 (.in(1'b1), .out(transistor_1_out), .gate(xnor_1_out));
  xnor xnor_2 (xnor_2_out, address_bus[1], 1'b1);
  Transistor transistor_2 (.in(transistor_1_out), .out(transistor_2_out), .gate(xnor_2_out));
  xnor xnor_3 (xnor_3_out, address_bus[2], 1'b1);
  Transistor transistor_3 (.in(transistor_2_out), .out(transistor_3_out), .gate(xnor_3_out));
  xnor xnor_4 (xnor_4_out, address_bus[3], 1'b1);
  Transistor transistor_4 (.in(transistor_3_out), .out(transistor_4_out), .gate(xnor_4_out));
  xnor xnor_5 (xnor_5_out, address_bus[4], 1'b1);
  Transistor transistor_5 (.in(transistor_4_out), .out(transistor_5_out), .gate(xnor_5_out));
  xnor xnor_6 (xnor_6_out, address_bus[5], 1'b1);
  Transistor transistor_6 (.in(transistor_5_out), .out(transistor_6_out), .gate(xnor_6_out));
  xnor xnor_7 (xnor_7_out, address_bus[6], 1'b1);
  Transistor transistor_7 (.in(transistor_6_out), .out(transistor_7_out), .gate(xnor_7_out));
  xnor xnor_8 (xnor_8_out, address_bus[7], 1'b1);
  Transistor transistor_8 (.in(transistor_7_out), .out(transistor_8_out), .gate(xnor_8_out));
  xnor xnor_9 (xnor_9_out, address_bus[8], 1'b1);
  Transistor transistor_9 (.in(transistor_8_out), .out(transistor_9_out), .gate(xnor_9_out));
  xnor xnor_10 (xnor_10_out, address_bus[9], 1'b1);
  Transistor transistor_10 (.in(transistor_9_out), .out(transistor_10_out), .gate(xnor_10_out));
  xnor xnor_11 (xnor_11_out, address_bus[10], 1'b1);
  Transistor transistor_11 (.in(transistor_10_out), .out(transistor_11_out), .gate(xnor_11_out));
  xnor xnor_12 (xnor_12_out, address_bus[11], 1'b1);
  Transistor transistor_12 (.in(transistor_11_out), .out(transistor_12_out), .gate(xnor_12_out));
  xnor xnor_13 (xnor_13_out, address_bus[12], 1'b1);
  Transistor transistor_13 (.in(transistor_12_out), .out(transistor_13_out), .gate(xnor_13_out));
  xnor xnor_14 (xnor_14_out, address_bus[13], 1'b1);
  Transistor transistor_14 (.in(transistor_13_out), .out(transistor_14_out), .gate(xnor_14_out));
  xnor xnor_15 (xnor_15_out, address_bus[14], 1'b1);
  Transistor transistor_15 (.in(transistor_14_out), .out(transistor_15_out), .gate(xnor_15_out));
  xnor xnor_16 (xnor_16_out, address_bus[15], 1'b1);
  Pull_Resistor pull_resistor_26 (.node(pull_resistor_26_node));
  Transistor transistor_16 (.in(transistor_15_out), .out(pull_resistor_26_node), .gate(xnor_16_out));
  Pull_Resistor pull_resistor_27 (.node(pull_resistor_27_node[0]));
  Pull_Resistor pull_resistor_28 (.node(pull_resistor_27_node[1]));
  Pull_Resistor pull_resistor_29 (.node(pull_resistor_27_node[2]));
  Pull_Resistor pull_resistor_30 (.node(pull_resistor_27_node[3]));
  Pull_Resistor pull_resistor_31 (.node(pull_resistor_27_node[4]));
  Pull_Resistor pull_resistor_32 (.node(pull_resistor_27_node[5]));
  Pull_Resistor pull_resistor_33 (.node(pull_resistor_27_node[6]));
  Pull_Resistor pull_resistor_34 (.node(pull_resistor_27_node[7]));
  not not_8 (not_8_out, and_5_out);
  not not_9 (not_9_out, and_6_out);
  and and_9 (and_9_out, and_7_out, clk_pin);
  not not_10 (not_10_out, pc_out_address_bus);
  D_Flip_Flop d_ff_4 (.D(d_ff_3_q), .clk(and_3_out), .Q(d_ff_4_q), .reset(or_1_out));  // open: Qn, preset
  xor xor_3 (xor_3_out, d_ff_3_q, d_ff_4_q);
  Register #(.trigger("falling")) i2 (.D(data_bus), .en(xor_3_out), .clk(clk_pin), .Q(i2_q), .clr(or_6_out));
  Transistor transistor_17 (.in(i2_q[0]), .out(data_bus[0]), .gate(not_7_out));
  Transistor transistor_18 (.in(i2_q[1]), .out(data_bus[1]), .gate(not_7_out));
  Transistor transistor_19 (.in(i2_q[2]), .out(data_bus[2]), .gate(not_7_out));
  Transistor transistor_20 (.in(i2_q[3]), .out(data_bus[3]), .gate(not_7_out));
  Transistor transistor_21 (.in(i2_q[4]), .out(data_bus[4]), .gate(not_7_out));
  Transistor transistor_22 (.in(i2_q[5]), .out(data_bus[5]), .gate(not_7_out));
  Transistor transistor_23 (.in(i2_q[6]), .out(data_bus[6]), .gate(not_7_out));
  Transistor transistor_24 (.in(i2_q[7]), .out(data_bus[7]), .gate(not_7_out));
  and and_10 (and_10_out, pull_resistor_26_node, IO_OUT);
  and and_11 (and_11_out, pull_resistor_26_node, IO_IN);
  not not_11 (not_11_out, and_11_out);
  Transistor transistor_25 (.in(pull_resistor_27_node[0]), .out(data_bus[0]), .gate(not_11_out));
  Transistor transistor_26 (.in(pull_resistor_27_node[1]), .out(data_bus[1]), .gate(not_11_out));
  Transistor transistor_27 (.in(pull_resistor_27_node[2]), .out(data_bus[2]), .gate(not_11_out));
  Transistor transistor_28 (.in(pull_resistor_27_node[3]), .out(data_bus[3]), .gate(not_11_out));
  Transistor transistor_29 (.in(pull_resistor_27_node[4]), .out(data_bus[4]), .gate(not_11_out));
  Transistor transistor_30 (.in(pull_resistor_27_node[5]), .out(data_bus[5]), .gate(not_11_out));
  Transistor transistor_31 (.in(pull_resistor_27_node[6]), .out(data_bus[6]), .gate(not_11_out));
  Transistor transistor_32 (.in(pull_resistor_27_node[7]), .out(data_bus[7]), .gate(not_11_out));
  Transistor transistor_33 (.in(rom_1_data[0]), .out(data_bus[0]), .gate(not_8_out));
  Transistor transistor_34 (.in(rom_1_data[1]), .out(data_bus[1]), .gate(not_8_out));
  Transistor transistor_35 (.in(rom_1_data[2]), .out(data_bus[2]), .gate(not_8_out));
  Transistor transistor_36 (.in(rom_1_data[3]), .out(data_bus[3]), .gate(not_8_out));
  Transistor transistor_37 (.in(rom_1_data[4]), .out(data_bus[4]), .gate(not_8_out));
  Transistor transistor_38 (.in(rom_1_data[5]), .out(data_bus[5]), .gate(not_8_out));
  Transistor transistor_39 (.in(rom_1_data[6]), .out(data_bus[6]), .gate(not_8_out));
  Transistor transistor_40 (.in(rom_1_data[7]), .out(data_bus[7]), .gate(not_8_out));
  Transistor transistor_41 (.in(ram_1_dout[0]), .out(data_bus[0]), .gate(not_9_out));
  Transistor transistor_42 (.in(ram_1_dout[1]), .out(data_bus[1]), .gate(not_9_out));
  Transistor transistor_43 (.in(ram_1_dout[2]), .out(data_bus[2]), .gate(not_9_out));
  Transistor transistor_44 (.in(ram_1_dout[3]), .out(data_bus[3]), .gate(not_9_out));
  Transistor transistor_45 (.in(ram_1_dout[4]), .out(data_bus[4]), .gate(not_9_out));
  Transistor transistor_46 (.in(ram_1_dout[5]), .out(data_bus[5]), .gate(not_9_out));
  Transistor transistor_47 (.in(ram_1_dout[6]), .out(data_bus[6]), .gate(not_9_out));
  Transistor transistor_48 (.in(ram_1_dout[7]), .out(data_bus[7]), .gate(not_9_out));
  and and_12 (INT_LOCK, INT_TRIGGER, and_14_out);
  D_Flip_Flop d_ff_5 (.D(d_ff_4_q), .clk(and_3_out), .Q(d_ff_5_q), .reset(or_1_out));  // open: Qn, preset
  ROM #(.addrWidth(11), .dataWidth(32)) MC1 (.addr({i0_q, counter_1_q}), .data(MC1_data));
  ROM #(.addrWidth(11), .dataWidth(32)) MC2 (.addr({i0_q, counter_1_q}), .data(MC2_data));
  Register #(.trigger("falling")) register_2 (
    .D(data_bus), .en(and_10_out), .clk(clk_pin), .Q(register_2_q), .clr(reset));
  Transistor transistor_49 (.in(pc_q[0]), .out(address_bus[0]), .gate(not_10_out));
  Transistor transistor_50 (.in(pc_q[1]), .out(address_bus[1]), .gate(not_10_out));
  Transistor transistor_51 (.in(pc_q[2]), .out(address_bus[2]), .gate(not_10_out));
  Transistor transistor_52 (.in(pc_q[3]), .out(address_bus[3]), .gate(not_10_out));
  Transistor transistor_53 (.in(pc_q[4]), .out(address_bus[4]), .gate(not_10_out));
  Transistor transistor_54 (.in(pc_q[5]), .out(address_bus[5]), .gate(not_10_out));
  Transistor transistor_55 (.in(pc_q[6]), .out(address_bus[6]), .gate(not_10_out));
  Transistor transistor_56 (.in(pc_q[7]), .out(address_bus[7]), .gate(not_10_out));
  Transistor transistor_57 (.in(pc_q[8]), .out(address_bus[8]), .gate(not_10_out));
  Transistor transistor_58 (.in(pc_q[9]), .out(address_bus[9]), .gate(not_10_out));
  Transistor transistor_59 (.in(pc_q[10]), .out(address_bus[10]), .gate(not_10_out));
  Transistor transistor_60 (.in(pc_q[11]), .out(address_bus[11]), .gate(not_10_out));
  Transistor transistor_61 (.in(pc_q[12]), .out(address_bus[12]), .gate(not_10_out));
  Transistor transistor_62 (.in(pc_q[13]), .out(address_bus[13]), .gate(not_10_out));
  Transistor transistor_63 (.in(pc_q[14]), .out(address_bus[14]), .gate(not_10_out));
  Transistor transistor_64 (.in(pc_q[15]), .out(address_bus[15]), .gate(not_10_out));
  Register #(.width(16)) register_3 (.D(pc_q), .en(1'b1), .clk(INT_LOCK), .Q(register_3_q), .clr(reset));
  Pull_Resistor pull_resistor_35 (.node(or_1_out));
  not not_12 (not_12_out, and_3_out);
  and and_13 (pc_count, not_12_out, or_8_out);
  or or_8 (or_8_out, xor_3_out, xor_2_out, xor_1_out);
  and and_14 (and_14_out, or_7_out, not_13_out);
  not not_13 (not_13_out, INT_DISABLE);
  buf buffer_1 (pc_out_address_bus, or_8_out);
  buf buffer_2 (memory_read, or_8_out);
  not not_14 (not_14_out, INT_RET_TO_ADDR);
  Transistor transistor_65 (.in(register_3_q[0]), .out(address_bus[0]), .gate(not_14_out));
  Transistor transistor_66 (.in(register_3_q[1]), .out(address_bus[1]), .gate(not_14_out));
  Transistor transistor_67 (.in(register_3_q[2]), .out(address_bus[2]), .gate(not_14_out));
  Transistor transistor_68 (.in(register_3_q[3]), .out(address_bus[3]), .gate(not_14_out));
  Transistor transistor_69 (.in(register_3_q[4]), .out(address_bus[4]), .gate(not_14_out));
  Transistor transistor_70 (.in(register_3_q[5]), .out(address_bus[5]), .gate(not_14_out));
  Transistor transistor_71 (.in(register_3_q[6]), .out(address_bus[6]), .gate(not_14_out));
  Transistor transistor_72 (.in(register_3_q[7]), .out(address_bus[7]), .gate(not_14_out));
  Transistor transistor_73 (.in(register_3_q[8]), .out(address_bus[8]), .gate(not_14_out));
  Transistor transistor_74 (.in(register_3_q[9]), .out(address_bus[9]), .gate(not_14_out));
  Transistor transistor_75 (.in(register_3_q[10]), .out(address_bus[10]), .gate(not_14_out));
  Transistor transistor_76 (.in(register_3_q[11]), .out(address_bus[11]), .gate(not_14_out));
  Transistor transistor_77 (.in(register_3_q[12]), .out(address_bus[12]), .gate(not_14_out));
  Transistor transistor_78 (.in(register_3_q[13]), .out(address_bus[13]), .gate(not_14_out));
  Transistor transistor_79 (.in(register_3_q[14]), .out(address_bus[14]), .gate(not_14_out));
  Transistor transistor_80 (.in(register_3_q[15]), .out(address_bus[15]), .gate(not_14_out));
  S_R_Flip_Flop #(.trigger("high")) s_r_ff_1 (
    .S(SAVE_PCB), .R(or_7_out), .clk(1'b1), .Q(INT_DISABLE), .reset(reset));  // open: Qn, preset
  Button button_3 (.out(INT0));
  Transistor transistor_81 (.in(MC1_data[0]), .out(PUT_A_ADDR), .gate(not_2_out));
  Transistor transistor_82 (.in(MC1_data[1]), .out(PUT_IR0_DB), .gate(not_2_out));
  Transistor transistor_83 (.in(MC1_data[2]), .out(PUT_IR1_DB), .gate(not_2_out));
  Transistor transistor_84 (.in(MC1_data[3]), .out(SAVE_DB_IR0), .gate(not_2_out));
  Transistor transistor_85 (.in(MC1_data[4]), .out(SAVE_DB_IR1), .gate(not_2_out));
  Transistor transistor_86 (.in(MC1_data[5]), .out(PUT_IIMM_DB), .gate(not_2_out));
  Transistor transistor_87 (.in(MC1_data[6]), .out(SAVE_DB_ALUA), .gate(not_2_out));
  Transistor transistor_88 (.in(MC1_data[7]), .out(SAVE_DB_ALUB), .gate(not_2_out));
  Transistor transistor_89 (.in(MC1_data[8]), .out(ALU_ADD), .gate(not_2_out));
  Transistor transistor_90 (.in(MC1_data[9]), .out(ALU_CMP), .gate(not_2_out));
  Transistor transistor_91 (.in(MC1_data[10]), .out(PUT_ALUOUT_DB), .gate(not_2_out));
  Transistor transistor_92 (.in(MC1_data[11]), .out(COND_INVERT), .gate(not_2_out));
  Transistor transistor_93 (.in(MC1_data[12]), .out(SAVE_PCB_IF_Z), .gate(not_2_out));
  Transistor transistor_94 (.in(MC1_data[13]), .out(SAVE_PCB_IF_EQ), .gate(not_2_out));
  Transistor transistor_95 (.in(MC1_data[14]), .out(SAVE_PCB), .gate(not_2_out));
  Transistor transistor_96 (.in(MC1_data[15]), .out(memory_write), .gate(not_2_out));
  Transistor transistor_97 (.in(MC1_data[16]), .out(memory_read), .gate(not_2_out));
  Transistor transistor_98 (.in(MC1_data[17]), .out(PC_FLUSH), .gate(not_2_out));
  Transistor transistor_99 (.in(MC1_data[18]), .out(PC_FLUSH_COND), .gate(not_2_out));
  Transistor transistor_100 (.in(MC1_data[19]), .out(ALU_SUB), .gate(not_2_out));
  Transistor transistor_101 (.in(MC1_data[20]), .out(ALU_NAND), .gate(not_2_out));
  Transistor transistor_102 (.in(MC1_data[21]), .out(ALU_NOR), .gate(not_2_out));
  Transistor transistor_103 (.in(MC1_data[22]), .out(IO_IN), .gate(not_2_out));
  Transistor transistor_104 (.in(MC1_data[23]), .out(IO_OUT), .gate(not_2_out));
  Transistor transistor_105 (.in(MC1_data[24]), .out(PUT_B_ADDR), .gate(not_2_out));
  Transistor transistor_106 (.in(MC1_data[25]), .out(PUT_IADR_ADDR), .gate(not_2_out));
  Transistor transistor_107 (.in(MC1_data[26]), .out(SAVE_ADDR_A), .gate(not_2_out));
  Transistor transistor_108 (.in(MC1_data[27]), .out(SAVE_ADDR_B), .gate(not_2_out));
  Transistor transistor_109 (.in(MC1_data[28]), .out(INT_RET_TO_ADDR), .gate(not_2_out));
  Transistor transistor_110 (.in(MC1_data[29]), .out(INT7), .gate(not_2_out));
  Transistor transistor_111 (.in(MC1_data[30]), .gate(not_2_out));  // open: out
  Transistor transistor_112 (.in(MC1_data[31]), .out(transistor_112_out), .gate(not_2_out));
  Transistor transistor_113 (.in(MC2_data[0]), .out(SAVE_PCB_IF_OF), .gate(not_2_out));
  Transistor transistor_114 (.in(MC2_data[1]), .out(CLEAR_FG), .gate(not_2_out));
  Transistor transistor_115 (.in(MC2_data[2]), .out(ALU_ADO), .gate(not_2_out));
  Transistor transistor_116 (.in(MC2_data[3]), .out(ALU_SBO), .gate(not_2_out));
  Transistor transistor_117 (.in(MC2_data[4]), .out(SAVE_IH), .gate(not_2_out));
  Transistor transistor_118 (.in(MC2_data[5]), .out(PUT_FG_DB), .gate(not_2_out));
  Transistor transistor_119 (.in(MC2_data[6]), .out(PUT_DB_FG), .gate(not_2_out));
  Transistor transistor_120 (.in(MC2_data[7]), .out(SP_UP), .gate(not_2_out));
  Transistor transistor_121 (.in(MC2_data[8]), .out(SP_DOWN), .gate(not_2_out));
  Transistor transistor_122 (.in(MC2_data[9]), .out(SAVE_ADDR_SP), .gate(not_2_out));
  Transistor transistor_123 (.in(MC2_data[10]), .out(PUT_SP_ADDR), .gate(not_2_out));
  Transistor transistor_124 (.in(MC2_data[11]), .gate(not_2_out));  // open: out
  Transistor transistor_125 (.in(MC2_data[12]), .gate(not_2_out));  // open: out
  Transistor transistor_126 (.in(MC2_data[13]), .gate(not_2_out));  // open: out
  Transistor transistor_127 (.in(MC2_data[14]), .gate(not_2_out));  // open: out
  Transistor transistor_128 (.in(MC2_data[15]), .gate(not_2_out));  // open: out
  Transistor transistor_129 (.in(MC2_data[16]), .gate(not_2_out));  // open: out
  Transistor transistor_130 (.in(MC2_data[17]), .gate(not_2_out));  // open: out
  Transistor transistor_131 (.in(MC2_data[18]), .gate(not_2_out));  // open: out
  Transistor transistor_132 (.in(MC2_data[19]), .gate(not_2_out));  // open: out
  Transistor transistor_133 (.in(MC2_data[20]), .gate(not_2_out));  // open: out
  Transistor transistor_134 (.in(MC2_data[21]), .gate(not_2_out));  // open: out
  Transistor transistor_135 (.in(MC2_data[22]), .gate(not_2_out));  // open: out
  Transistor transistor_136 (.in(MC2_data[23]), .gate(not_2_out));  // open: out
  Transistor transistor_137 (.in(MC2_data[24]), .gate(not_2_out));  // open: out
  Transistor transistor_138 (.in(MC2_data[25]), .gate(not_2_out));  // open: out
  Transistor transistor_139 (.in(MC2_data[26]), .gate(not_2_out));  // open: out
  Transistor transistor_140 (.in(MC2_data[27]), .gate(not_2_out));  // open: out
  Transistor transistor_141 (.in(MC2_data[28]), .gate(not_2_out));  // open: out
  Transistor transistor_142 (.in(MC2_data[29]), .gate(not_2_out));  // open: out
  Transistor transistor_143 (.in(MC2_data[30]), .gate(not_2_out));  // open: out
  Transistor transistor_144 (.in(MC2_data[31]), .gate(not_2_out));  // open: out
  Pull_Resistor pull_resistor_36 (.node(INT_TRIGGER));
  Pull_Resistor pull_resistor_37 (.node(transistor_112_out));
  Register #(.trigger("falling"), .width(16)) u_ih (.D(address_bus), .en(SAVE_IH), .clk(clk_pin), .Q(ih), .clr(reset));
  Pull_Resistor pull_resistor_38 (.node(memory_read));
  Pull_Resistor pull_resistor_39 (.node(memory_write));
  Pull_Resistor pull_resistor_40 (.node(PUT_A_ADDR));
  Pull_Resistor pull_resistor_41 (.node(PUT_IR0_DB));
  Pull_Resistor pull_resistor_42 (.node(PUT_IR1_DB));
  Pull_Resistor pull_resistor_43 (.node(SAVE_DB_IR0));
  Pull_Resistor pull_resistor_44 (.node(SAVE_DB_IR1));
  Pull_Resistor pull_resistor_45 (.node(PUT_IIMM_DB));
  Pull_Resistor pull_resistor_46 (.node(SAVE_DB_ALUA));
  Pull_Resistor pull_resistor_47 (.node(SAVE_DB_ALUB));
  Pull_Resistor pull_resistor_48 (.node(ALU_ADD));
  Pull_Resistor pull_resistor_49 (.node(ALU_CMP));
  Pull_Resistor pull_resistor_50 (.node(PUT_ALUOUT_DB));
  Pull_Resistor pull_resistor_51 (.node(COND_INVERT));
  Pull_Resistor pull_resistor_52 (.node(SAVE_PCB_IF_Z));
  Pull_Resistor pull_resistor_53 (.node(SAVE_PCB_IF_EQ));
  Pull_Resistor pull_resistor_54 (.node(SAVE_PCB));
  Pull_Resistor pull_resistor_55 (.node(memory_write));
  Pull_Resistor pull_resistor_56 (.node(memory_read));
  Pull_Resistor pull_resistor_57 (.node(PC_FLUSH));
  Pull_Resistor pull_resistor_58 (.node(PC_FLUSH_COND));
  Pull_Resistor pull_resistor_59 (.node(ALU_SUB));
  Pull_Resistor pull_resistor_60 (.node(ALU_NAND));
  Pull_Resistor pull_resistor_61 (.node(ALU_NOR));
  Pull_Resistor pull_resistor_62 (.node(IO_IN));
  Pull_Resistor pull_resistor_63 (.node(IO_OUT));
  Pull_Resistor pull_resistor_64 (.node(PUT_B_ADDR));
  Pull_Resistor pull_resistor_65 (.node(PUT_IADR_ADDR));
  Pull_Resistor pull_resistor_66 (.node(SAVE_ADDR_A));
  Pull_Resistor pull_resistor_67 (.node(SAVE_ADDR_B));
  Pull_Resistor pull_resistor_68 (.node(INT_RET_TO_ADDR));
  Pull_Resistor pull_resistor_69 (.node(SAVE_PCB_IF_OF));
  Pull_Resistor pull_resistor_70 (.node(CLEAR_FG));
  Pull_Resistor pull_resistor_71 (.node(ALU_ADO));
  Pull_Resistor pull_resistor_72 (.node(ALU_SBO));
  Pull_Resistor pull_resistor_73 (.node(SAVE_IH));
  Pull_Resistor pull_resistor_74 (.node(PUT_FG_DB));
  Pull_Resistor pull_resistor_75 (.node(PUT_DB_FG));
  Pull_Resistor pull_resistor_76 (.node(SP_UP));
  Pull_Resistor pull_resistor_77 (.node(SP_DOWN));
  Pull_Resistor pull_resistor_78 (.node(SAVE_ADDR_SP));
  Pull_Resistor pull_resistor_79 (.node(PUT_SP_ADDR));
  Pull_Resistor pull_resistor_80 (.node(pc_load));
  Transistor transistor_145 (.in(instruction_reg0[0]), .out(address_bus[0]), .gate(not_15_out));
  Transistor transistor_146 (.in(instruction_reg0[1]), .out(address_bus[1]), .gate(not_15_out));
  Transistor transistor_147 (.in(instruction_reg0[2]), .out(address_bus[2]), .gate(not_15_out));
  Transistor transistor_148 (.in(instruction_reg0[3]), .out(address_bus[3]), .gate(not_15_out));
  Transistor transistor_149 (.in(instruction_reg1[0]), .out(address_bus[4]), .gate(not_15_out));
  Transistor transistor_150 (.in(instruction_reg1[1]), .out(address_bus[5]), .gate(not_15_out));
  Transistor transistor_151 (.in(instruction_reg1[2]), .out(address_bus[6]), .gate(not_15_out));
  Transistor transistor_152 (.in(instruction_reg1[3]), .out(address_bus[7]), .gate(not_15_out));
  Transistor transistor_153 (.in(i2_q[0]), .out(address_bus[8]), .gate(not_15_out));
  Transistor transistor_154 (.in(i2_q[1]), .out(address_bus[9]), .gate(not_15_out));
  Transistor transistor_155 (.in(i2_q[2]), .out(address_bus[10]), .gate(not_15_out));
  Transistor transistor_156 (.in(i2_q[3]), .out(address_bus[11]), .gate(not_15_out));
  Transistor transistor_157 (.in(i2_q[4]), .out(address_bus[12]), .gate(not_15_out));
  Transistor transistor_158 (.in(i2_q[5]), .out(address_bus[13]), .gate(not_15_out));
  Transistor transistor_159 (.in(i2_q[6]), .out(address_bus[14]), .gate(not_15_out));
  Transistor transistor_160 (.in(i2_q[7]), .out(address_bus[15]), .gate(not_15_out));
  not not_15 (not_15_out, PUT_IADR_ADDR);
  Pull_Resistor pull_resistor_81 (.node(pc_out_address_bus));
  xnor xnor_17 (xnor_17_out, address_bus[0], 1'b0);
  xnor xnor_18 (xnor_18_out, address_bus[1], 1'b1);
  xnor xnor_19 (xnor_19_out, address_bus[2], 1'b1);
  xnor xnor_20 (xnor_20_out, address_bus[3], 1'b1);
  xnor xnor_21 (xnor_21_out, address_bus[4], 1'b1);
  xnor xnor_22 (xnor_22_out, address_bus[5], 1'b1);
  xnor xnor_23 (xnor_23_out, address_bus[6], 1'b1);
  xnor xnor_24 (xnor_24_out, address_bus[7], 1'b1);
  xnor xnor_25 (xnor_25_out, address_bus[8], 1'b0);
  xnor xnor_26 (xnor_26_out, address_bus[9], 1'b0);
  xnor xnor_27 (xnor_27_out, address_bus[10], 1'b0);
  xnor xnor_28 (xnor_28_out, address_bus[11], 1'b0);
  xnor xnor_29 (xnor_29_out, address_bus[12], 1'b0);
  xnor xnor_30 (xnor_30_out, address_bus[13], 1'b0);
  xnor xnor_31 (xnor_31_out, address_bus[14], 1'b0);
  xnor xnor_32 (xnor_32_out, address_bus[15], 1'b0);
  Transistor transistor_161 (.in(1'b1), .out(transistor_161_out), .gate(xnor_17_out));
  Transistor transistor_162 (.in(transistor_161_out), .out(transistor_162_out), .gate(xnor_18_out));
  Transistor transistor_163 (.in(transistor_162_out), .out(transistor_163_out), .gate(xnor_19_out));
  Transistor transistor_164 (.in(transistor_163_out), .out(transistor_164_out), .gate(xnor_20_out));
  Transistor transistor_165 (.in(transistor_164_out), .out(transistor_165_out), .gate(xnor_21_out));
  Transistor transistor_166 (.in(transistor_165_out), .out(transistor_166_out), .gate(xnor_22_out));
  Transistor transistor_167 (.in(transistor_166_out), .out(transistor_167_out), .gate(xnor_23_out));
  Transistor transistor_168 (.in(transistor_167_out), .out(transistor_168_out), .gate(xnor_24_out));
  Transistor transistor_169 (.in(transistor_168_out), .out(transistor_169_out), .gate(xnor_25_out));
  Transistor transistor_170 (.in(transistor_169_out), .out(transistor_170_out), .gate(xnor_26_out));
  Transistor transistor_171 (.in(transistor_170_out), .out(transistor_171_out), .gate(xnor_27_out));
  Transistor transistor_172 (.in(transistor_171_out), .out(transistor_172_out), .gate(xnor_28_out));
  Transistor transistor_173 (.in(transistor_172_out), .out(transistor_173_out), .gate(xnor_29_out));
  Transistor transistor_174 (.in(transistor_173_out), .out(transistor_174_out), .gate(xnor_30_out));
  Transistor transistor_175 (.in(transistor_174_out), .out(transistor_175_out), .gate(xnor_31_out));
  Pull_Resistor pull_resistor_82 (.node(pull_resistor_82_node));
  Transistor transistor_176 (.in(transistor_175_out), .out(pull_resistor_82_node), .gate(xnor_32_out));
  and and_15 (and_15_out, pull_resistor_82_node, IO_OUT);
  and and_16 (and_16_out, pull_resistor_82_node, IO_IN);
  not not_16 (not_16_out, and_16_out);
  Transistor transistor_177 (.in(register_4_q[0]), .out(data_bus[0]), .gate(not_16_out));
  Transistor transistor_178 (.in(register_4_q[1]), .out(data_bus[1]), .gate(not_16_out));
  Transistor transistor_179 (.in(register_4_q[2]), .out(data_bus[2]), .gate(not_16_out));
  Transistor transistor_180 (.in(register_4_q[3]), .out(data_bus[3]), .gate(not_16_out));
  Transistor transistor_181 (.in(register_4_q[4]), .out(data_bus[4]), .gate(not_16_out));
  Transistor transistor_182 (.in(register_4_q[5]), .out(data_bus[5]), .gate(not_16_out));
  Transistor transistor_183 (.in(register_4_q[6]), .out(data_bus[6]), .gate(not_16_out));
  Transistor transistor_184 (.in(register_4_q[7]), .out(data_bus[7]), .gate(not_16_out));
  xor xor_4 (xor_4_out, COND_INVERT, fg[0]);
  and and_17 (and_17_out, xor_4_out, SAVE_PCB_IF_Z);
  xor xor_5 (xor_5_out, COND_INVERT, fg[1]);
  and and_18 (and_18_out, xor_5_out, SAVE_PCB_IF_EQ);
  xor xor_6 (xor_6_out, COND_INVERT, fg[2]);
  and and_19 (and_19_out, xor_6_out, SAVE_PCB_IF_OF);
  Register #(.trigger("falling")) register_4 (
    .D(data_bus), .en(and_15_out), .clk(clk_pin), .Q(register_4_q), .clr(reset));
  buf buffer_3 (SAVE_PCB, and_17_out);
  buf buffer_4 (SAVE_PCB, and_18_out);
  buf buffer_5 (SAVE_PCB, and_19_out);
  or or_9 (or_9_out, SAVE_PCB_IF_Z, SAVE_PCB_IF_EQ, SAVE_PCB_IF_OF);
  or or_10 (or_10_out, and_17_out, and_18_out, and_19_out);
  D_Flip_Flop d_ff_6 (.clk(clk_pin), .Q(d_ff_6_q), .preset(or_10_out), .reset(or_9_out));  // open: D, Qn
  Register #(.trigger("falling")) alua (.D(data_bus), .en(SAVE_DB_ALUA), .clk(clk_pin), .Q(alua_q), .clr(reset));
  Register #(.trigger("falling")) alub (.D(data_bus), .en(SAVE_DB_ALUB), .clk(clk_pin), .Q(alub_q), .clr(reset));
  xnor xnor_33 (xnor_33_out, address_bus[0], 1'b1);
  Transistor transistor_185 (.in(1'b1), .out(transistor_185_out), .gate(xnor_33_out));
  xnor xnor_34 (xnor_34_out, address_bus[1], 1'b0);
  Transistor transistor_186 (.in(transistor_185_out), .out(transistor_186_out), .gate(xnor_34_out));
  xnor xnor_35 (xnor_35_out, address_bus[2], 1'b1);
  Transistor transistor_187 (.in(transistor_186_out), .out(transistor_187_out), .gate(xnor_35_out));
  xnor xnor_36 (xnor_36_out, address_bus[3], 1'b1);
  Transistor transistor_188 (.in(transistor_187_out), .out(transistor_188_out), .gate(xnor_36_out));
  xnor xnor_37 (xnor_37_out, address_bus[4], 1'b1);
  Transistor transistor_189 (.in(transistor_188_out), .out(transistor_189_out), .gate(xnor_37_out));
  xnor xnor_38 (xnor_38_out, address_bus[5], 1'b1);
  Transistor transistor_190 (.in(transistor_189_out), .out(transistor_190_out), .gate(xnor_38_out));
  xnor xnor_39 (xnor_39_out, address_bus[6], 1'b1);
  Transistor transistor_191 (.in(transistor_190_out), .out(transistor_191_out), .gate(xnor_39_out));
  xnor xnor_40 (xnor_40_out, address_bus[7], 1'b1);
  Transistor transistor_192 (.in(transistor_191_out), .out(transistor_192_out), .gate(xnor_40_out));
  xnor xnor_41 (xnor_41_out, address_bus[8], 1'b0);
  Transistor transistor_193 (.in(transistor_192_out), .out(transistor_193_out), .gate(xnor_41_out));
  xnor xnor_42 (xnor_42_out, address_bus[9], 1'b0);
  Transistor transistor_194 (.in(transistor_193_out), .out(transistor_194_out), .gate(xnor_42_out));
  xnor xnor_43 (xnor_43_out, address_bus[10], 1'b0);
  Transistor transistor_195 (.in(transistor_194_out), .out(transistor_195_out), .gate(xnor_43_out));
  xnor xnor_44 (xnor_44_out, address_bus[11], 1'b0);
  Transistor transistor_196 (.in(transistor_195_out), .out(transistor_196_out), .gate(xnor_44_out));
  xnor xnor_45 (xnor_45_out, address_bus[12], 1'b0);
  Transistor transistor_197 (.in(transistor_196_out), .out(transistor_197_out), .gate(xnor_45_out));
  xnor xnor_46 (xnor_46_out, address_bus[13], 1'b0);
  Transistor transistor_198 (.in(transistor_197_out), .out(transistor_198_out), .gate(xnor_46_out));
  xnor xnor_47 (xnor_47_out, address_bus[14], 1'b0);
  Transistor transistor_199 (.in(transistor_198_out), .out(transistor_199_out), .gate(xnor_47_out));
  xnor xnor_48 (xnor_48_out, address_bus[15], 1'b0);
  Pull_Resistor pull_resistor_83 (.node(pull_resistor_83_node));
  Transistor transistor_200 (.in(transistor_199_out), .out(pull_resistor_83_node), .gate(xnor_48_out));
  xnor xnor_49 (xnor_49_out, address_bus[0], 1'b1);
  Transistor transistor_201 (.in(1'b1), .out(transistor_201_out), .gate(xnor_49_out));
  xnor xnor_50 (xnor_50_out, address_bus[1], 1'b1);
  Transistor transistor_202 (.in(transistor_201_out), .out(transistor_202_out), .gate(xnor_50_out));
  xnor xnor_51 (xnor_51_out, address_bus[2], 1'b1);
  Transistor transistor_203 (.in(transistor_202_out), .out(transistor_203_out), .gate(xnor_51_out));
  xnor xnor_52 (xnor_52_out, address_bus[3], 1'b1);
  Transistor transistor_204 (.in(transistor_203_out), .out(transistor_204_out), .gate(xnor_52_out));
  xnor xnor_53 (xnor_53_out, address_bus[4], 1'b1);
  Transistor transistor_205 (.in(transistor_204_out), .out(transistor_205_out), .gate(xnor_53_out));
  xnor xnor_54 (xnor_54_out, address_bus[5], 1'b1);
  Transistor transistor_206 (.in(transistor_205_out), .out(transistor_206_out), .gate(xnor_54_out));
  xnor xnor_55 (xnor_55_out, address_bus[6], 1'b1);
  Transistor transistor_207 (.in(transistor_206_out), .out(transistor_207_out), .gate(xnor_55_out));
  xnor xnor_56 (xnor_56_out, address_bus[7], 1'b1);
  Transistor transistor_208 (.in(transistor_207_out), .out(transistor_208_out), .gate(xnor_56_out));
  xnor xnor_57 (xnor_57_out, address_bus[8], 1'b0);
  Transistor transistor_209 (.in(transistor_208_out), .out(transistor_209_out), .gate(xnor_57_out));
  xnor xnor_58 (xnor_58_out, address_bus[9], 1'b0);
  Transistor transistor_210 (.in(transistor_209_out), .out(transistor_210_out), .gate(xnor_58_out));
  xnor xnor_59 (xnor_59_out, address_bus[10], 1'b0);
  Transistor transistor_211 (.in(transistor_210_out), .out(transistor_211_out), .gate(xnor_59_out));
  xnor xnor_60 (xnor_60_out, address_bus[11], 1'b0);
  Transistor transistor_212 (.in(transistor_211_out), .out(transistor_212_out), .gate(xnor_60_out));
  xnor xnor_61 (xnor_61_out, address_bus[12], 1'b0);
  Transistor transistor_213 (.in(transistor_212_out), .out(transistor_213_out), .gate(xnor_61_out));
  xnor xnor_62 (xnor_62_out, address_bus[13], 1'b0);
  Transistor transistor_214 (.in(transistor_213_out), .out(transistor_214_out), .gate(xnor_62_out));
  xnor xnor_63 (xnor_63_out, address_bus[14], 1'b0);
  Transistor transistor_215 (.in(transistor_214_out), .out(transistor_215_out), .gate(xnor_63_out));
  xnor xnor_64 (xnor_64_out, address_bus[15], 1'b0);
  Pull_Resistor pull_resistor_84 (.node(pull_resistor_84_node));
  Transistor transistor_216 (.in(transistor_215_out), .out(pull_resistor_84_node), .gate(xnor_64_out));
  and and_20 (and_20_out, pull_resistor_83_node, IO_OUT);
  and and_21 (and_21_out, pull_resistor_83_node, IO_IN);
  not not_17 (not_17_out, and_21_out);
  Transistor transistor_217 (.in(register_5_q[0]), .out(data_bus[0]), .gate(not_17_out));
  Transistor transistor_218 (.in(register_5_q[1]), .out(data_bus[1]), .gate(not_17_out));
  Transistor transistor_219 (.in(register_5_q[2]), .out(data_bus[2]), .gate(not_17_out));
  Transistor transistor_220 (.in(register_5_q[3]), .out(data_bus[3]), .gate(not_17_out));
  Transistor transistor_221 (.in(register_5_q[4]), .out(data_bus[4]), .gate(not_17_out));
  Transistor transistor_222 (.in(register_5_q[5]), .out(data_bus[5]), .gate(not_17_out));
  Transistor transistor_223 (.in(register_5_q[6]), .out(data_bus[6]), .gate(not_17_out));
  Transistor transistor_224 (.in(register_5_q[7]), .out(data_bus[7]), .gate(not_17_out));
  and and_22 (and_22_out, pull_resistor_84_node, IO_OUT);
  and and_23 (and_23_out, pull_resistor_84_node, IO_IN);
  not not_18 (not_18_out, and_23_out);
  Transistor transistor_225 (.in(s_r_ff_11_q[0]), .out(data_bus[0]), .gate(not_18_out));
  Transistor transistor_226 (.in(s_r_ff_11_q[1]), .out(data_bus[1]), .gate(not_18_out));
  Transistor transistor_227 (.in(s_r_ff_11_q[2]), .out(data_bus[2]), .gate(not_18_out));
  Transistor transistor_228 (.in(s_r_ff_11_q[3]), .out(data_bus[3]), .gate(not_18_out));
  Transistor transistor_229 (.in(s_r_ff_11_q[4]), .out(data_bus[4]), .gate(not_18_out));
  Transistor transistor_230 (.in(s_r_ff_11_q[5]), .out(data_bus[5]), .gate(not_18_out));
  Transistor transistor_231 (.in(s_r_ff_11_q[6]), .out(data_bus[6]), .gate(not_18_out));
  Transistor transistor_232 (.in(s_r_ff_11_q[7]), .out(data_bus[7]), .gate(not_18_out));
  and and_24 (and_24_out, d_ff_6_q, PC_FLUSH_COND);
  Transistor transistor_233 (.in(alua_q[0]), .out(transistor_233_out[0]), .gate(not_19_out));
  Transistor transistor_234 (.in(alua_q[1]), .out(transistor_233_out[1]), .gate(not_19_out));
  Transistor transistor_235 (.in(alua_q[2]), .out(transistor_233_out[2]), .gate(not_19_out));
  Transistor transistor_236 (.in(alua_q[3]), .out(transistor_233_out[3]), .gate(not_19_out));
  Transistor transistor_237 (.in(alua_q[4]), .out(transistor_233_out[4]), .gate(not_19_out));
  Transistor transistor_238 (.in(alua_q[5]), .out(transistor_233_out[5]), .gate(not_19_out));
  Transistor transistor_239 (.in(alua_q[6]), .out(transistor_233_out[6]), .gate(not_19_out));
  Transistor transistor_240 (.in(alua_q[7]), .out(transistor_233_out[7]), .gate(not_19_out));
  not not_19 (not_19_out, or_11_out);
  or or_11 (or_11_out, and_32_out, and_29_out);
  or or_12 (or_12_out, CLEAR_FG, reset);
  Register #(.trigger("falling")) register_5 (
    .D(data_bus), .en(and_20_out), .clk(clk_pin), .Q(register_5_q), .clr(reset));
  not not_20 (not_20_out, clk_pin);
  buf buffer_6 (PC_FLUSH, and_24_out);
  Register #(.trigger("falling")) register_6 (
    .D(data_bus), .en(and_22_out), .clk(clk_pin), .Q(register_6_q), .clr(reset));
  D_Flip_Flop #(.trigger("falling")) d_ff_7 (
    .D(data_bus[3]), .clk(and_25_out), .Q(fg[3]), .preset(halt), .reset(or_12_out));  // open: Qn
  and and_25 (and_25_out, PUT_DB_FG, clk_pin);
  xnor xnor_65 (xnor_65_out, address_bus[0], 1'b0);
  Transistor transistor_241 (.in(1'b1), .out(transistor_241_out), .gate(xnor_65_out));
  xnor xnor_66 (xnor_66_out, address_bus[1], 1'b0);
  Transistor transistor_242 (.in(transistor_241_out), .out(transistor_242_out), .gate(xnor_66_out));
  xnor xnor_67 (xnor_67_out, address_bus[2], 1'b1);
  Transistor transistor_243 (.in(transistor_242_out), .out(transistor_243_out), .gate(xnor_67_out));
  xnor xnor_68 (xnor_68_out, address_bus[3], 1'b1);
  Transistor transistor_244 (.in(transistor_243_out), .out(transistor_244_out), .gate(xnor_68_out));
  xnor xnor_69 (xnor_69_out, address_bus[4], 1'b1);
  Transistor transistor_245 (.in(transistor_244_out), .out(transistor_245_out), .gate(xnor_69_out));
  xnor xnor_70 (xnor_70_out, address_bus[5], 1'b1);
  Transistor transistor_246 (.in(transistor_245_out), .out(transistor_246_out), .gate(xnor_70_out));
  xnor xnor_71 (xnor_71_out, address_bus[6], 1'b1);
  Transistor transistor_247 (.in(transistor_246_out), .out(transistor_247_out), .gate(xnor_71_out));
  xnor xnor_72 (xnor_72_out, address_bus[7], 1'b1);
  Transistor transistor_248 (.in(transistor_247_out), .out(transistor_248_out), .gate(xnor_72_out));
  xnor xnor_73 (xnor_73_out, address_bus[8], 1'b0);
  Transistor transistor_249 (.in(transistor_248_out), .out(transistor_249_out), .gate(xnor_73_out));
  xnor xnor_74 (xnor_74_out, address_bus[9], 1'b0);
  Transistor transistor_250 (.in(transistor_249_out), .out(transistor_250_out), .gate(xnor_74_out));
  xnor xnor_75 (xnor_75_out, address_bus[10], 1'b0);
  Transistor transistor_251 (.in(transistor_250_out), .out(transistor_251_out), .gate(xnor_75_out));
  xnor xnor_76 (xnor_76_out, address_bus[11], 1'b0);
  Transistor transistor_252 (.in(transistor_251_out), .out(transistor_252_out), .gate(xnor_76_out));
  xnor xnor_77 (xnor_77_out, address_bus[12], 1'b0);
  Transistor transistor_253 (.in(transistor_252_out), .out(transistor_253_out), .gate(xnor_77_out));
  xnor xnor_78 (xnor_78_out, address_bus[13], 1'b0);
  Transistor transistor_254 (.in(transistor_253_out), .out(transistor_254_out), .gate(xnor_78_out));
  xnor xnor_79 (xnor_79_out, address_bus[14], 1'b0);
  Transistor transistor_255 (.in(transistor_254_out), .out(transistor_255_out), .gate(xnor_79_out));
  xnor xnor_80 (xnor_80_out, address_bus[15], 1'b0);
  Pull_Resistor pull_resistor_85 (.node(pull_resistor_85_node));
  Transistor transistor_256 (.in(transistor_255_out), .out(pull_resistor_85_node), .gate(xnor_80_out));
  and and_26 (and_26_out, register_7_q[0], not_20_out);
  Multiplexer multiplexer_1 (.in0(and_26_out), .in1(comparator_1_eq), .out(multiplexer_1_out), .sel(register_7_q[1]));
  nand nand_1 (nand_1_out, alub_q[0], alua_q[0]);
  nand nand_2 (nand_2_out, alub_q[1], alua_q[1]);
  nand nand_3 (nand_3_out, alub_q[2], alua_q[2]);
  nand nand_4 (nand_4_out, alub_q[3], alua_q[3]);
  nand nand_5 (nand_5_out, alub_q[4], alua_q[4]);
  nand nand_6 (nand_6_out, alub_q[5], alua_q[5]);
  nand nand_7 (nand_7_out, alub_q[6], alua_q[6]);
  nand nand_8 (nand_8_out, alub_q[7], alua_q[7]);
  not not_21 (not_21_out, ALU_NAND);
  Adder adder_1 (.a(alua_q), .b(alub_q), .out(adder_1_out), .cout(adder_1_cout));  // open: cin
  and and_27 (and_27_out, adder_1_cout, ALU_ADD);
  and and_28 (and_28_out, ALU_ADO, fg[2]);
  and and_29 (and_29_out, ALU_ADO, not_22_out);
  not not_22 (not_22_out, and_28_out);
  Subtractor subtractor_1 (.a(alua_q), .b(alub_q), .out(subtractor_1_out), .bout(subtractor_1_bout));  // open: bin
  and and_30 (and_30_out, subtractor_1_bout, ALU_SUB);
  and and_31 (and_31_out, ALU_SBO, fg[2]);
  and and_32 (and_32_out, ALU_SBO, not_23_out);
  not not_23 (not_23_out, and_31_out);
  and and_33 (and_33_out, pull_resistor_85_node, IO_OUT);
  and and_34 (and_34_out, pull_resistor_85_node, IO_IN);
  not not_24 (not_24_out, and_34_out);
  Transistor transistor_257 (.in(register_7_q[0]), .out(data_bus[0]), .gate(not_24_out));
  Transistor transistor_258 (.in(register_7_q[1]), .out(data_bus[1]), .gate(not_24_out));
  Transistor transistor_259 (.in(register_7_q[2]), .out(data_bus[2]), .gate(not_24_out));
  Transistor transistor_260 (.in(register_7_q[3]), .out(data_bus[3]), .gate(not_24_out));
  Transistor transistor_261 (.in(register_7_q[4]), .out(data_bus[4]), .gate(not_24_out));
  Transistor transistor_262 (.in(register_7_q[5]), .out(data_bus[5]), .gate(not_24_out));
  Transistor transistor_263 (.in(register_7_q[6]), .out(data_bus[6]), .gate(not_24_out));
  Transistor transistor_264 (.in(register_7_q[7]), .out(data_bus[7]), .gate(not_24_out));
  Counter tpsc (.clr(or_13_out), .clk(and_26_out), .Q(tpsc_q));  // open: load, up, count, D, carry
  or or_13 (or_13_out, reset, comparator_1_eq);
  Counter tcnt (.clr(or_14_out), .clk(multiplexer_1_out), .Q(tcnt_q));  // open: load, up, count, D, carry
  or or_14 (or_14_out, reset, comparator_2_eq);
  D_Flip_Flop d_ff_8 (.D(d_ff_8_qn), .clk(and_35_out), .Qn(d_ff_8_qn), .reset(reset));  // open: Q, preset
  Transistor transistor_265 (.in(nand_1_out), .out(transistor_233_out[0]), .gate(not_21_out));
  Transistor transistor_266 (.in(nand_2_out), .out(transistor_233_out[1]), .gate(not_21_out));
  Transistor transistor_267 (.in(nand_3_out), .out(transistor_233_out[2]), .gate(not_21_out));
  Transistor transistor_268 (.in(nand_4_out), .out(transistor_233_out[3]), .gate(not_21_out));
  Transistor transistor_269 (.in(nand_5_out), .out(transistor_233_out[4]), .gate(not_21_out));
  Transistor transistor_270 (.in(nand_6_out), .out(transistor_233_out[5]), .gate(not_21_out));
  Transistor transistor_271 (.in(nand_7_out), .out(transistor_233_out[6]), .gate(not_21_out));
  Transistor transistor_272 (.in(nand_8_out), .out(transistor_233_out[7]), .gate(not_21_out));
  or or_15 (or_15_out, ALU_ADD, and_28_out);
  buf buffer_7 (buffer_7_out, and_27_out);
  Pull_Resistor pull_resistor_86 (.node(buffer_7_out));
  or or_16 (or_16_out, ALU_SUB, and_31_out);
  buf buffer_8 (buffer_7_out, and_30_out);
  D_Flip_Flop #(.trigger("falling")) d_ff_9 (
    .D(data_bus[2]), .clk(and_25_out), .Q(fg[2]), .preset(buffer_7_out), .reset(or_12_out));  // open: Qn
  and and_35 (and_35_out, comparator_2_eq, register_7_q[0]);
  S_R_Flip_Flop #(.trigger("high")) s_r_ff_2 (
    .S(INT_LOCK), .R(or_17_out), .clk(1'b1), .Qn(s_r_ff_2_qn));  // open: Q, reset, preset
  or or_17 (or_17_out, reset, INT_RET_TO_ADDR);
  not not_25 (not_25_out, instruction_reg0[0]);
  not not_26 (not_26_out, instruction_reg0[1]);
  not not_27 (not_27_out, instruction_reg0[2]);
  not not_28 (not_28_out, instruction_reg0[3]);
  not not_29 (not_29_out, instruction_reg1[0]);
  not not_30 (not_30_out, instruction_reg1[1]);
  not not_31 (not_31_out, instruction_reg1[2]);
  not not_32 (not_32_out, instruction_reg1[3]);
  not not_33 (not_33_out, instruction_reg0[1]);
  not not_34 (not_34_out, instruction_reg0[2]);
  not not_35 (not_35_out, instruction_reg0[3]);
  not not_36 (not_36_out, instruction_reg1[1]);
  not not_37 (not_37_out, instruction_reg1[2]);
  not not_38 (not_38_out, instruction_reg1[3]);
  Transistor transistor_273 (.in(adder_1_out[0]), .out(transistor_233_out[0]), .gate(not_39_out));
  Transistor transistor_274 (.in(adder_1_out[1]), .out(transistor_233_out[1]), .gate(not_39_out));
  Transistor transistor_275 (.in(adder_1_out[2]), .out(transistor_233_out[2]), .gate(not_39_out));
  Transistor transistor_276 (.in(adder_1_out[3]), .out(transistor_233_out[3]), .gate(not_39_out));
  Transistor transistor_277 (.in(adder_1_out[4]), .out(transistor_233_out[4]), .gate(not_39_out));
  Transistor transistor_278 (.in(adder_1_out[5]), .out(transistor_233_out[5]), .gate(not_39_out));
  Transistor transistor_279 (.in(adder_1_out[6]), .out(transistor_233_out[6]), .gate(not_39_out));
  Transistor transistor_280 (.in(adder_1_out[7]), .out(transistor_233_out[7]), .gate(not_39_out));
  not not_39 (not_39_out, or_15_out);
  Transistor transistor_281 (.in(subtractor_1_out[0]), .out(transistor_233_out[0]), .gate(not_40_out));
  Transistor transistor_282 (.in(subtractor_1_out[1]), .out(transistor_233_out[1]), .gate(not_40_out));
  Transistor transistor_283 (.in(subtractor_1_out[2]), .out(transistor_233_out[2]), .gate(not_40_out));
  Transistor transistor_284 (.in(subtractor_1_out[3]), .out(transistor_233_out[3]), .gate(not_40_out));
  Transistor transistor_285 (.in(subtractor_1_out[4]), .out(transistor_233_out[4]), .gate(not_40_out));
  Transistor transistor_286 (.in(subtractor_1_out[5]), .out(transistor_233_out[5]), .gate(not_40_out));
  Transistor transistor_287 (.in(subtractor_1_out[6]), .out(transistor_233_out[6]), .gate(not_40_out));
  Transistor transistor_288 (.in(subtractor_1_out[7]), .out(transistor_233_out[7]), .gate(not_40_out));
  not not_40 (not_40_out, or_16_out);
  and and_36 (and_36_out, transistor_308_out, ALU_CMP);
  D_Flip_Flop #(.trigger("falling")) d_ff_10 (
    .D(data_bus[1]), .clk(and_25_out), .Q(fg[1]), .preset(and_36_out), .reset(or_12_out));  // open: Qn
  Register #(.trigger("falling")) register_7 (
    .D(data_bus), .en(and_33_out), .clk(clk_pin), .Q(register_7_q), .clr(reset));
  Pull_Resistor pull_resistor_87 (.node(INT0));
  or or_18 (or_18_out, reset, INT_LOCK);
  Pull_Resistor pull_resistor_88 (.node(INT1));
  or or_19 (or_19_out, reset, INT_LOCK);
  Pull_Resistor pull_resistor_89 (.node(INT2));
  or or_20 (or_20_out, reset, INT_LOCK);
  Pull_Resistor pull_resistor_90 (.node(INT3));
  or or_21 (or_21_out, reset, INT_LOCK);
  Pull_Resistor pull_resistor_91 (.node(INT4));
  or or_22 (or_22_out, reset, INT_LOCK);
  Pull_Resistor pull_resistor_92 (.node(INT5));
  or or_23 (or_23_out, reset, INT_LOCK);
  Pull_Resistor pull_resistor_93 (.node(INT6));
  or or_24 (or_24_out, reset, INT_LOCK);
  Pull_Resistor pull_resistor_94 (.node(INT7));
  or or_25 (or_25_out, reset, INT_LOCK);
  and and_37 (and_37_out, not_25_out, not_26_out);
  and and_38 (and_38_out, not_27_out, not_28_out);
  and and_39 (and_39_out, not_29_out, not_30_out);
  and and_40 (and_40_out, not_31_out, not_32_out);
  and and_41 (and_41_out, instruction_reg0[0], not_33_out);
  and and_42 (and_42_out, not_34_out, not_35_out);
  and and_43 (and_43_out, instruction_reg1[0], not_36_out);
  and and_44 (and_44_out, not_37_out, not_38_out);
  D_Flip_Flop #(.trigger("falling")) d_ff_11 (
    .D(data_bus[0]), .clk(and_25_out), .Q(fg[0]), .preset(and_59_out), .reset(or_12_out));  // open: Qn
  not not_41 (not_41_out, PUT_FG_DB);
  Comparator comparator_1 (.a(tpsc_q), .b(register_4_q), .eq(comparator_1_eq));  // open: gt, lt
  Comparator comparator_2 (.a(tcnt_q), .b(register_5_q), .eq(comparator_2_eq));  // open: gt, lt
  and and_45 (and_45_out, and_35_out, register_7_q[3]);
  or or_26 (tout, and_45_out, and_46_out);
  and and_46 (and_46_out, d_ff_8_qn, register_7_q[4]);
  S_R_Flip_Flop #(.trigger("high")) s_r_ff_3 (
    .S(and_47_out), .R(or_18_out), .clk(1'b1), .Q(s_r_ff_3_q));  // open: reset, Qn, preset
  and and_47 (and_47_out, register_6_q[0], s_r_ff_2_qn, INT0);
  S_R_Flip_Flop #(.trigger("high")) s_r_ff_4 (
    .S(and_48_out), .R(or_19_out), .clk(1'b1), .Q(s_r_ff_4_q));  // open: reset, Qn, preset
  and and_48 (and_48_out, register_6_q[1], s_r_ff_2_qn, INT1);
  S_R_Flip_Flop #(.trigger("high")) s_r_ff_5 (
    .S(and_49_out), .R(or_20_out), .clk(1'b1), .Q(s_r_ff_5_q));  // open: reset, Qn, preset
  and and_49 (and_49_out, register_6_q[2], s_r_ff_2_qn, INT2);
  S_R_Flip_Flop #(.trigger("high")) s_r_ff_6 (
    .S(and_50_out), .R(or_21_out), .clk(1'b1), .Q(s_r_ff_6_q));  // open: reset, Qn, preset
  and and_50 (and_50_out, register_6_q[3], s_r_ff_2_qn, INT3);
  S_R_Flip_Flop #(.trigger("high")) s_r_ff_7 (
    .S(and_51_out), .R(or_22_out), .clk(1'b1), .Q(s_r_ff_7_q));  // open: reset, Qn, preset
  and and_51 (and_51_out, register_6_q[4], s_r_ff_2_qn, INT4);
  S_R_Flip_Flop #(.trigger("high")) s_r_ff_8 (
    .S(and_52_out), .R(or_23_out), .clk(1'b1), .Q(s_r_ff_8_q));  // open: reset, Qn, preset
  and and_52 (and_52_out, register_6_q[5], s_r_ff_2_qn, INT5);
  S_R_Flip_Flop #(.trigger("high")) s_r_ff_9 (
    .S(and_53_out), .R(or_24_out), .clk(1'b1), .Q(s_r_ff_9_q));  // open: reset, Qn, preset
  and and_53 (and_53_out, register_6_q[6], s_r_ff_2_qn, INT6);
  S_R_Flip_Flop #(.trigger("high")) s_r_ff_10 (
    .S(and_54_out), .R(or_25_out), .clk(1'b1), .Q(s_r_ff_10_q));  // open: reset, Qn, preset
  and and_54 (and_54_out, register_6_q[7], s_r_ff_2_qn, INT7);
  and and_55 (and_55_out, and_37_out, and_38_out);
  and and_56 (and_56_out, and_39_out, and_40_out);
  and and_57 (and_57_out, and_41_out, and_42_out);
  and and_58 (and_58_out, and_43_out, and_44_out);
  Pull_Resistor pull_resistor_95 (.node(transistor_233_out[0]));
  Pull_Resistor pull_resistor_96 (.node(transistor_233_out[1]));
  Pull_Resistor pull_resistor_97 (.node(transistor_233_out[2]));
  Pull_Resistor pull_resistor_98 (.node(transistor_233_out[3]));
  Pull_Resistor pull_resistor_99 (.node(transistor_233_out[4]));
  Pull_Resistor pull_resistor_100 (.node(transistor_233_out[5]));
  Pull_Resistor pull_resistor_101 (.node(transistor_233_out[6]));
  Pull_Resistor pull_resistor_102 (.node(transistor_233_out[7]));
  or or_27 (or_27_out, ALU_ADD, ALU_ADO, ALU_SUB, ALU_SBO, ALU_NAND, ALU_NOR);
  and and_59 (and_59_out, ALU_CMP, transistor_340_out);
  Transistor transistor_289 (.in(fg[0]), .out(data_bus[0]), .gate(not_41_out));
  Transistor transistor_290 (.in(fg[1]), .out(data_bus[1]), .gate(not_41_out));
  Transistor transistor_291 (.in(fg[2]), .out(data_bus[2]), .gate(not_41_out));
  Transistor transistor_292 (.in(fg[3]), .out(data_bus[3]), .gate(not_41_out));
  and and_60 (INT6, and_35_out, register_7_q[2]);
  // Probe on tout
  Transistor transistor_293 (.in(nor_1_out), .out(transistor_233_out[0]), .gate(not_42_out));
  nor nor_1 (nor_1_out, alub_q[0], alua_q[0]);
  Transistor transistor_294 (.in(nor_2_out), .out(transistor_233_out[1]), .gate(not_42_out));
  nor nor_2 (nor_2_out, alub_q[1], alua_q[1]);
  Transistor transistor_295 (.in(nor_3_out), .out(transistor_233_out[2]), .gate(not_42_out));
  nor nor_3 (nor_3_out, alub_q[2], alua_q[2]);
  Transistor transistor_296 (.in(nor_4_out), .out(transistor_233_out[3]), .gate(not_42_out));
  nor nor_4 (nor_4_out, alub_q[3], alua_q[3]);
  Transistor transistor_297 (.in(nor_5_out), .out(transistor_233_out[4]), .gate(not_42_out));
  nor nor_5 (nor_5_out, alub_q[4], alua_q[4]);
  Transistor transistor_298 (.in(nor_6_out), .out(transistor_233_out[5]), .gate(not_42_out));
  nor nor_6 (nor_6_out, alub_q[5], alua_q[5]);
  Transistor transistor_299 (.in(nor_7_out), .out(transistor_233_out[6]), .gate(not_42_out));
  nor nor_7 (nor_7_out, alub_q[6], alua_q[6]);
  Transistor transistor_300 (.in(nor_8_out), .out(transistor_233_out[7]), .gate(not_42_out));
  nor nor_8 (nor_8_out, alub_q[7], alua_q[7]);
  not not_42 (not_42_out, ALU_NOR);
  Register #(.trigger("falling")) aluout (
    .D(transistor_233_out), .en(or_27_out), .clk(clk_pin), .Q(aluout_q), .clr(reset));
  // Probe on fg
  buf buffer_9 (INT_TRIGGER, s_r_ff_3_q);
  buf buffer_10 (INT_TRIGGER, s_r_ff_4_q);
  buf buffer_11 (INT_TRIGGER, s_r_ff_5_q);
  buf buffer_12 (INT_TRIGGER, s_r_ff_6_q);
  buf buffer_13 (INT_TRIGGER, s_r_ff_7_q);
  buf buffer_14 (INT_TRIGGER, s_r_ff_8_q);
  buf buffer_15 (INT_TRIGGER, s_r_ff_9_q);
  buf buffer_16 (INT_TRIGGER, s_r_ff_10_q);
  Pull_Resistor pull_resistor_103 (.node(pull_resistor_103_node[0]));
  Pull_Resistor pull_resistor_104 (.node(pull_resistor_103_node[1]));
  Pull_Resistor pull_resistor_105 (.node(pull_resistor_103_node[2]));
  Pull_Resistor pull_resistor_106 (.node(pull_resistor_103_node[3]));
  Pull_Resistor pull_resistor_107 (.node(pull_resistor_103_node[4]));
  Pull_Resistor pull_resistor_108 (.node(pull_resistor_103_node[5]));
  Pull_Resistor pull_resistor_109 (.node(pull_resistor_103_node[6]));
  Pull_Resistor pull_resistor_110 (.node(pull_resistor_103_node[7]));
  Pull_Resistor pull_resistor_111 (.node(pull_resistor_111_node[0]));
  Pull_Resistor pull_resistor_112 (.node(pull_resistor_111_node[1]));
  Pull_Resistor pull_resistor_113 (.node(pull_resistor_111_node[2]));
  Pull_Resistor pull_resistor_114 (.node(pull_resistor_111_node[3]));
  Pull_Resistor pull_resistor_115 (.node(pull_resistor_111_node[4]));
  Pull_Resistor pull_resistor_116 (.node(pull_resistor_111_node[5]));
  Pull_Resistor pull_resistor_117 (.node(pull_resistor_111_node[6]));
  Pull_Resistor pull_resistor_118 (.node(pull_resistor_111_node[7]));
  Transistor transistor_301 (.in(1'b1), .out(transistor_301_out), .gate(alua_q[0]));
  Transistor transistor_302 (.in(transistor_301_out), .out(transistor_302_out), .gate(alua_q[1]));
  Transistor transistor_303 (.in(transistor_302_out), .out(transistor_303_out), .gate(alua_q[2]));
  Transistor transistor_304 (.in(transistor_303_out), .out(transistor_304_out), .gate(alua_q[3]));
  Transistor transistor_305 (.in(transistor_304_out), .out(transistor_305_out), .gate(alua_q[4]));
  Transistor transistor_306 (.in(transistor_305_out), .out(transistor_306_out), .gate(alua_q[5]));
  Transistor transistor_307 (.in(transistor_306_out), .out(transistor_307_out), .gate(alua_q[6]));
  Transistor transistor_308 (.in(transistor_307_out), .out(transistor_308_out), .gate(alua_q[7]));
  Pull_Resistor pull_resistor_119 (.node(transistor_308_out));
  Transistor transistor_309 (.in(address_bus[0]), .out(pull_resistor_103_node[0]), .gate(not_43_out));
  Transistor transistor_310 (.in(address_bus[1]), .out(pull_resistor_103_node[1]), .gate(not_43_out));
  Transistor transistor_311 (.in(address_bus[2]), .out(pull_resistor_103_node[2]), .gate(not_43_out));
  Transistor transistor_312 (.in(address_bus[3]), .out(pull_resistor_103_node[3]), .gate(not_43_out));
  Transistor transistor_313 (.in(address_bus[4]), .out(pull_resistor_103_node[4]), .gate(not_43_out));
  Transistor transistor_314 (.in(address_bus[5]), .out(pull_resistor_103_node[5]), .gate(not_43_out));
  Transistor transistor_315 (.in(address_bus[6]), .out(pull_resistor_103_node[6]), .gate(not_43_out));
  Transistor transistor_316 (.in(address_bus[7]), .out(pull_resistor_103_node[7]), .gate(not_43_out));
  Transistor transistor_317 (.in(address_bus[8]), .out(pull_resistor_111_node[0]), .gate(not_43_out));
  Transistor transistor_318 (.in(address_bus[9]), .out(pull_resistor_111_node[1]), .gate(not_43_out));
  Transistor transistor_319 (.in(address_bus[10]), .out(pull_resistor_111_node[2]), .gate(not_43_out));
  Transistor transistor_320 (.in(address_bus[11]), .out(pull_resistor_111_node[3]), .gate(not_43_out));
  Transistor transistor_321 (.in(address_bus[12]), .out(pull_resistor_111_node[4]), .gate(not_43_out));
  Transistor transistor_322 (.in(address_bus[13]), .out(pull_resistor_111_node[5]), .gate(not_43_out));
  Transistor transistor_323 (.in(address_bus[14]), .out(pull_resistor_111_node[6]), .gate(not_43_out));
  Transistor transistor_324 (.in(address_bus[15]), .out(pull_resistor_111_node[7]), .gate(not_43_out));
  not not_43 (not_43_out, SAVE_ADDR_A);
  and and_61 (and_61_out, SAVE_DB_IR0, and_55_out);
  and and_62 (and_62_out, SAVE_DB_IR1, and_56_out);
  and and_63 (and_63_out, SAVE_DB_IR0, and_57_out);
  or or_28 (or_28_out, and_63_out, SAVE_ADDR_A, and_64_out);
  and and_64 (and_64_out, SAVE_DB_IR1, and_58_out);
  Transistor transistor_325 (.in(aluout_q[0]), .out(data_bus[0]), .gate(not_44_out));
  Transistor transistor_326 (.in(aluout_q[1]), .out(data_bus[1]), .gate(not_44_out));
  Transistor transistor_327 (.in(aluout_q[2]), .out(data_bus[2]), .gate(not_44_out));
  Transistor transistor_328 (.in(aluout_q[3]), .out(data_bus[3]), .gate(not_44_out));
  Transistor transistor_329 (.in(aluout_q[4]), .out(data_bus[4]), .gate(not_44_out));
  Transistor transistor_330 (.in(aluout_q[5]), .out(data_bus[5]), .gate(not_44_out));
  Transistor transistor_331 (.in(aluout_q[6]), .out(data_bus[6]), .gate(not_44_out));
  Transistor transistor_332 (.in(aluout_q[7]), .out(data_bus[7]), .gate(not_44_out));
  not not_44 (not_44_out, PUT_ALUOUT_DB);
  or or_29 (or_29_out, and_61_out, SAVE_ADDR_A, and_62_out);
  xor xor_7 (xor_7_out, alua_q[0], alub_q[0]);
  xor xor_8 (xor_8_out, alua_q[1], alub_q[1]);
  xor xor_9 (xor_9_out, alua_q[2], alub_q[2]);
  xor xor_10 (xor_10_out, alua_q[3], alub_q[3]);
  xor xor_11 (xor_11_out, alua_q[4], alub_q[4]);
  xor xor_12 (xor_12_out, alua_q[5], alub_q[5]);
  xor xor_13 (xor_13_out, alua_q[6], alub_q[6]);
  xor xor_14 (xor_14_out, alua_q[7], alub_q[7]);
  S_R_Flip_Flop #(.trigger("high")) s_r_ff_11 (
    .S(s_r_ff_3_q), .R(or_30_out), .clk(1'b1), .Q(s_r_ff_11_q[0]));  // open: reset, Qn, preset
  or or_30 (or_30_out, reset, INT_RET_TO_ADDR);
  S_R_Flip_Flop #(.trigger("high")) s_r_ff_12 (
    .S(s_r_ff_4_q), .R(or_31_out), .clk(1'b1), .Q(s_r_ff_11_q[1]));  // open: reset, Qn, preset
  or or_31 (or_31_out, reset, INT_RET_TO_ADDR);
  S_R_Flip_Flop #(.trigger("high")) s_r_ff_13 (
    .S(s_r_ff_5_q), .R(or_32_out), .clk(1'b1), .Q(s_r_ff_11_q[2]));  // open: reset, Qn, preset
  or or_32 (or_32_out, reset, INT_RET_TO_ADDR);
  S_R_Flip_Flop #(.trigger("high")) s_r_ff_14 (
    .S(s_r_ff_6_q), .R(or_33_out), .clk(1'b1), .Q(s_r_ff_11_q[3]));  // open: reset, Qn, preset
  or or_33 (or_33_out, reset, INT_RET_TO_ADDR);
  S_R_Flip_Flop #(.trigger("high")) s_r_ff_15 (
    .S(s_r_ff_7_q), .R(or_34_out), .clk(1'b1), .Q(s_r_ff_11_q[4]));  // open: reset, Qn, preset
  or or_34 (or_34_out, reset, INT_RET_TO_ADDR);
  S_R_Flip_Flop #(.trigger("high")) s_r_ff_16 (
    .S(s_r_ff_8_q), .R(or_35_out), .clk(1'b1), .Q(s_r_ff_11_q[5]));  // open: reset, Qn, preset
  or or_35 (or_35_out, reset, INT_RET_TO_ADDR);
  S_R_Flip_Flop #(.trigger("high")) s_r_ff_17 (
    .S(s_r_ff_9_q), .R(or_36_out), .clk(1'b1), .Q(s_r_ff_11_q[6]));  // open: reset, Qn, preset
  or or_36 (or_36_out, reset, INT_RET_TO_ADDR);
  S_R_Flip_Flop #(.trigger("high")) s_r_ff_18 (
    .S(s_r_ff_10_q), .R(or_37_out), .clk(1'b1), .Q(s_r_ff_11_q[7]));  // open: reset, Qn, preset
  or or_37 (or_37_out, reset, INT_RET_TO_ADDR);
  assign or_38_out = pull_resistor_103_node | data_bus;  // OR_Gate or_38, 8 bits wide
  assign or_39_out = pull_resistor_111_node | data_bus;  // OR_Gate or_39, 8 bits wide
  Register #(.trigger("falling")) r0 (.D(or_38_out), .en(or_29_out), .clk(clk_pin), .Q(r0_q), .clr(reset));
  and and_65 (and_65_out, PUT_IR0_DB, and_55_out);
  and and_66 (and_66_out, PUT_IR1_DB, and_56_out);
  Register #(.trigger("falling")) r1 (.D(or_39_out), .en(or_28_out), .clk(clk_pin), .Q(r1_q), .clr(reset));
  and and_67 (and_67_out, PUT_IR0_DB, and_57_out);
  and and_68 (and_68_out, PUT_IR1_DB, and_58_out);
  Transistor transistor_333 (.in(1'b1), .out(transistor_333_out), .gate(xor_7_out));
  Transistor transistor_334 (.in(transistor_333_out), .out(transistor_334_out), .gate(xor_8_out));
  Transistor transistor_335 (.in(transistor_334_out), .out(transistor_335_out), .gate(xor_9_out));
  Transistor transistor_336 (.in(transistor_335_out), .out(transistor_336_out), .gate(xor_10_out));
  Transistor transistor_337 (.in(transistor_336_out), .out(transistor_337_out), .gate(xor_11_out));
  Transistor transistor_338 (.in(transistor_337_out), .out(transistor_338_out), .gate(xor_12_out));
  Transistor transistor_339 (.in(transistor_338_out), .out(transistor_339_out), .gate(xor_13_out));
  Transistor transistor_340 (.in(transistor_339_out), .out(transistor_340_out), .gate(xor_14_out));
  Pull_Resistor pull_resistor_120 (.node(transistor_340_out));
  or or_40 (or_40_out, and_65_out, and_66_out);
  or or_41 (or_41_out, and_67_out, and_68_out);
  Transistor transistor_341 (.in(r0_q[0]), .out(data_bus[0]), .gate(not_45_out));
  Transistor transistor_342 (.in(r0_q[1]), .out(data_bus[1]), .gate(not_45_out));
  Transistor transistor_343 (.in(r0_q[2]), .out(data_bus[2]), .gate(not_45_out));
  Transistor transistor_344 (.in(r0_q[3]), .out(data_bus[3]), .gate(not_45_out));
  Transistor transistor_345 (.in(r0_q[4]), .out(data_bus[4]), .gate(not_45_out));
  Transistor transistor_346 (.in(r0_q[5]), .out(data_bus[5]), .gate(not_45_out));
  Transistor transistor_347 (.in(r0_q[6]), .out(data_bus[6]), .gate(not_45_out));
  Transistor transistor_348 (.in(r0_q[7]), .out(data_bus[7]), .gate(not_45_out));
  not not_45 (not_45_out, or_40_out);
  Transistor transistor_349 (.in(r1_q[0]), .out(data_bus[0]), .gate(not_46_out));
  Transistor transistor_350 (.in(r1_q[1]), .out(data_bus[1]), .gate(not_46_out));
  Transistor transistor_351 (.in(r1_q[2]), .out(data_bus[2]), .gate(not_46_out));
  Transistor transistor_352 (.in(r1_q[3]), .out(data_bus[3]), .gate(not_46_out));
  Transistor transistor_353 (.in(r1_q[4]), .out(data_bus[4]), .gate(not_46_out));
  Transistor transistor_354 (.in(r1_q[5]), .out(data_bus[5]), .gate(not_46_out));
  Transistor transistor_355 (.in(r1_q[6]), .out(data_bus[6]), .gate(not_46_out));
  Transistor transistor_356 (.in(r1_q[7]), .out(data_bus[7]), .gate(not_46_out));
  not not_46 (not_46_out, or_41_out);
  not not_47 (not_47_out, PUT_A_ADDR);
  Transistor transistor_357 (.in(r0_q[0]), .out(address_bus[0]), .gate(not_47_out));
  Transistor transistor_358 (.in(r0_q[1]), .out(address_bus[1]), .gate(not_47_out));
  Transistor transistor_359 (.in(r0_q[2]), .out(address_bus[2]), .gate(not_47_out));
  Transistor transistor_360 (.in(r0_q[3]), .out(address_bus[3]), .gate(not_47_out));
  Transistor transistor_361 (.in(r0_q[4]), .out(address_bus[4]), .gate(not_47_out));
  Transistor transistor_362 (.in(r0_q[5]), .out(address_bus[5]), .gate(not_47_out));
  Transistor transistor_363 (.in(r0_q[6]), .out(address_bus[6]), .gate(not_47_out));
  Transistor transistor_364 (.in(r0_q[7]), .out(address_bus[7]), .gate(not_47_out));
  Transistor transistor_365 (.in(r1_q[0]), .out(address_bus[8]), .gate(not_47_out));
  Transistor transistor_366 (.in(r1_q[1]), .out(address_bus[9]), .gate(not_47_out));
  Transistor transistor_367 (.in(r1_q[2]), .out(address_bus[10]), .gate(not_47_out));
  Transistor transistor_368 (.in(r1_q[3]), .out(address_bus[11]), .gate(not_47_out));
  Transistor transistor_369 (.in(r1_q[4]), .out(address_bus[12]), .gate(not_47_out));
  Transistor transistor_370 (.in(r1_q[5]), .out(address_bus[13]), .gate(not_47_out));
  Transistor transistor_371 (.in(r1_q[6]), .out(address_bus[14]), .gate(not_47_out));
  Transistor transistor_372 (.in(r1_q[7]), .out(address_bus[15]), .gate(not_47_out));
  not not_48 (not_48_out, instruction_reg0[0]);
  not not_49 (not_49_out, instruction_reg0[1]);
  not not_50 (not_50_out, instruction_reg0[3]);
  not not_51 (not_51_out, instruction_reg1[0]);
  not not_52 (not_52_out, instruction_reg1[1]);
  not not_53 (not_53_out, instruction_reg1[3]);
  not not_54 (not_54_out, instruction_reg0[1]);
  not not_55 (not_55_out, instruction_reg0[3]);
  not not_56 (not_56_out, instruction_reg1[1]);
  not not_57 (not_57_out, instruction_reg1[3]);
  not not_58 (not_58_out, instruction_reg0[0]);
  not not_59 (not_59_out, instruction_reg0[3]);
  not not_60 (not_60_out, instruction_reg1[0]);
  not not_61 (not_61_out, instruction_reg1[3]);
  not not_62 (not_62_out, instruction_reg0[3]);
  not not_63 (not_63_out, instruction_reg1[3]);
  not not_64 (not_64_out, instruction_reg0[0]);
  not not_65 (not_65_out, instruction_reg0[1]);
  not not_66 (not_66_out, instruction_reg0[2]);
  not not_67 (not_67_out, instruction_reg1[0]);
  not not_68 (not_68_out, instruction_reg1[1]);
  not not_69 (not_69_out, instruction_reg1[2]);
  not not_70 (not_70_out, instruction_reg0[1]);
  not not_71 (not_71_out, instruction_reg0[2]);
  not not_72 (not_72_out, instruction_reg1[1]);
  not not_73 (not_73_out, instruction_reg1[2]);
  not not_74 (not_74_out, instruction_reg0[0]);
  not not_75 (not_75_out, instruction_reg0[2]);
  not not_76 (not_76_out, instruction_reg1[0]);
  not not_77 (not_77_out, instruction_reg1[2]);
  not not_78 (not_78_out, instruction_reg0[2]);
  not not_79 (not_79_out, instruction_reg1[2]);
  not not_80 (not_80_out, instruction_reg0[0]);
  not not_81 (not_81_out, instruction_reg0[1]);
  not not_82 (not_82_out, instruction_reg1[0]);
  not not_83 (not_83_out, instruction_reg1[1]);
  not not_84 (not_84_out, instruction_reg0[1]);
  not not_85 (not_85_out, instruction_reg1[1]);
  not not_86 (not_86_out, instruction_reg0[0]);
  not not_87 (not_87_out, instruction_reg1[0]);
  not not_88 (not_88_out, instruction_reg0[0]);
  not not_89 (not_89_out, instruction_reg0[2]);
  not not_90 (not_90_out, instruction_reg0[3]);
  not not_91 (not_91_out, instruction_reg1[0]);
  not not_92 (not_92_out, instruction_reg1[2]);
  not not_93 (not_93_out, instruction_reg1[3]);
  and and_69 (and_69_out, instruction_reg0[0], instruction_reg0[1]);
  not not_94 (not_94_out, instruction_reg0[2]);
  and and_70 (and_70_out, not_94_out, not_95_out);
  not not_95 (not_95_out, instruction_reg0[3]);
  and and_71 (and_71_out, instruction_reg1[0], instruction_reg1[1]);
  not not_96 (not_96_out, instruction_reg1[2]);
  and and_72 (and_72_out, not_96_out, not_97_out);
  not not_97 (not_97_out, instruction_reg1[3]);
  and and_73 (and_73_out, not_48_out, not_49_out);
  and and_74 (and_74_out, instruction_reg0[2], not_50_out);
  and and_75 (and_75_out, not_51_out, not_52_out);
  and and_76 (and_76_out, instruction_reg1[2], not_53_out);
  and and_77 (and_77_out, instruction_reg0[0], not_54_out);
  and and_78 (and_78_out, instruction_reg0[2], not_55_out);
  and and_79 (and_79_out, instruction_reg1[0], not_56_out);
  and and_80 (and_80_out, instruction_reg1[2], not_57_out);
  and and_81 (and_81_out, not_58_out, instruction_reg0[1]);
  and and_82 (and_82_out, instruction_reg0[2], not_59_out);
  and and_83 (and_83_out, not_60_out, instruction_reg1[1]);
  and and_84 (and_84_out, instruction_reg1[2], not_61_out);
  and and_85 (and_85_out, instruction_reg0[0], instruction_reg0[1]);
  and and_86 (and_86_out, instruction_reg0[2], not_62_out);
  and and_87 (and_87_out, instruction_reg1[0], instruction_reg1[1]);
  and and_88 (and_88_out, instruction_reg1[2], not_63_out);
  and and_89 (and_89_out, not_64_out, not_65_out);
  and and_90 (and_90_out, not_66_out, instruction_reg0[3]);
  and and_91 (and_91_out, not_67_out, not_68_out);
  and and_92 (and_92_out, not_69_out, instruction_reg1[3]);
  and and_93 (and_93_out, instruction_reg0[0], not_70_out);
  and and_94 (and_94_out, not_71_out, instruction_reg0[3]);
  and and_95 (and_95_out, instruction_reg1[0], not_72_out);
  and and_96 (and_96_out, not_73_out, instruction_reg1[3]);
  and and_97 (and_97_out, not_74_out, instruction_reg0[1]);
  and and_98 (and_98_out, not_75_out, instruction_reg0[3]);
  and and_99 (and_99_out, not_76_out, instruction_reg1[1]);
  and and_100 (and_100_out, not_77_out, instruction_reg1[3]);
  and and_101 (and_101_out, instruction_reg0[0], instruction_reg0[1]);
  and and_102 (and_102_out, not_78_out, instruction_reg0[3]);
  and and_103 (and_103_out, instruction_reg1[0], instruction_reg1[1]);
  and and_104 (and_104_out, not_79_out, instruction_reg1[3]);
  and and_105 (and_105_out, not_80_out, not_81_out);
  and and_106 (and_106_out, instruction_reg0[2], instruction_reg0[3]);
  and and_107 (and_107_out, not_82_out, not_83_out);
  and and_108 (and_108_out, instruction_reg1[2], instruction_reg1[3]);
  and and_109 (and_109_out, instruction_reg0[0], not_84_out);
  and and_110 (and_110_out, instruction_reg0[2], instruction_reg0[3]);
  and and_111 (and_111_out, instruction_reg1[0], not_85_out);
  and and_112 (and_112_out, instruction_reg1[2], instruction_reg1[3]);
  and and_113 (and_113_out, not_86_out, instruction_reg0[1]);
  and and_114 (and_114_out, instruction_reg0[2], instruction_reg0[3]);
  and and_115 (and_115_out, not_87_out, instruction_reg1[1]);
  and and_116 (and_116_out, instruction_reg1[2], instruction_reg1[3]);
  and and_117 (and_117_out, instruction_reg0[0], instruction_reg0[1]);
  and and_118 (and_118_out, instruction_reg0[2], instruction_reg0[3]);
  and and_119 (and_119_out, instruction_reg1[0], instruction_reg1[1]);
  and and_120 (and_120_out, instruction_reg1[2], instruction_reg1[3]);
  and and_121 (and_121_out, not_88_out, instruction_reg0[1]);
  and and_122 (and_122_out, not_89_out, not_90_out);
  and and_123 (and_123_out, not_91_out, instruction_reg1[1]);
  and and_124 (and_124_out, not_92_out, not_93_out);
  and and_125 (and_125_out, and_69_out, and_70_out);
  and and_126 (and_126_out, and_71_out, and_72_out);
  and and_127 (and_127_out, and_73_out, and_74_out);
  and and_128 (and_128_out, and_75_out, and_76_out);
  and and_129 (and_129_out, and_77_out, and_78_out);
  and and_130 (and_130_out, and_79_out, and_80_out);
  and and_131 (and_131_out, and_81_out, and_82_out);
  and and_132 (and_132_out, and_83_out, and_84_out);
  and and_133 (and_133_out, and_85_out, and_86_out);
  and and_134 (and_134_out, and_87_out, and_88_out);
  and and_135 (and_135_out, and_89_out, and_90_out);
  and and_136 (and_136_out, and_91_out, and_92_out);
  and and_137 (and_137_out, and_93_out, and_94_out);
  and and_138 (and_138_out, and_95_out, and_96_out);
  and and_139 (and_139_out, and_97_out, and_98_out);
  and and_140 (and_140_out, and_99_out, and_100_out);
  and and_141 (and_141_out, and_101_out, and_102_out);
  and and_142 (and_142_out, and_103_out, and_104_out);
  and and_143 (and_143_out, and_105_out, and_106_out);
  and and_144 (and_144_out, and_107_out, and_108_out);
  and and_145 (and_145_out, and_109_out, and_110_out);
  and and_146 (and_146_out, and_111_out, and_112_out);
  and and_147 (and_147_out, and_113_out, and_114_out);
  and and_148 (and_148_out, and_115_out, and_116_out);
  and and_149 (and_149_out, and_117_out, and_118_out);
  and and_150 (and_150_out, and_119_out, and_120_out);
  and and_151 (and_151_out, and_121_out, and_122_out);
  and and_152 (and_152_out, and_123_out, and_124_out);
  Pull_Resistor pull_resistor_121 (.node(pull_resistor_121_node[0]));
  Pull_Resistor pull_resistor_122 (.node(pull_resistor_121_node[1]));
  Pull_Resistor pull_resistor_123 (.node(pull_resistor_121_node[2]));
  Pull_Resistor pull_resistor_124 (.node(pull_resistor_121_node[3]));
  Pull_Resistor pull_resistor_125 (.node(pull_resistor_121_node[4]));
  Pull_Resistor pull_resistor_126 (.node(pull_resistor_121_node[5]));
  Pull_Resistor pull_resistor_127 (.node(pull_resistor_121_node[6]));
  Pull_Resistor pull_resistor_128 (.node(pull_resistor_121_node[7]));
  Pull_Resistor pull_resistor_129 (.node(pull_resistor_129_node[0]));
  Pull_Resistor pull_resistor_130 (.node(pull_resistor_129_node[1]));
  Pull_Resistor pull_resistor_131 (.node(pull_resistor_129_node[2]));
  Pull_Resistor pull_resistor_132 (.node(pull_resistor_129_node[3]));
  Pull_Resistor pull_resistor_133 (.node(pull_resistor_129_node[4]));
  Pull_Resistor pull_resistor_134 (.node(pull_resistor_129_node[5]));
  Pull_Resistor pull_resistor_135 (.node(pull_resistor_129_node[6]));
  Pull_Resistor pull_resistor_136 (.node(pull_resistor_129_node[7]));
  not not_98 (not_98_out, SAVE_ADDR_B);
  and and_153 (and_153_out, SAVE_DB_IR0, and_125_out);
  and and_154 (and_154_out, SAVE_DB_IR1, and_126_out);
  and and_155 (and_155_out, SAVE_DB_IR0, and_127_out);
  and and_156 (and_156_out, SAVE_DB_IR1, and_128_out);
  and and_157 (and_157_out, SAVE_DB_IR0, and_129_out);
  and and_158 (and_158_out, SAVE_DB_IR1, and_130_out);
  and and_159 (and_159_out, SAVE_DB_IR0, and_131_out);
  and and_160 (and_160_out, SAVE_DB_IR1, and_132_out);
  and and_161 (and_161_out, SAVE_DB_IR0, and_133_out);
  and and_162 (and_162_out, SAVE_DB_IR1, and_134_out);
  and and_163 (and_163_out, SAVE_DB_IR0, and_135_out);
  and and_164 (and_164_out, SAVE_DB_IR1, and_136_out);
  and and_165 (and_165_out, SAVE_DB_IR0, and_137_out);
  and and_166 (and_166_out, SAVE_DB_IR1, and_138_out);
  and and_167 (and_167_out, SAVE_DB_IR0, and_139_out);
  and and_168 (and_168_out, SAVE_DB_IR1, and_140_out);
  and and_169 (and_169_out, SAVE_DB_IR0, and_141_out);
  and and_170 (and_170_out, SAVE_DB_IR1, and_142_out);
  and and_171 (and_171_out, SAVE_DB_IR0, and_143_out);
  and and_172 (and_172_out, SAVE_DB_IR1, and_144_out);
  and and_173 (and_173_out, SAVE_DB_IR0, and_145_out);
  and and_174 (and_174_out, SAVE_DB_IR1, and_146_out);
  and and_175 (and_175_out, SAVE_DB_IR0, and_147_out);
  and and_176 (and_176_out, SAVE_DB_IR1, and_148_out);
  and and_177 (and_177_out, SAVE_DB_IR0, and_149_out);
  and and_178 (and_178_out, SAVE_DB_IR1, and_150_out);
  Transistor transistor_373 (.in(address_bus[0]), .out(pull_resistor_121_node[0]), .gate(not_98_out));
  Transistor transistor_374 (.in(address_bus[1]), .out(pull_resistor_121_node[1]), .gate(not_98_out));
  Transistor transistor_375 (.in(address_bus[2]), .out(pull_resistor_121_node[2]), .gate(not_98_out));
  Transistor transistor_376 (.in(address_bus[3]), .out(pull_resistor_121_node[3]), .gate(not_98_out));
  Transistor transistor_377 (.in(address_bus[4]), .out(pull_resistor_121_node[4]), .gate(not_98_out));
  Transistor transistor_378 (.in(address_bus[5]), .out(pull_resistor_121_node[5]), .gate(not_98_out));
  Transistor transistor_379 (.in(address_bus[6]), .out(pull_resistor_121_node[6]), .gate(not_98_out));
  Transistor transistor_380 (.in(address_bus[7]), .out(pull_resistor_121_node[7]), .gate(not_98_out));
  Transistor transistor_381 (.in(address_bus[8]), .out(pull_resistor_129_node[0]), .gate(not_98_out));
  Transistor transistor_382 (.in(address_bus[9]), .out(pull_resistor_129_node[1]), .gate(not_98_out));
  Transistor transistor_383 (.in(address_bus[10]), .out(pull_resistor_129_node[2]), .gate(not_98_out));
  Transistor transistor_384 (.in(address_bus[11]), .out(pull_resistor_129_node[3]), .gate(not_98_out));
  Transistor transistor_385 (.in(address_bus[12]), .out(pull_resistor_129_node[4]), .gate(not_98_out));
  Transistor transistor_386 (.in(address_bus[13]), .out(pull_resistor_129_node[5]), .gate(not_98_out));
  Transistor transistor_387 (.in(address_bus[14]), .out(pull_resistor_129_node[6]), .gate(not_98_out));
  Transistor transistor_388 (.in(address_bus[15]), .out(pull_resistor_129_node[7]), .gate(not_98_out));
  and and_179 (and_179_out, SAVE_DB_IR0, and_151_out);
  or or_42 (or_42_out, and_179_out, SAVE_ADDR_B, and_180_out);
  and and_180 (and_180_out, SAVE_DB_IR1, and_152_out);
  or or_43 (or_43_out, and_153_out, SAVE_ADDR_B, and_154_out);
  or or_44 (or_44_out, and_155_out, and_156_out);
  or or_45 (or_45_out, and_157_out, and_158_out);
  or or_46 (or_46_out, and_159_out, and_160_out);
  or or_47 (or_47_out, and_161_out, and_162_out);
  or or_48 (or_48_out, and_163_out, and_164_out);
  or or_49 (or_49_out, and_165_out, and_166_out);
  or or_50 (or_50_out, and_167_out, and_168_out);
  or or_51 (or_51_out, and_169_out, and_170_out);
  or or_52 (or_52_out, and_171_out, and_172_out);
  or or_53 (or_53_out, and_173_out, and_174_out);
  or or_54 (or_54_out, and_175_out, and_176_out);
  or or_55 (or_55_out, and_177_out, and_178_out);
  Register #(.trigger("falling")) r3 (.D(or_57_out), .en(or_43_out), .clk(clk_pin), .Q(r3_q), .clr(reset));
  Register #(.trigger("falling")) r4 (.D(data_bus), .en(or_44_out), .clk(clk_pin), .Q(r4_q), .clr(reset));
  and and_181 (and_181_out, PUT_IR0_DB, and_127_out);
  and and_182 (and_182_out, PUT_IR1_DB, and_128_out);
  Register #(.trigger("falling")) r5 (.D(data_bus), .en(or_45_out), .clk(clk_pin), .Q(r5_q), .clr(reset));
  and and_183 (and_183_out, PUT_IR0_DB, and_129_out);
  and and_184 (and_184_out, PUT_IR1_DB, and_130_out);
  Register #(.trigger("falling")) r6 (.D(data_bus), .en(or_46_out), .clk(clk_pin), .Q(r6_q), .clr(reset));
  and and_185 (and_185_out, PUT_IR0_DB, and_131_out);
  and and_186 (and_186_out, PUT_IR1_DB, and_132_out);
  Register #(.trigger("falling")) r7 (.D(data_bus), .en(or_47_out), .clk(clk_pin), .Q(r7_q), .clr(reset));
  and and_187 (and_187_out, PUT_IR0_DB, and_133_out);
  and and_188 (and_188_out, PUT_IR1_DB, and_134_out);
  Register #(.trigger("falling")) r8 (.D(data_bus), .en(or_48_out), .clk(clk_pin), .Q(r8_q), .clr(reset));
  and and_189 (and_189_out, PUT_IR0_DB, and_135_out);
  and and_190 (and_190_out, PUT_IR1_DB, and_136_out);
  Register #(.trigger("falling")) r9 (.D(data_bus), .en(or_49_out), .clk(clk_pin), .Q(r9_q), .clr(reset));
  Register #(.trigger("falling")) r10 (.D(data_bus), .en(or_50_out), .clk(clk_pin), .Q(r10_q), .clr(reset));
  and and_191 (and_191_out, PUT_IR0_DB, and_139_out);
  and and_192 (and_192_out, PUT_IR1_DB, and_140_out);
  Register #(.trigger("falling")) r11 (.D(data_bus), .en(or_51_out), .clk(clk_pin), .Q(r11_q), .clr(reset));
  Register #(.trigger("falling")) r12 (.D(data_bus), .en(or_52_out), .clk(clk_pin), .Q(r12_q), .clr(reset));
  and and_193 (and_193_out, PUT_IR0_DB, and_143_out);
  and and_194 (and_194_out, PUT_IR1_DB, and_144_out);
  Register #(.trigger("falling")) r13 (.D(data_bus), .en(or_53_out), .clk(clk_pin), .Q(r13_q), .clr(reset));
  and and_195 (and_195_out, PUT_IR0_DB, and_145_out);
  and and_196 (and_196_out, PUT_IR1_DB, and_146_out);
  Register #(.trigger("falling")) r14 (.D(data_bus), .en(or_54_out), .clk(clk_pin), .Q(r14_q), .clr(reset));
  and and_197 (and_197_out, PUT_IR0_DB, and_147_out);
  and and_198 (and_198_out, PUT_IR1_DB, and_148_out);
  Register #(.trigger("falling")) r15 (.D(data_bus), .en(or_55_out), .clk(clk_pin), .Q(r15_q), .clr(reset));
  and and_199 (and_199_out, PUT_IR0_DB, and_149_out);
  and and_200 (and_200_out, PUT_IR1_DB, and_150_out);
  assign or_56_out = pull_resistor_121_node | data_bus;  // OR_Gate or_56, 8 bits wide
  assign or_57_out = pull_resistor_129_node | data_bus;  // OR_Gate or_57, 8 bits wide
  Register #(.trigger("falling")) r2 (.D(or_56_out), .en(or_42_out), .clk(clk_pin), .Q(r2_q), .clr(reset));
  and and_201 (and_201_out, PUT_IR0_DB, and_151_out);
  and and_202 (and_202_out, PUT_IR1_DB, and_152_out);
  and and_203 (and_203_out, PUT_IR0_DB, and_125_out);
  and and_204 (and_204_out, PUT_IR1_DB, and_126_out);
  and and_205 (and_205_out, PUT_IR0_DB, and_137_out);
  and and_206 (and_206_out, PUT_IR1_DB, and_138_out);
  and and_207 (and_207_out, PUT_IR0_DB, and_141_out);
  and and_208 (and_208_out, PUT_IR1_DB, and_142_out);
  or or_58 (or_58_out, and_201_out, and_202_out);
  or or_59 (or_59_out, and_203_out, and_204_out);
  not not_99 (not_99_out, or_59_out);
  or or_60 (or_60_out, and_181_out, and_182_out);
  not not_100 (not_100_out, or_60_out);
  or or_61 (or_61_out, and_183_out, and_184_out);
  not not_101 (not_101_out, or_61_out);
  or or_62 (or_62_out, and_185_out, and_186_out);
  not not_102 (not_102_out, or_62_out);
  or or_63 (or_63_out, and_187_out, and_188_out);
  not not_103 (not_103_out, or_63_out);
  or or_64 (or_64_out, and_189_out, and_190_out);
  not not_104 (not_104_out, or_64_out);
  or or_65 (or_65_out, and_205_out, and_206_out);
  not not_105 (not_105_out, or_65_out);
  or or_66 (or_66_out, and_191_out, and_192_out);
  not not_106 (not_106_out, or_66_out);
  or or_67 (or_67_out, and_207_out, and_208_out);
  not not_107 (not_107_out, or_67_out);
  or or_68 (or_68_out, and_193_out, and_194_out);
  not not_108 (not_108_out, or_68_out);
  or or_69 (or_69_out, and_195_out, and_196_out);
  not not_109 (not_109_out, or_69_out);
  or or_70 (or_70_out, and_197_out, and_198_out);
  not not_110 (not_110_out, or_70_out);
  or or_71 (or_71_out, and_199_out, and_200_out);
  not not_111 (not_111_out, or_71_out);
  Transistor transistor_389 (.in(r2_q[0]), .out(data_bus[0]), .gate(not_112_out));
  Transistor transistor_390 (.in(r2_q[1]), .out(data_bus[1]), .gate(not_112_out));
  Transistor transistor_391 (.in(r2_q[2]), .out(data_bus[2]), .gate(not_112_out));
  Transistor transistor_392 (.in(r2_q[3]), .out(data_bus[3]), .gate(not_112_out));
  Transistor transistor_393 (.in(r2_q[4]), .out(data_bus[4]), .gate(not_112_out));
  Transistor transistor_394 (.in(r2_q[5]), .out(data_bus[5]), .gate(not_112_out));
  Transistor transistor_395 (.in(r2_q[6]), .out(data_bus[6]), .gate(not_112_out));
  Transistor transistor_396 (.in(r2_q[7]), .out(data_bus[7]), .gate(not_112_out));
  not not_112 (not_112_out, or_58_out);
  Transistor transistor_397 (.in(r3_q[0]), .out(data_bus[0]), .gate(not_99_out));
  Transistor transistor_398 (.in(r3_q[1]), .out(data_bus[1]), .gate(not_99_out));
  Transistor transistor_399 (.in(r3_q[2]), .out(data_bus[2]), .gate(not_99_out));
  Transistor transistor_400 (.in(r3_q[3]), .out(data_bus[3]), .gate(not_99_out));
  Transistor transistor_401 (.in(r3_q[4]), .out(data_bus[4]), .gate(not_99_out));
  Transistor transistor_402 (.in(r3_q[5]), .out(data_bus[5]), .gate(not_99_out));
  Transistor transistor_403 (.in(r3_q[6]), .out(data_bus[6]), .gate(not_99_out));
  Transistor transistor_404 (.in(r3_q[7]), .out(data_bus[7]), .gate(not_99_out));
  Transistor transistor_405 (.in(r4_q[0]), .out(data_bus[0]), .gate(not_100_out));
  Transistor transistor_406 (.in(r4_q[1]), .out(data_bus[1]), .gate(not_100_out));
  Transistor transistor_407 (.in(r4_q[2]), .out(data_bus[2]), .gate(not_100_out));
  Transistor transistor_408 (.in(r4_q[3]), .out(data_bus[3]), .gate(not_100_out));
  Transistor transistor_409 (.in(r4_q[4]), .out(data_bus[4]), .gate(not_100_out));
  Transistor transistor_410 (.in(r4_q[5]), .out(data_bus[5]), .gate(not_100_out));
  Transistor transistor_411 (.in(r4_q[6]), .out(data_bus[6]), .gate(not_100_out));
  Transistor transistor_412 (.in(r4_q[7]), .out(data_bus[7]), .gate(not_100_out));
  Transistor transistor_413 (.in(r5_q[0]), .out(data_bus[0]), .gate(not_101_out));
  Transistor transistor_414 (.in(r5_q[1]), .out(data_bus[1]), .gate(not_101_out));
  Transistor transistor_415 (.in(r5_q[2]), .out(data_bus[2]), .gate(not_101_out));
  Transistor transistor_416 (.in(r5_q[3]), .out(data_bus[3]), .gate(not_101_out));
  Transistor transistor_417 (.in(r5_q[4]), .out(data_bus[4]), .gate(not_101_out));
  Transistor transistor_418 (.in(r5_q[5]), .out(data_bus[5]), .gate(not_101_out));
  Transistor transistor_419 (.in(r5_q[6]), .out(data_bus[6]), .gate(not_101_out));
  Transistor transistor_420 (.in(r5_q[7]), .out(data_bus[7]), .gate(not_101_out));
  Transistor transistor_421 (.in(r6_q[0]), .out(data_bus[0]), .gate(not_102_out));
  Transistor transistor_422 (.in(r6_q[1]), .out(data_bus[1]), .gate(not_102_out));
  Transistor transistor_423 (.in(r6_q[2]), .out(data_bus[2]), .gate(not_102_out));
  Transistor transistor_424 (.in(r6_q[3]), .out(data_bus[3]), .gate(not_102_out));
  Transistor transistor_425 (.in(r6_q[4]), .out(data_bus[4]), .gate(not_102_out));
  Transistor transistor_426 (.in(r6_q[5]), .out(data_bus[5]), .gate(not_102_out));
  Transistor transistor_427 (.in(r6_q[6]), .out(data_bus[6]), .gate(not_102_out));
  Transistor transistor_428 (.in(r6_q[7]), .out(data_bus[7]), .gate(not_102_out));
  Transistor transistor_429 (.in(r7_q[0]), .out(data_bus[0]), .gate(not_103_out));
  Transistor transistor_430 (.in(r7_q[1]), .out(data_bus[1]), .gate(not_103_out));
  Transistor transistor_431 (.in(r7_q[2]), .out(data_bus[2]), .gate(not_103_out));
  Transistor transistor_432 (.in(r7_q[3]), .out(data_bus[3]), .gate(not_103_out));
  Transistor transistor_433 (.in(r7_q[4]), .out(data_bus[4]), .gate(not_103_out));
  Transistor transistor_434 (.in(r7_q[5]), .out(data_bus[5]), .gate(not_103_out));
  Transistor transistor_435 (.in(r7_q[6]), .out(data_bus[6]), .gate(not_103_out));
  Transistor transistor_436 (.in(r7_q[7]), .out(data_bus[7]), .gate(not_103_out));
  Transistor transistor_437 (.in(r8_q[0]), .out(data_bus[0]), .gate(not_104_out));
  Transistor transistor_438 (.in(r8_q[1]), .out(data_bus[1]), .gate(not_104_out));
  Transistor transistor_439 (.in(r8_q[2]), .out(data_bus[2]), .gate(not_104_out));
  Transistor transistor_440 (.in(r8_q[3]), .out(data_bus[3]), .gate(not_104_out));
  Transistor transistor_441 (.in(r8_q[4]), .out(data_bus[4]), .gate(not_104_out));
  Transistor transistor_442 (.in(r8_q[5]), .out(data_bus[5]), .gate(not_104_out));
  Transistor transistor_443 (.in(r8_q[6]), .out(data_bus[6]), .gate(not_104_out));
  Transistor transistor_444 (.in(r8_q[7]), .out(data_bus[7]), .gate(not_104_out));
  Transistor transistor_445 (.in(r9_q[0]), .out(data_bus[0]), .gate(not_105_out));
  Transistor transistor_446 (.in(r9_q[1]), .out(data_bus[1]), .gate(not_105_out));
  Transistor transistor_447 (.in(r9_q[2]), .out(data_bus[2]), .gate(not_105_out));
  Transistor transistor_448 (.in(r9_q[3]), .out(data_bus[3]), .gate(not_105_out));
  Transistor transistor_449 (.in(r9_q[4]), .out(data_bus[4]), .gate(not_105_out));
  Transistor transistor_450 (.in(r9_q[5]), .out(data_bus[5]), .gate(not_105_out));
  Transistor transistor_451 (.in(r9_q[6]), .out(data_bus[6]), .gate(not_105_out));
  Transistor transistor_452 (.in(r9_q[7]), .out(data_bus[7]), .gate(not_105_out));
  Transistor transistor_453 (.in(r10_q[0]), .out(data_bus[0]), .gate(not_106_out));
  Transistor transistor_454 (.in(r10_q[1]), .out(data_bus[1]), .gate(not_106_out));
  Transistor transistor_455 (.in(r10_q[2]), .out(data_bus[2]), .gate(not_106_out));
  Transistor transistor_456 (.in(r10_q[3]), .out(data_bus[3]), .gate(not_106_out));
  Transistor transistor_457 (.in(r10_q[4]), .out(data_bus[4]), .gate(not_106_out));
  Transistor transistor_458 (.in(r10_q[5]), .out(data_bus[5]), .gate(not_106_out));
  Transistor transistor_459 (.in(r10_q[6]), .out(data_bus[6]), .gate(not_106_out));
  Transistor transistor_460 (.in(r10_q[7]), .out(data_bus[7]), .gate(not_106_out));
  Transistor transistor_461 (.in(r11_q[0]), .out(data_bus[0]), .gate(not_107_out));
  Transistor transistor_462 (.in(r11_q[1]), .out(data_bus[1]), .gate(not_107_out));
  Transistor transistor_463 (.in(r11_q[2]), .out(data_bus[2]), .gate(not_107_out));
  Transistor transistor_464 (.in(r11_q[3]), .out(data_bus[3]), .gate(not_107_out));
  Transistor transistor_465 (.in(r11_q[4]), .out(data_bus[4]), .gate(not_107_out));
  Transistor transistor_466 (.in(r11_q[5]), .out(data_bus[5]), .gate(not_107_out));
  Transistor transistor_467 (.in(r11_q[6]), .out(data_bus[6]), .gate(not_107_out));
  Transistor transistor_468 (.in(r11_q[7]), .out(data_bus[7]), .gate(not_107_out));
  Transistor transistor_469 (.in(r12_q[0]), .out(data_bus[0]), .gate(not_108_out));
  Transistor transistor_470 (.in(r12_q[1]), .out(data_bus[1]), .gate(not_108_out));
  Transistor transistor_471 (.in(r12_q[2]), .out(data_bus[2]), .gate(not_108_out));
  Transistor transistor_472 (.in(r12_q[3]), .out(data_bus[3]), .gate(not_108_out));
  Transistor transistor_473 (.in(r12_q[4]), .out(data_bus[4]), .gate(not_108_out));
  Transistor transistor_474 (.in(r12_q[5]), .out(data_bus[5]), .gate(not_108_out));
  Transistor transistor_475 (.in(r12_q[6]), .out(data_bus[6]), .gate(not_108_out));
  Transistor transistor_476 (.in(r12_q[7]), .out(data_bus[7]), .gate(not_108_out));
  Transistor transistor_477 (.in(r13_q[0]), .out(data_bus[0]), .gate(not_109_out));
  Transistor transistor_478 (.in(r13_q[1]), .out(data_bus[1]), .gate(not_109_out));
  Transistor transistor_479 (.in(r13_q[2]), .out(data_bus[2]), .gate(not_109_out));
  Transistor transistor_480 (.in(r13_q[3]), .out(data_bus[3]), .gate(not_109_out));
  Transistor transistor_481 (.in(r13_q[4]), .out(data_bus[4]), .gate(not_109_out));
  Transistor transistor_482 (.in(r13_q[5]), .out(data_bus[5]), .gate(not_109_out));
  Transistor transistor_483 (.in(r13_q[6]), .out(data_bus[6]), .gate(not_109_out));
  Transistor transistor_484 (.in(r13_q[7]), .out(data_bus[7]), .gate(not_109_out));
  Transistor transistor_485 (.in(r14_q[0]), .out(data_bus[0]), .gate(not_110_out));
  Transistor transistor_486 (.in(r14_q[1]), .out(data_bus[1]), .gate(not_110_out));
  Transistor transistor_487 (.in(r14_q[2]), .out(data_bus[2]), .gate(not_110_out));
  Transistor transistor_488 (.in(r14_q[3]), .out(data_bus[3]), .gate(not_110_out));
  Transistor transistor_489 (.in(r14_q[4]), .out(data_bus[4]), .gate(not_110_out));
  Transistor transistor_490 (.in(r14_q[5]), .out(data_bus[5]), .gate(not_110_out));
  Transistor transistor_491 (.in(r14_q[6]), .out(data_bus[6]), .gate(not_110_out));
  Transistor transistor_492 (.in(r14_q[7]), .out(data_bus[7]), .gate(not_110_out));
  Transistor transistor_493 (.in(r15_q[0]), .out(data_bus[0]), .gate(not_111_out));
  Transistor transistor_494 (.in(r15_q[1]), .out(data_bus[1]), .gate(not_111_out));
  Transistor transistor_495 (.in(r15_q[2]), .out(data_bus[2]), .gate(not_111_out));
  Transistor transistor_496 (.in(r15_q[3]), .out(data_bus[3]), .gate(not_111_out));
  Transistor transistor_497 (.in(r15_q[4]), .out(data_bus[4]), .gate(not_111_out));
  Transistor transistor_498 (.in(r15_q[5]), .out(data_bus[5]), .gate(not_111_out));
  Transistor transistor_499 (.in(r15_q[6]), .out(data_bus[6]), .gate(not_111_out));
  Transistor transistor_500 (.in(r15_q[7]), .out(data_bus[7]), .gate(not_111_out));
  not not_113 (not_113_out, PUT_B_ADDR);
  Transistor transistor_501 (.in(r2_q[0]), .out(address_bus[0]), .gate(not_113_out));
  Transistor transistor_502 (.in(r2_q[1]), .out(address_bus[1]), .gate(not_113_out));
  Transistor transistor_503 (.in(r2_q[2]), .out(address_bus[2]), .gate(not_113_out));
  Transistor transistor_504 (.in(r2_q[3]), .out(address_bus[3]), .gate(not_113_out));
  Transistor transistor_505 (.in(r2_q[4]), .out(address_bus[4]), .gate(not_113_out));
  Transistor transistor_506 (.in(r2_q[5]), .out(address_bus[5]), .gate(not_113_out));
  Transistor transistor_507 (.in(r2_q[6]), .out(address_bus[6]), .gate(not_113_out));
  Transistor transistor_508 (.in(r2_q[7]), .out(address_bus[7]), .gate(not_113_out));
  Transistor transistor_509 (.in(r3_q[0]), .out(address_bus[8]), .gate(not_113_out));
  Transistor transistor_510 (.in(r3_q[1]), .out(address_bus[9]), .gate(not_113_out));
  Transistor transistor_511 (.in(r3_q[2]), .out(address_bus[10]), .gate(not_113_out));
  Transistor transistor_512 (.in(r3_q[3]), .out(address_bus[11]), .gate(not_113_out));
  Transistor transistor_513 (.in(r3_q[4]), .out(address_bus[12]), .gate(not_113_out));
  Transistor transistor_514 (.in(r3_q[5]), .out(address_bus[13]), .gate(not_113_out));
  Transistor transistor_515 (.in(r3_q[6]), .out(address_bus[14]), .gate(not_113_out));
  Transistor transistor_516 (.in(r3_q[7]), .out(address_bus[15]), .gate(not_113_out));
  or or_72 (or_72_out, SP_UP, SP_DOWN, SAVE_ADDR_SP);
  Counter #(.max('hffff), .trigger("falling"), .width(16)) sp (
    .clr(reset), .load(SAVE_ADDR_SP), .up(SP_UP), .count(or_72_out), .clk(clk_pin), .D(address_bus), .Q(sp_q));  // open: carry
  not not_114 (not_114_out, PUT_SP_ADDR);
  Transistor transistor_517 (.in(sp_q[0]), .out(address_bus[0]), .gate(not_114_out));
  Transistor transistor_518 (.in(sp_q[1]), .out(address_bus[1]), .gate(not_114_out));
  Transistor transistor_519 (.in(sp_q[2]), .out(address_bus[2]), .gate(not_114_out));
  Transistor transistor_520 (.in(sp_q[3]), .out(address_bus[3]), .gate(not_114_out));
  Transistor transistor_521 (.in(sp_q[4]), .out(address_bus[4]), .gate(not_114_out));
  Transistor transistor_522 (.in(sp_q[5]), .out(address_bus[5]), .gate(not_114_out));
  Transistor transistor_523 (.in(sp_q[6]), .out(address_bus[6]), .gate(not_114_out));
  Transistor transistor_524 (.in(sp_q[7]), .out(address_bus[7]), .gate(not_114_out));
  Transistor transistor_525 (.in(sp_q[8]), .out(address_bus[8]), .gate(not_114_out));
  Transistor transistor_526 (.in(sp_q[9]), .out(address_bus[9]), .gate(not_114_out));
  Transistor transistor_527 (.in(sp_q[10]), .out(address_bus[10]), .gate(not_114_out));
  Transistor transistor_528 (.in(sp_q[11]), .out(address_bus[11]), .gate(not_114_out));
  Transistor transistor_529 (.in(sp_q[12]), .out(address_bus[12]), .gate(not_114_out));
  Transistor transistor_530 (.in(sp_q[13]), .out(address_bus[13]), .gate(not_114_out));
  Transistor transistor_531 (.in(sp_q[14]), .out(address_bus[14]), .gate(not_114_out));
  Transistor transistor_532 (.in(sp_q[15]), .out(address_bus[15]), .gate(not_114_out));

  // Other names for the same wires on the sheet: clk = clk_pin; INT_RESET = INT_LOCK; PUT_MEM_DB = memory_read;
  //   SAVE_DB_MEM = memory_write

  // Notes on the sheet:
  //   contents of rom_1 (hex, n*v repeats v):
  //   22 2 ff 2 4 f 3 4 0 22 3 ff 2 4 11 3 4 0 1d 12
  //   contents of MC1 (hex, n*v repeats v):
  //   0 80000000 7*0 c 80000000 6*0 28 80000000 6*0 800003 80000000 6*0 400009 80000000 6*0 1801 40000
  //   80000000 5*0 42 84 100 408 80000000 0 0 0 42 a0 100 408 80000000 0 0 0 42 84 80000 408 80000000 0 0
  //   0 42 a0 80000 408 80000000 0 0 0 42 84 100000 408 80000000 0 0 0 42 a0 100000 408 80000000 0 0 0 42
  //   84 200000 408 80000000 0 0 0 42 a0 200000 408 80000000 0 0 0 42 84 200 80000000 4*0 42 a0 200
  //   80000000 4*0 1001 40000 80000000 5*0 10009 80000000 6*0 8003 80000000 6*0 4001 20000 0 80000000 4*0
  //   2001 40000 80000000 5*0 2801 40000 80000000 5*0 1001800 40000 80000000 5*0 1001000 40000 80000000
  //   5*0 1004000 20000 0 80000000 4*0 1002000 40000 80000000 5*0 1002800 40000 80000000 5*0 1010008
  //   80000000 6*0 1008002 80000000 6*0 2004000 20000 0 80000000 4*0 2002000 40000 80000000 5*0 2002800
  //   40000 80000000 13*0 2001800 40000 80000000 5*0 6000000 80000000 6*0 a000000 80000000 6*0 1800002
  //   80000000 6*0 1400008 80000000 6*0 10004000 20000 80000000 5*0 20000000 80000000 6*0 1 40000 80000000
  //   5*0 1000000 40000 80000000 5*0 2000000 40000 80000000 5*0 801 40000 6*0 1000800 40000 80000000 5*0
  //   2000800 80000000 80000000 5*0 42 84 0 408 80000000 0 0 0 42 a0 0 408 80000000 0 0 0 42 84 0 408
  //   80000000 0 0 0 42 a0 0 408 80000000 11*0 1 80000000 6*0 1000000 80000000 6*0 2000000 80000000 6*0 2
  //   80000000 6*0 8 80000000 6*0 1 80000000 6*0 1000000 80000000 6*0 2000000 80000000 6*0 4000000
  //   80000000 6*0 8000000 80000000 6*0 8020 0 80000000 5*0 8002 0 80000000 6*0 10008 80000000
  //   contents of MC2 (hex, n*v repeats v):
  //   114*0 2 206*0 1 7*0 1 7*0 1 7*0 1 7*0 1 7*0 1 9*0 4 7*0 4 7*0 8 7*0 8 5*0 2 7*0 10 7*0 10 7*0 10 7*0
  //   40 7*0 20 7*0 200 7*0 200 7*0 200 7*0 400 7*0 400 7*0 400 100 6*0 400 100 6*0 80 400
  //   buffer_1 drives only 1 and floats otherwise
  //   buffer_2 drives only 1 and floats otherwise
  //   buffer_3 drives only 1 and floats otherwise
  //   buffer_4 drives only 1 and floats otherwise
  //   buffer_5 drives only 1 and floats otherwise
  //   buffer_6 drives only 1 and floats otherwise
  //   buffer_7 drives only 1 and floats otherwise
  //   buffer_8 drives only 1 and floats otherwise
  //   buffer_9 drives only 1 and floats otherwise
  //   buffer_10 drives only 1 and floats otherwise
  //   buffer_11 drives only 1 and floats otherwise
  //   buffer_12 drives only 1 and floats otherwise
  //   buffer_13 drives only 1 and floats otherwise
  //   buffer_14 drives only 1 and floats otherwise
  //   buffer_15 drives only 1 and floats otherwise
  //   buffer_16 drives only 1 and floats otherwise
endmodule
