// Logisim project phoenix.circ as structural Verilog: 3 circuits, main circuit main
module core (
  input  int0,
  input  int1,
  input  int2,
  input  int3,
  input  int4,
  input  int5,
  input  [7:0] data_bus_in,
  input  reset,
  input  clk,
  output mem_write,
  output mem_read,
  output [7:0] data_bus_out,
  output [15:0] address_bus,
  output clk_out,
  output io_in,
  output io_out,
  output timer_out
);

  wire adder_1_cout, ALU_ADD, ALU_ADO, ALU_CMP, ALU_NAND, ALU_NOR, ALU_SBO, ALU_SUB, and_1_out, and_3_out,
       and_4_out, and_7_out, and_8_out, and_9_out, and_10_out, and_11_out, and_12_out, and_13_out,
       and_14_out, and_15_out, and_16_out, and_17_out, and_18_out, and_19_out, and_20_out, and_21_out,
       and_22_out, and_23_out, and_24_out, and_25_out, and_26_out, and_27_out, and_28_out, and_29_out,
       and_30_out, and_31_out, and_32_out, and_33_out, and_34_out, and_35_out, and_36_out, and_37_out,
       and_38_out, and_39_out, and_40_out, and_41_out, and_42_out, and_43_out, and_44_out, and_45_out,
       and_46_out, and_47_out, and_48_out, and_49_out, and_50_out, and_51_out, and_52_out, and_54_out,
       and_55_out, and_56_out, and_57_out, and_58_out, and_59_out, and_60_out, and_61_out, and_62_out,
       and_63_out, and_64_out, and_65_out, and_66_out, and_67_out, and_68_out, and_69_out, and_70_out,
       and_71_out, and_72_out, and_73_out, and_74_out, and_75_out, and_76_out, and_77_out, and_78_out,
       and_79_out, and_80_out, and_81_out, and_82_out, and_83_out, and_84_out, and_85_out, and_86_out,
       and_87_out, and_88_out, and_89_out, and_90_out, and_91_out, and_92_out, and_93_out, and_94_out,
       and_95_out, and_96_out, and_97_out, and_98_out, and_99_out, and_100_out, and_101_out, and_102_out,
       and_103_out, and_104_out, and_105_out, and_106_out, and_107_out, and_108_out, and_109_out,
       and_110_out, and_111_out, and_112_out, and_113_out, and_114_out, and_115_out, and_116_out,
       and_117_out, and_118_out, and_119_out, and_120_out, and_121_out, and_122_out, and_123_out,
       and_124_out, and_125_out, and_126_out, and_127_out, and_128_out, and_129_out, and_130_out,
       and_131_out, and_132_out, and_133_out, and_134_out, and_135_out, and_136_out, and_137_out,
       and_138_out, and_139_out, and_140_out, and_141_out, and_142_out, and_143_out, and_144_out,
       and_145_out, and_146_out, and_147_out, and_148_out, and_149_out, and_150_out, and_151_out,
       and_152_out, and_153_out, and_154_out, and_155_out, and_156_out, and_157_out, and_158_out,
       and_159_out, and_160_out, and_161_out, and_162_out, and_163_out, and_164_out, and_165_out,
       and_166_out, and_167_out, and_168_out, and_169_out, and_170_out, and_171_out, and_172_out,
       and_173_out, and_174_out, and_175_out, and_176_out, and_177_out, and_178_out, and_179_out,
       and_180_out, and_181_out, and_182_out, and_183_out, and_184_out, and_185_out, and_186_out,
       and_187_out, and_188_out, and_189_out, and_190_out, and_191_out, and_192_out, and_193_out,
       and_194_out, and_195_out, and_196_out, and_197_out, and_198_out, and_199_out, and_200_out,
       and_201_out, buffer_8_out, CLEAR_FG, comparator_1_eq, comparator_2_eq, COND_INVERT, counter_1_carry,
       d_ff_1_q, d_ff_2_q, d_ff_3_q, d_ff_4_q, d_ff_5_q, d_ff_6_q, d_ff_8_qn, halt, INT6, INT7, INT_DISABLE,
       INT_LOCK, INT_RET_TO_ADDR, INT_TRIGGER, multiplexer_1_out, nand_1_out, nand_2_out, nand_3_out,
       nand_4_out, nand_5_out, nand_6_out, nand_7_out, nand_8_out, nor_1_out, nor_2_out, nor_3_out,
       nor_4_out, nor_5_out, nor_6_out, nor_7_out, nor_8_out, not_1_out, not_2_out, not_3_out, not_4_out,
       not_5_out, not_6_out, not_7_out, not_8_out, not_9_out, not_10_out, not_11_out, not_12_out, not_13_out,
       not_14_out, not_15_out, not_16_out, not_17_out, not_18_out, not_19_out, not_20_out, not_21_out,
       not_22_out, not_23_out, not_24_out, not_25_out, not_26_out, not_27_out, not_28_out, not_29_out,
       not_30_out, not_31_out, not_32_out, not_33_out, not_34_out, not_35_out, not_36_out, not_37_out,
       not_38_out, not_39_out, not_40_out, not_41_out, not_42_out, not_43_out, not_44_out, not_45_out,
       not_46_out, not_47_out, not_48_out, not_49_out, not_50_out, not_51_out, not_52_out, not_53_out,
       not_54_out, not_55_out, not_56_out, not_57_out, not_58_out, not_59_out, not_60_out, not_61_out,
       not_62_out, not_63_out, not_64_out, not_65_out, not_66_out, not_67_out, not_68_out, not_69_out,
       not_70_out, not_71_out, not_72_out, not_73_out, not_74_out, not_75_out, not_76_out, not_77_out,
       not_78_out, not_79_out, not_80_out, not_81_out, not_82_out, not_83_out, not_84_out, not_85_out,
       not_86_out, not_87_out, not_88_out, not_89_out, not_90_out, not_91_out, not_92_out, not_93_out,
       not_94_out, not_95_out, not_96_out, not_97_out, not_98_out, not_99_out, not_100_out, not_101_out,
       not_102_out, not_103_out, not_104_out, not_105_out, not_106_out, not_107_out, not_108_out,
       not_109_out, not_110_out, or_1_out, or_2_out, or_3_out, or_4_out, or_5_out, or_6_out, or_7_out,
       or_8_out, or_9_out, or_10_out, or_11_out, or_12_out, or_13_out, or_14_out, or_15_out, or_16_out,
       or_17_out, or_18_out, or_19_out, or_20_out, or_21_out, or_22_out, or_23_out, or_24_out, or_26_out,
       or_27_out, or_28_out, or_29_out, or_30_out, or_31_out, or_32_out, or_33_out, or_34_out, or_35_out,
       or_36_out, or_39_out, or_40_out, or_41_out, or_42_out, or_43_out, or_44_out, or_45_out, or_46_out,
       or_47_out, or_48_out, or_49_out, or_50_out, or_51_out, or_52_out, or_53_out, or_54_out, or_57_out,
       or_58_out, or_59_out, or_60_out, or_61_out, or_62_out, or_63_out, or_64_out, or_65_out, or_66_out,
       or_67_out, or_68_out, or_69_out, or_70_out, or_71_out, pc_count, PC_FLUSH, PC_FLUSH_COND, pc_load,
       pc_out_address_bus, pull_resistor_72_node, pull_resistor_73_node, pull_resistor_74_node,
       pull_resistor_75_node, PUT_A_ADDR, PUT_ALUOUT_DB, PUT_B_ADDR, PUT_DB_FG, PUT_FG_DB, PUT_IADR_ADDR,
       PUT_IIMM_DB, PUT_IR0_DB, PUT_IR1_DB, PUT_SP_ADDR, s_r_ff_2_qn, s_r_ff_3_q, s_r_ff_4_q, s_r_ff_5_q,
       s_r_ff_6_q, s_r_ff_7_q, s_r_ff_8_q, s_r_ff_9_q, s_r_ff_10_q, SAVE_ADDR_A, SAVE_ADDR_B, SAVE_ADDR_SP,
       SAVE_DB_ALUA, SAVE_DB_ALUB, SAVE_DB_IR0, SAVE_DB_IR1, SAVE_IH, SAVE_PCB, SAVE_PCB_IF_EQ,
       SAVE_PCB_IF_OF, SAVE_PCB_IF_Z, SP_DOWN, SP_UP, subtractor_1_bout, transistor_72_out,
       transistor_121_out, transistor_122_out, transistor_123_out, transistor_124_out, transistor_125_out,
       transistor_126_out, transistor_127_out, transistor_128_out, transistor_129_out, transistor_130_out,
       transistor_131_out, transistor_132_out, transistor_133_out, transistor_134_out, transistor_135_out,
       transistor_145_out, transistor_146_out, transistor_147_out, transistor_148_out, transistor_149_out,
       transistor_150_out, transistor_151_out, transistor_152_out, transistor_153_out, transistor_154_out,
       transistor_155_out, transistor_156_out, transistor_157_out, transistor_158_out, transistor_159_out,
       transistor_161_out, transistor_162_out, transistor_163_out, transistor_164_out, transistor_165_out,
       transistor_166_out, transistor_167_out, transistor_168_out, transistor_169_out, transistor_170_out,
       transistor_171_out, transistor_172_out, transistor_173_out, transistor_174_out, transistor_175_out,
       transistor_201_out, transistor_202_out, transistor_203_out, transistor_204_out, transistor_205_out,
       transistor_206_out, transistor_207_out, transistor_208_out, transistor_209_out, transistor_210_out,
       transistor_211_out, transistor_212_out, transistor_213_out, transistor_214_out, transistor_215_out,
       transistor_261_out, transistor_262_out, transistor_263_out, transistor_264_out, transistor_265_out,
       transistor_266_out, transistor_267_out, transistor_268_out, transistor_293_out, transistor_294_out,
       transistor_295_out, transistor_296_out, transistor_297_out, transistor_298_out, transistor_299_out,
       transistor_300_out, xnor_1_out, xnor_2_out, xnor_3_out, xnor_4_out, xnor_5_out, xnor_6_out,
       xnor_7_out, xnor_8_out, xnor_9_out, xnor_10_out, xnor_11_out, xnor_12_out, xnor_13_out, xnor_14_out,
       xnor_15_out, xnor_16_out, xnor_17_out, xnor_18_out, xnor_19_out, xnor_20_out, xnor_21_out,
       xnor_22_out, xnor_23_out, xnor_24_out, xnor_25_out, xnor_26_out, xnor_27_out, xnor_28_out,
       xnor_29_out, xnor_30_out, xnor_31_out, xnor_32_out, xnor_33_out, xnor_34_out, xnor_35_out,
       xnor_36_out, xnor_37_out, xnor_38_out, xnor_39_out, xnor_40_out, xnor_41_out, xnor_42_out,
       xnor_43_out, xnor_44_out, xnor_45_out, xnor_46_out, xnor_47_out, xnor_48_out, xnor_49_out,
       xnor_50_out, xnor_51_out, xnor_52_out, xnor_53_out, xnor_54_out, xnor_55_out, xnor_56_out,
       xnor_57_out, xnor_58_out, xnor_59_out, xnor_60_out, xnor_61_out, xnor_62_out, xnor_63_out,
       xnor_64_out, xor_1_out, xor_2_out, xor_3_out, xor_4_out, xor_5_out, xor_6_out, xor_7_out, xor_8_out,
       xor_9_out, xor_10_out, xor_11_out, xor_12_out, xor_13_out, xor_14_out;
  wire [2:0] counter_1_q;
  wire [3:0] fg, instruction_reg0, instruction_reg1;
  wire [7:0] adder_1_out, alua_q, alub_q, aluout_q, i0_q, i2_q, or_37_out, or_38_out, or_55_out, or_56_out,
       pull_resistor_93_node, pull_resistor_101_node, pull_resistor_111_node, pull_resistor_119_node, r0_q,
       r1_q, r2_q, r3_q, r4_q, r5_q, r6_q, r7_q, r8_q, r9_q, r10_q, r11_q, r12_q, r13_q, r14_q, r15_q,
       register_3_q, register_4_q, register_5_q, register_6_q, s_r_ff_11_q, subtractor_1_out, tcnt_q, tpsc_q,
       transistor_193_out;
  wire [15:0] controlled_buffer_1_out, ih, pc_q, register_1_q, register_2_q, sp_q;
  wire [31:0] MC1_data, MC2_data;

  Pull_Resistor pull_resistor_1 (.node(address_bus[0]));
  Pull_Resistor pull_resistor_2 (.node(address_bus[1]));
  Pull_Resistor pull_resistor_3 (.node(address_bus[2]));
  Pull_Resistor pull_resistor_4 (.node(address_bus[3]));
  Pull_Resistor pull_resistor_5 (.node(address_bus[4]));
  Pull_Resistor pull_resistor_6 (.node(address_bus[5]));
  Pull_Resistor pull_resistor_7 (.node(address_bus[6]));
  Pull_Resistor pull_resistor_8 (.node(address_bus[7]));
  Pull_Resistor pull_resistor_9 (.node(address_bus[8]));
  Pull_Resistor pull_resistor_10 (.node(address_bus[9]));
  Pull_Resistor pull_resistor_11 (.node(address_bus[10]));
  Pull_Resistor pull_resistor_12 (.node(address_bus[11]));
  Pull_Resistor pull_resistor_13 (.node(address_bus[12]));
  Pull_Resistor pull_resistor_14 (.node(address_bus[13]));
  Pull_Resistor pull_resistor_15 (.node(address_bus[14]));
  Pull_Resistor pull_resistor_16 (.node(address_bus[15]));
  Pull_Resistor pull_resistor_17 (.node(data_bus_out[0]));
  Pull_Resistor pull_resistor_18 (.node(data_bus_out[1]));
  Pull_Resistor pull_resistor_19 (.node(data_bus_out[2]));
  Pull_Resistor pull_resistor_20 (.node(data_bus_out[3]));
  Pull_Resistor pull_resistor_21 (.node(data_bus_out[4]));
  Pull_Resistor pull_resistor_22 (.node(data_bus_out[5]));
  Pull_Resistor pull_resistor_23 (.node(data_bus_out[6]));
  Pull_Resistor pull_resistor_24 (.node(data_bus_out[7]));
  Register #(.trigger("falling"), .width(16)) register_1 (
    .D(address_bus), .en(SAVE_PCB), .clk(clk_out), .Q(register_1_q), .clr(reset));
  not not_1 (not_1_out, INT_DISABLE);
  not not_2 (not_2_out, fg[3]);
  or or_1 (or_1_out, d_ff_5_q, reset);
  not not_3 (not_3_out, d_ff_4_q);
  or or_2 (or_2_out, PC_FLUSH, pc_count, INT_LOCK);
  assign controlled_buffer_1_out = not_4_out ? register_1_q : 16'bz;  // Controlled_Buffer controlled_buffer_1
  not not_4 (not_4_out, and_1_out);
  and and_1 (and_1_out, INT_TRIGGER, not_1_out);
  and and_2 (clk_out, clk, not_2_out);
  and and_3 (and_3_out, clk_out, or_3_out);
  not not_5 (not_5_out, d_ff_4_q);
  or or_3 (or_3_out, not_5_out, or_6_out);
  Counter #(.max('h7), .width(3)) counter_1 (
    .clr(xor_3_out), .up(1'b1), .clk(and_4_out), .carry(counter_1_carry), .Q(counter_1_q));  // open: load, count, D
  and and_4 (and_4_out, clk_out, d_ff_4_q);
  Counter #(.max('hffff), .width(16)) pc (
    .clr(reset), .load(or_4_out), .up(1'b1), .clk(or_2_out), .D(controlled_buffer_1_out), .carry(halt),
    .Q(pc_q));  // open: count
  or or_4 (or_4_out, PC_FLUSH, INT_LOCK);
  assign controlled_buffer_1_out = and_1_out ? ih : 16'bz;  // Controlled_Buffer controlled_buffer_2
  D_Flip_Flop d_ff_1 (.D(1'b1), .clk(and_3_out), .Q(d_ff_1_q), .reset(or_1_out));  // open: Qn, preset
  or or_5 (or_5_out, or_1_out, reset);
  or or_6 (or_6_out, transistor_72_out, counter_1_carry);
  D_Flip_Flop d_ff_2 (.D(d_ff_1_q), .clk(and_3_out), .Q(d_ff_2_q), .reset(or_1_out));  // open: Qn, preset
  xor xor_1 (xor_1_out, d_ff_1_q, d_ff_2_q);
  Register #(.trigger("falling")) i0 (.D(data_bus_out), .en(xor_1_out), .clk(clk_out), .Q(i0_q), .clr(or_5_out));
  D_Flip_Flop d_ff_3 (.D(d_ff_2_q), .clk(and_3_out), .Q(d_ff_3_q), .reset(or_1_out));  // open: Qn, preset
  xor xor_2 (xor_2_out, d_ff_2_q, d_ff_3_q);
  Register #(.trigger("falling")) i1 (
    .D(data_bus_out), .en(xor_2_out), .clk(clk_out), .Q({instruction_reg1, instruction_reg0}), .clr(or_5_out));
  not not_6 (not_6_out, PUT_IIMM_DB);
  not not_7 (not_7_out, pc_out_address_bus);
  D_Flip_Flop d_ff_4 (.D(d_ff_3_q), .clk(and_3_out), .Q(d_ff_4_q), .reset(or_1_out));  // open: Qn, preset
  xor xor_3 (xor_3_out, d_ff_3_q, d_ff_4_q);
  Register #(.trigger("falling")) i2 (.D(data_bus_out), .en(xor_3_out), .clk(clk_out), .Q(i2_q), .clr(or_5_out));
  Transistor transistor_1 (.in(i2_q[0]), .out(data_bus_out[0]), .gate(not_6_out));
  Transistor transistor_2 (.in(i2_q[1]), .out(data_bus_out[1]), .gate(not_6_out));
  Transistor transistor_3 (.in(i2_q[2]), .out(data_bus_out[2]), .gate(not_6_out));
  Transistor transistor_4 (.in(i2_q[3]), .out(data_bus_out[3]), .gate(not_6_out));
  Transistor transistor_5 (.in(i2_q[4]), .out(data_bus_out[4]), .gate(not_6_out));
  Transistor transistor_6 (.in(i2_q[5]), .out(data_bus_out[5]), .gate(not_6_out));
  Transistor transistor_7 (.in(i2_q[6]), .out(data_bus_out[6]), .gate(not_6_out));
  Transistor transistor_8 (.in(i2_q[7]), .out(data_bus_out[7]), .gate(not_6_out));
  and and_5 (INT_LOCK, INT_TRIGGER, and_7_out);
  D_Flip_Flop d_ff_5 (.D(d_ff_4_q), .clk(and_3_out), .Q(d_ff_5_q), .reset(or_1_out));  // open: Qn, preset
  ROM #(.addrWidth(11), .dataWidth(32)) MC1 (.addr({i0_q, counter_1_q}), .data(MC1_data));
  ROM #(.addrWidth(11), .dataWidth(32)) MC2 (.addr({i0_q, counter_1_q}), .data(MC2_data));
  Transistor transistor_9 (.in(pc_q[0]), .out(address_bus[0]), .gate(not_7_out));
  Transistor transistor_10 (.in(pc_q[1]), .out(address_bus[1]), .gate(not_7_out));
  Transistor transistor_11 (.in(pc_q[2]), .out(address_bus[2]), .gate(not_7_out));
  Transistor transistor_12 (.in(pc_q[3]), .out(address_bus[3]), .gate(not_7_out));
  Transistor transistor_13 (.in(pc_q[4]), .out(address_bus[4]), .gate(not_7_out));
  Transistor transistor_14 (.in(pc_q[5]), .out(address_bus[5]), .gate(not_7_out));
  Transistor transistor_15 (.in(pc_q[6]), .out(address_bus[6]), .gate(not_7_out));
  Transistor transistor_16 (.in(pc_q[7]), .out(address_bus[7]), .gate(not_7_out));
  Transistor transistor_17 (.in(pc_q[8]), .out(address_bus[8]), .gate(not_7_out));
  Transistor transistor_18 (.in(pc_q[9]), .out(address_bus[9]), .gate(not_7_out));
  Transistor transistor_19 (.in(pc_q[10]), .out(address_bus[10]), .gate(not_7_out));
  Transistor transistor_20 (.in(pc_q[11]), .out(address_bus[11]), .gate(not_7_out));
  Transistor transistor_21 (.in(pc_q[12]), .out(address_bus[12]), .gate(not_7_out));
  Transistor transistor_22 (.in(pc_q[13]), .out(address_bus[13]), .gate(not_7_out));
  Transistor transistor_23 (.in(pc_q[14]), .out(address_bus[14]), .gate(not_7_out));
  Transistor transistor_24 (.in(pc_q[15]), .out(address_bus[15]), .gate(not_7_out));
  Register #(.width(16)) register_2 (.D(pc_q), .en(1'b1), .clk(INT_LOCK), .Q(register_2_q), .clr(reset));
  Pull_Resistor pull_resistor_25 (.node(or_1_out));
  not not_8 (not_8_out, and_3_out);
  and and_6 (pc_count, not_8_out, or_7_out);
  or or_7 (or_7_out, xor_3_out, xor_2_out, xor_1_out);
  and and_7 (and_7_out, or_6_out, not_9_out);
  not not_9 (not_9_out, INT_DISABLE);
  buf buffer_1 (pc_out_address_bus, or_7_out);
  buf buffer_2 (mem_read, or_7_out);
  assign data_bus_out = data_bus_in;  // Buffer buffer_3, 8 bits wide
  not not_10 (not_10_out, INT_RET_TO_ADDR);
  Transistor transistor_25 (.in(register_2_q[0]), .out(address_bus[0]), .gate(not_10_out));
  Transistor transistor_26 (.in(register_2_q[1]), .out(address_bus[1]), .gate(not_10_out));
  Transistor transistor_27 (.in(register_2_q[2]), .out(address_bus[2]), .gate(not_10_out));
  Transistor transistor_28 (.in(register_2_q[3]), .out(address_bus[3]), .gate(not_10_out));
  Transistor transistor_29 (.in(register_2_q[4]), .out(address_bus[4]), .gate(not_10_out));
  Transistor transistor_30 (.in(register_2_q[5]), .out(address_bus[5]), .gate(not_10_out));
  Transistor transistor_31 (.in(register_2_q[6]), .out(address_bus[6]), .gate(not_10_out));
  Transistor transistor_32 (.in(register_2_q[7]), .out(address_bus[7]), .gate(not_10_out));
  Transistor transistor_33 (.in(register_2_q[8]), .out(address_bus[8]), .gate(not_10_out));
  Transistor transistor_34 (.in(register_2_q[9]), .out(address_bus[9]), .gate(not_10_out));
  Transistor transistor_35 (.in(register_2_q[10]), .out(address_bus[10]), .gate(not_10_out));
  Transistor transistor_36 (.in(register_2_q[11]), .out(address_bus[11]), .gate(not_10_out));
  Transistor transistor_37 (.in(register_2_q[12]), .out(address_bus[12]), .gate(not_10_out));
  Transistor transistor_38 (.in(register_2_q[13]), .out(address_bus[13]), .gate(not_10_out));
  Transistor transistor_39 (.in(register_2_q[14]), .out(address_bus[14]), .gate(not_10_out));
  Transistor transistor_40 (.in(register_2_q[15]), .out(address_bus[15]), .gate(not_10_out));
  S_R_Flip_Flop #(.trigger("high")) s_r_ff_1 (
    .S(SAVE_PCB), .R(or_6_out), .clk(1'b1), .Q(INT_DISABLE), .reset(reset));  // open: Qn, preset
  Transistor transistor_41 (.in(MC1_data[0]), .out(PUT_A_ADDR), .gate(not_3_out));
  Transistor transistor_42 (.in(MC1_data[1]), .out(PUT_IR0_DB), .gate(not_3_out));
  Transistor transistor_43 (.in(MC1_data[2]), .out(PUT_IR1_DB), .gate(not_3_out));
  Transistor transistor_44 (.in(MC1_data[3]), .out(SAVE_DB_IR0), .gate(not_3_out));
  Transistor transistor_45 (.in(MC1_data[4]), .out(SAVE_DB_IR1), .gate(not_3_out));
  Transistor transistor_46 (.in(MC1_data[5]), .out(PUT_IIMM_DB), .gate(not_3_out));
  Transistor transistor_47 (.in(MC1_data[6]), .out(SAVE_DB_ALUA), .gate(not_3_out));
  Transistor transistor_48 (.in(MC1_data[7]), .out(SAVE_DB_ALUB), .gate(not_3_out));
  Transistor transistor_49 (.in(MC1_data[8]), .out(ALU_ADD), .gate(not_3_out));
  Transistor transistor_50 (.in(MC1_data[9]), .out(ALU_CMP), .gate(not_3_out));
  Transistor transistor_51 (.in(MC1_data[10]), .out(PUT_ALUOUT_DB), .gate(not_3_out));
  Transistor transistor_52 (.in(MC1_data[11]), .out(COND_INVERT), .gate(not_3_out));
  Transistor transistor_53 (.in(MC1_data[12]), .out(SAVE_PCB_IF_Z), .gate(not_3_out));
  Transistor transistor_54 (.in(MC1_data[13]), .out(SAVE_PCB_IF_EQ), .gate(not_3_out));
  Transistor transistor_55 (.in(MC1_data[14]), .out(SAVE_PCB), .gate(not_3_out));
  Transistor transistor_56 (.in(MC1_data[15]), .out(mem_write), .gate(not_3_out));
  Transistor transistor_57 (.in(MC1_data[16]), .out(mem_read), .gate(not_3_out));
  Transistor transistor_58 (.in(MC1_data[17]), .out(PC_FLUSH), .gate(not_3_out));
  Transistor transistor_59 (.in(MC1_data[18]), .out(PC_FLUSH_COND), .gate(not_3_out));
  Transistor transistor_60 (.in(MC1_data[19]), .out(ALU_SUB), .gate(not_3_out));
  Transistor transistor_61 (.in(MC1_data[20]), .out(ALU_NAND), .gate(not_3_out));
  Transistor transistor_62 (.in(MC1_data[21]), .out(ALU_NOR), .gate(not_3_out));
  Transistor transistor_63 (.in(MC1_data[22]), .out(io_in), .gate(not_3_out));
  Transistor transistor_64 (.in(MC1_data[23]), .out(io_out), .gate(not_3_out));
  Transistor transistor_65 (.in(MC1_data[24]), .out(PUT_B_ADDR), .gate(not_3_out));
  Transistor transistor_66 (.in(MC1_data[25]), .out(PUT_IADR_ADDR), .gate(not_3_out));
  Transistor transistor_67 (.in(MC1_data[26]), .out(SAVE_ADDR_A), .gate(not_3_out));
  Transistor transistor_68 (.in(MC1_data[27]), .out(SAVE_ADDR_B), .gate(not_3_out));
  Transistor transistor_69 (.in(MC1_data[28]), .out(INT_RET_TO_ADDR), .gate(not_3_out));
  Transistor transistor_70 (.in(MC1_data[29]), .out(INT7), .gate(not_3_out));
  Transistor transistor_71 (.in(MC1_data[30]), .gate(not_3_out));  // open: out
  Transistor transistor_72 (.in(MC1_data[31]), .out(transistor_72_out), .gate(not_3_out));
  Transistor transistor_73 (.in(MC2_data[0]), .out(SAVE_PCB_IF_OF), .gate(not_3_out));
  Transistor transistor_74 (.in(MC2_data[1]), .out(CLEAR_FG), .gate(not_3_out));
  Transistor transistor_75 (.in(MC2_data[2]), .out(ALU_ADO), .gate(not_3_out));
  Transistor transistor_76 (.in(MC2_data[3]), .out(ALU_SBO), .gate(not_3_out));
  Transistor transistor_77 (.in(MC2_data[4]), .out(SAVE_IH), .gate(not_3_out));
  Transistor transistor_78 (.in(MC2_data[5]), .out(PUT_FG_DB), .gate(not_3_out));
  Transistor transistor_79 (.in(MC2_data[6]), .out(PUT_DB_FG), .gate(not_3_out));
  Transistor transistor_80 (.in(MC2_data[7]), .out(SP_UP), .gate(not_3_out));
  Transistor transistor_81 (.in(MC2_data[8]), .out(SP_DOWN), .gate(not_3_out));
  Transistor transistor_82 (.in(MC2_data[9]), .out(SAVE_ADDR_SP), .gate(not_3_out));
  Transistor transistor_83 (.in(MC2_data[10]), .out(PUT_SP_ADDR), .gate(not_3_out));
  Transistor transistor_84 (.in(MC2_data[11]), .gate(not_3_out));  // open: out
  Transistor transistor_85 (.in(MC2_data[12]), .gate(not_3_out));  // open: out
  Transistor transistor_86 (.in(MC2_data[13]), .gate(not_3_out));  // open: out
  Transistor transistor_87 (.in(MC2_data[14]), .gate(not_3_out));  // open: out
  Transistor transistor_88 (.in(MC2_data[15]), .gate(not_3_out));  // open: out
  Transistor transistor_89 (.in(MC2_data[16]), .gate(not_3_out));  // open: out
  Transistor transistor_90 (.in(MC2_data[17]), .gate(not_3_out));  // open: out
  Transistor transistor_91 (.in(MC2_data[18]), .gate(not_3_out));  // open: out
  Transistor transistor_92 (.in(MC2_data[19]), .gate(not_3_out));  // open: out
  Transistor transistor_93 (.in(MC2_data[20]), .gate(not_3_out));  // open: out
  Transistor transistor_94 (.in(MC2_data[21]), .gate(not_3_out));  // open: out
  Transistor transistor_95 (.in(MC2_data[22]), .gate(not_3_out));  // open: out
  Transistor transistor_96 (.in(MC2_data[23]), .gate(not_3_out));  // open: out
  Transistor transistor_97 (.in(MC2_data[24]), .gate(not_3_out));  // open: out
  Transistor transistor_98 (.in(MC2_data[25]), .gate(not_3_out));  // open: out
  Transistor transistor_99 (.in(MC2_data[26]), .gate(not_3_out));  // open: out
  Transistor transistor_100 (.in(MC2_data[27]), .gate(not_3_out));  // open: out
  Transistor transistor_101 (.in(MC2_data[28]), .gate(not_3_out));  // open: out
  Transistor transistor_102 (.in(MC2_data[29]), .gate(not_3_out));  // open: out
  Transistor transistor_103 (.in(MC2_data[30]), .gate(not_3_out));  // open: out
  Transistor transistor_104 (.in(MC2_data[31]), .gate(not_3_out));  // open: out
  Pull_Resistor pull_resistor_26 (.node(INT_TRIGGER));
  Pull_Resistor pull_resistor_27 (.node(transistor_72_out));
  Register #(.trigger("falling"), .width(16)) u_ih (.D(address_bus), .en(SAVE_IH), .clk(clk_out), .Q(ih), .clr(reset));
  Pull_Resistor pull_resistor_28 (.node(mem_read));
  Pull_Resistor pull_resistor_29 (.node(mem_write));
  Pull_Resistor pull_resistor_30 (.node(PUT_A_ADDR));
  Pull_Resistor pull_resistor_31 (.node(PUT_IR0_DB));
  Pull_Resistor pull_resistor_32 (.node(PUT_IR1_DB));
  Pull_Resistor pull_resistor_33 (.node(SAVE_DB_IR0));
  Pull_Resistor pull_resistor_34 (.node(SAVE_DB_IR1));
  Pull_Resistor pull_resistor_35 (.node(PUT_IIMM_DB));
  Pull_Resistor pull_resistor_36 (.node(SAVE_DB_ALUA));
  Pull_Resistor pull_resistor_37 (.node(SAVE_DB_ALUB));
  Pull_Resistor pull_resistor_38 (.node(ALU_ADD));
  Pull_Resistor pull_resistor_39 (.node(ALU_CMP));
  Pull_Resistor pull_resistor_40 (.node(PUT_ALUOUT_DB));
  Pull_Resistor pull_resistor_41 (.node(COND_INVERT));
  Pull_Resistor pull_resistor_42 (.node(SAVE_PCB_IF_Z));
  Pull_Resistor pull_resistor_43 (.node(SAVE_PCB_IF_EQ));
  Pull_Resistor pull_resistor_44 (.node(SAVE_PCB));
  Pull_Resistor pull_resistor_45 (.node(mem_write));
  Pull_Resistor pull_resistor_46 (.node(mem_read));
  Pull_Resistor pull_resistor_47 (.node(PC_FLUSH));
  Pull_Resistor pull_resistor_48 (.node(PC_FLUSH_COND));
  Pull_Resistor pull_resistor_49 (.node(ALU_SUB));
  Pull_Resistor pull_resistor_50 (.node(ALU_NAND));
  Pull_Resistor pull_resistor_51 (.node(ALU_NOR));
  Pull_Resistor pull_resistor_52 (.node(io_in));
  Pull_Resistor pull_resistor_53 (.node(io_out));
  Pull_Resistor pull_resistor_54 (.node(PUT_B_ADDR));
  Pull_Resistor pull_resistor_55 (.node(PUT_IADR_ADDR));
  Pull_Resistor pull_resistor_56 (.node(SAVE_ADDR_A));
  Pull_Resistor pull_resistor_57 (.node(SAVE_ADDR_B));
  Pull_Resistor pull_resistor_58 (.node(INT_RET_TO_ADDR));
  Pull_Resistor pull_resistor_59 (.node(SAVE_PCB_IF_OF));
  Pull_Resistor pull_resistor_60 (.node(CLEAR_FG));
  Pull_Resistor pull_resistor_61 (.node(ALU_ADO));
  Pull_Resistor pull_resistor_62 (.node(ALU_SBO));
  Pull_Resistor pull_resistor_63 (.node(SAVE_IH));
  Pull_Resistor pull_resistor_64 (.node(PUT_FG_DB));
  Pull_Resistor pull_resistor_65 (.node(PUT_DB_FG));
  Pull_Resistor pull_resistor_66 (.node(SP_UP));
  Pull_Resistor pull_resistor_67 (.node(SP_DOWN));
  Pull_Resistor pull_resistor_68 (.node(SAVE_ADDR_SP));
  Pull_Resistor pull_resistor_69 (.node(PUT_SP_ADDR));
  Pull_Resistor pull_resistor_70 (.node(pc_load));
  Transistor transistor_105 (.in(instruction_reg0[0]), .out(address_bus[0]), .gate(not_11_out));
  Transistor transistor_106 (.in(instruction_reg0[1]), .out(address_bus[1]), .gate(not_11_out));
  Transistor transistor_107 (.in(instruction_reg0[2]), .out(address_bus[2]), .gate(not_11_out));
  Transistor transistor_108 (.in(instruction_reg0[3]), .out(address_bus[3]), .gate(not_11_out));
  Transistor transistor_109 (.in(instruction_reg1[0]), .out(address_bus[4]), .gate(not_11_out));
  Transistor transistor_110 (.in(instruction_reg1[1]), .out(address_bus[5]), .gate(not_11_out));
  Transistor transistor_111 (.in(instruction_reg1[2]), .out(address_bus[6]), .gate(not_11_out));
  Transistor transistor_112 (.in(instruction_reg1[3]), .out(address_bus[7]), .gate(not_11_out));
  Transistor transistor_113 (.in(i2_q[0]), .out(address_bus[8]), .gate(not_11_out));
  Transistor transistor_114 (.in(i2_q[1]), .out(address_bus[9]), .gate(not_11_out));
  Transistor transistor_115 (.in(i2_q[2]), .out(address_bus[10]), .gate(not_11_out));
  Transistor transistor_116 (.in(i2_q[3]), .out(address_bus[11]), .gate(not_11_out));
  Transistor transistor_117 (.in(i2_q[4]), .out(address_bus[12]), .gate(not_11_out));
  Transistor transistor_118 (.in(i2_q[5]), .out(address_bus[13]), .gate(not_11_out));
  Transistor transistor_119 (.in(i2_q[6]), .out(address_bus[14]), .gate(not_11_out));
  Transistor transistor_120 (.in(i2_q[7]), .out(address_bus[15]), .gate(not_11_out));
  not not_11 (not_11_out, PUT_IADR_ADDR);
  Pull_Resistor pull_resistor_71 (.node(pc_out_address_bus));
  xnor xnor_1 (xnor_1_out, address_bus[0], 1'b0);
  xnor xnor_2 (xnor_2_out, address_bus[1], 1'b1);
  xnor xnor_3 (xnor_3_out, address_bus[2], 1'b1);
  xnor xnor_4 (xnor_4_out, address_bus[3], 1'b1);
  xnor xnor_5 (xnor_5_out, address_bus[4], 1'b1);
  xnor xnor_6 (xnor_6_out, address_bus[5], 1'b1);
  xnor xnor_7 (xnor_7_out, address_bus[6], 1'b1);
  xnor xnor_8 (xnor_8_out, address_bus[7], 1'b1);
  xnor xnor_9 (xnor_9_out, address_bus[8], 1'b0);
  xnor xnor_10 (xnor_10_out, address_bus[9], 1'b0);
  xnor xnor_11 (xnor_11_out, address_bus[10], 1'b0);
  xnor xnor_12 (xnor_12_out, address_bus[11], 1'b0);
  xnor xnor_13 (xnor_13_out, address_bus[12], 1'b0);
  xnor xnor_14 (xnor_14_out, address_bus[13], 1'b0);
  xnor xnor_15 (xnor_15_out, address_bus[14], 1'b0);
  xnor xnor_16 (xnor_16_out, address_bus[15], 1'b0);
  Transistor transistor_121 (.in(1'b1), .out(transistor_121_out), .gate(xnor_1_out));
  Transistor transistor_122 (.in(transistor_121_out), .out(transistor_122_out), .gate(xnor_2_out));
  Transistor transistor_123 (.in(transistor_122_out), .out(transistor_123_out), .gate(xnor_3_out));
  Transistor transistor_124 (.in(transistor_123_out), .out(transistor_124_out), .gate(xnor_4_out));
  Transistor transistor_125 (.in(transistor_124_out), .out(transistor_125_out), .gate(xnor_5_out));
  Transistor transistor_126 (.in(transistor_125_out), .out(transistor_126_out), .gate(xnor_6_out));
  Transistor transistor_127 (.in(transistor_126_out), .out(transistor_127_out), .gate(xnor_7_out));
  Transistor transistor_128 (.in(transistor_127_out), .out(transistor_128_out), .gate(xnor_8_out));
  Transistor transistor_129 (.in(transistor_128_out), .out(transistor_129_out), .gate(xnor_9_out));
  Transistor transistor_130 (.in(transistor_129_out), .out(transistor_130_out), .gate(xnor_10_out));
  Transistor transistor_131 (.in(transistor_130_out), .out(transistor_131_out), .gate(xnor_11_out));
  Transistor transistor_132 (.in(transistor_131_out), .out(transistor_132_out), .gate(xnor_12_out));
  Transistor transistor_133 (.in(transistor_132_out), .out(transistor_133_out), .gate(xnor_13_out));
  Transistor transistor_134 (.in(transistor_133_out), .out(transistor_134_out), .gate(xnor_14_out));
  Transistor transistor_135 (.in(transistor_134_out), .out(transistor_135_out), .gate(xnor_15_out));
  Pull_Resistor pull_resistor_72 (.node(pull_resistor_72_node));
  Transistor transistor_136 (.in(transistor_135_out), .out(pull_resistor_72_node), .gate(xnor_16_out));
  and and_8 (and_8_out, pull_resistor_72_node, io_out);
  and and_9 (and_9_out, pull_resistor_72_node, io_in);
  not not_12 (not_12_out, and_9_out);
  Transistor transistor_137 (.in(register_3_q[0]), .out(data_bus_out[0]), .gate(not_12_out));
  Transistor transistor_138 (.in(register_3_q[1]), .out(data_bus_out[1]), .gate(not_12_out));
  Transistor transistor_139 (.in(register_3_q[2]), .out(data_bus_out[2]), .gate(not_12_out));
  Transistor transistor_140 (.in(register_3_q[3]), .out(data_bus_out[3]), .gate(not_12_out));
  Transistor transistor_141 (.in(register_3_q[4]), .out(data_bus_out[4]), .gate(not_12_out));
  Transistor transistor_142 (.in(register_3_q[5]), .out(data_bus_out[5]), .gate(not_12_out));
  Transistor transistor_143 (.in(register_3_q[6]), .out(data_bus_out[6]), .gate(not_12_out));
  Transistor transistor_144 (.in(register_3_q[7]), .out(data_bus_out[7]), .gate(not_12_out));
  xor xor_4 (xor_4_out, COND_INVERT, fg[0]);
  and and_10 (and_10_out, xor_4_out, SAVE_PCB_IF_Z);
  xor xor_5 (xor_5_out, COND_INVERT, fg[1]);
  and and_11 (and_11_out, xor_5_out, SAVE_PCB_IF_EQ);
  xor xor_6 (xor_6_out, COND_INVERT, fg[2]);
  and and_12 (and_12_out, xor_6_out, SAVE_PCB_IF_OF);
  Register #(.trigger("falling")) register_3 (
    .D(data_bus_out), .en(and_8_out), .clk(clk_out), .Q(register_3_q), .clr(reset));
  buf buffer_4 (SAVE_PCB, and_10_out);
  buf buffer_5 (SAVE_PCB, and_11_out);
  buf buffer_6 (SAVE_PCB, and_12_out);
  or or_8 (or_8_out, SAVE_PCB_IF_Z, SAVE_PCB_IF_EQ, SAVE_PCB_IF_OF);
  or or_9 (or_9_out, and_10_out, and_11_out, and_12_out);
  D_Flip_Flop d_ff_6 (.clk(clk_out), .Q(d_ff_6_q), .preset(or_9_out), .reset(or_8_out));  // open: D, Qn
  Register #(.trigger("falling")) alua (.D(data_bus_out), .en(SAVE_DB_ALUA), .clk(clk_out), .Q(alua_q), .clr(reset));
  Register #(.trigger("falling")) alub (.D(data_bus_out), .en(SAVE_DB_ALUB), .clk(clk_out), .Q(alub_q), .clr(reset));
  xnor xnor_17 (xnor_17_out, address_bus[0], 1'b1);
  Transistor transistor_145 (.in(1'b1), .out(transistor_145_out), .gate(xnor_17_out));
  xnor xnor_18 (xnor_18_out, address_bus[1], 1'b0);
  Transistor transistor_146 (.in(transistor_145_out), .out(transistor_146_out), .gate(xnor_18_out));
  xnor xnor_19 (xnor_19_out, address_bus[2], 1'b1);
  Transistor transistor_147 (.in(transistor_146_out), .out(transistor_147_out), .gate(xnor_19_out));
  xnor xnor_20 (xnor_20_out, address_bus[3], 1'b1);
  Transistor transistor_148 (.in(transistor_147_out), .out(transistor_148_out), .gate(xnor_20_out));
  xnor xnor_21 (xnor_21_out, address_bus[4], 1'b1);
  Transistor transistor_149 (.in(transistor_148_out), .out(transistor_149_out), .gate(xnor_21_out));
  xnor xnor_22 (xnor_22_out, address_bus[5], 1'b1);
  Transistor transistor_150 (.in(transistor_149_out), .out(transistor_150_out), .gate(xnor_22_out));
  xnor xnor_23 (xnor_23_out, address_bus[6], 1'b1);
  Transistor transistor_151 (.in(transistor_150_out), .out(transistor_151_out), .gate(xnor_23_out));
  xnor xnor_24 (xnor_24_out, address_bus[7], 1'b1);
  Transistor transistor_152 (.in(transistor_151_out), .out(transistor_152_out), .gate(xnor_24_out));
  xnor xnor_25 (xnor_25_out, address_bus[8], 1'b0);
  Transistor transistor_153 (.in(transistor_152_out), .out(transistor_153_out), .gate(xnor_25_out));
  xnor xnor_26 (xnor_26_out, address_bus[9], 1'b0);
  Transistor transistor_154 (.in(transistor_153_out), .out(transistor_154_out), .gate(xnor_26_out));
  xnor xnor_27 (xnor_27_out, address_bus[10], 1'b0);
  Transistor transistor_155 (.in(transistor_154_out), .out(transistor_155_out), .gate(xnor_27_out));
  xnor xnor_28 (xnor_28_out, address_bus[11], 1'b0);
  Transistor transistor_156 (.in(transistor_155_out), .out(transistor_156_out), .gate(xnor_28_out));
  xnor xnor_29 (xnor_29_out, address_bus[12], 1'b0);
  Transistor transistor_157 (.in(transistor_156_out), .out(transistor_157_out), .gate(xnor_29_out));
  xnor xnor_30 (xnor_30_out, address_bus[13], 1'b0);
  Transistor transistor_158 (.in(transistor_157_out), .out(transistor_158_out), .gate(xnor_30_out));
  xnor xnor_31 (xnor_31_out, address_bus[14], 1'b0);
  Transistor transistor_159 (.in(transistor_158_out), .out(transistor_159_out), .gate(xnor_31_out));
  xnor xnor_32 (xnor_32_out, address_bus[15], 1'b0);
  Pull_Resistor pull_resistor_73 (.node(pull_resistor_73_node));
  Transistor transistor_160 (.in(transistor_159_out), .out(pull_resistor_73_node), .gate(xnor_32_out));
  xnor xnor_33 (xnor_33_out, address_bus[0], 1'b1);
  Transistor transistor_161 (.in(1'b1), .out(transistor_161_out), .gate(xnor_33_out));
  xnor xnor_34 (xnor_34_out, address_bus[1], 1'b1);
  Transistor transistor_162 (.in(transistor_161_out), .out(transistor_162_out), .gate(xnor_34_out));
  xnor xnor_35 (xnor_35_out, address_bus[2], 1'b1);
  Transistor transistor_163 (.in(transistor_162_out), .out(transistor_163_out), .gate(xnor_35_out));
  xnor xnor_36 (xnor_36_out, address_bus[3], 1'b1);
  Transistor transistor_164 (.in(transistor_163_out), .out(transistor_164_out), .gate(xnor_36_out));
  xnor xnor_37 (xnor_37_out, address_bus[4], 1'b1);
  Transistor transistor_165 (.in(transistor_164_out), .out(transistor_165_out), .gate(xnor_37_out));
  xnor xnor_38 (xnor_38_out, address_bus[5], 1'b1);
  Transistor transistor_166 (.in(transistor_165_out), .out(transistor_166_out), .gate(xnor_38_out));
  xnor xnor_39 (xnor_39_out, address_bus[6], 1'b1);
  Transistor transistor_167 (.in(transistor_166_out), .out(transistor_167_out), .gate(xnor_39_out));
  xnor xnor_40 (xnor_40_out, address_bus[7], 1'b1);
  Transistor transistor_168 (.in(transistor_167_out), .out(transistor_168_out), .gate(xnor_40_out));
  xnor xnor_41 (xnor_41_out, address_bus[8], 1'b0);
  Transistor transistor_169 (.in(transistor_168_out), .out(transistor_169_out), .gate(xnor_41_out));
  xnor xnor_42 (xnor_42_out, address_bus[9], 1'b0);
  Transistor transistor_170 (.in(transistor_169_out), .out(transistor_170_out), .gate(xnor_42_out));
  xnor xnor_43 (xnor_43_out, address_bus[10], 1'b0);
  Transistor transistor_171 (.in(transistor_170_out), .out(transistor_171_out), .gate(xnor_43_out));
  xnor xnor_44 (xnor_44_out, address_bus[11], 1'b0);
  Transistor transistor_172 (.in(transistor_171_out), .out(transistor_172_out), .gate(xnor_44_out));
  xnor xnor_45 (xnor_45_out, address_bus[12], 1'b0);
  Transistor transistor_173 (.in(transistor_172_out), .out(transistor_173_out), .gate(xnor_45_out));
  xnor xnor_46 (xnor_46_out, address_bus[13], 1'b0);
  Transistor transistor_174 (.in(transistor_173_out), .out(transistor_174_out), .gate(xnor_46_out));
  xnor xnor_47 (xnor_47_out, address_bus[14], 1'b0);
  Transistor transistor_175 (.in(transistor_174_out), .out(transistor_175_out), .gate(xnor_47_out));
  xnor xnor_48 (xnor_48_out, address_bus[15], 1'b0);
  Pull_Resistor pull_resistor_74 (.node(pull_resistor_74_node));
  Transistor transistor_176 (.in(transistor_175_out), .out(pull_resistor_74_node), .gate(xnor_48_out));
  and and_13 (and_13_out, pull_resistor_73_node, io_out);
  and and_14 (and_14_out, pull_resistor_73_node, io_in);
  not not_13 (not_13_out, and_14_out);
  Transistor transistor_177 (.in(register_4_q[0]), .out(data_bus_out[0]), .gate(not_13_out));
  Transistor transistor_178 (.in(register_4_q[1]), .out(data_bus_out[1]), .gate(not_13_out));
  Transistor transistor_179 (.in(register_4_q[2]), .out(data_bus_out[2]), .gate(not_13_out));
  Transistor transistor_180 (.in(register_4_q[3]), .out(data_bus_out[3]), .gate(not_13_out));
  Transistor transistor_181 (.in(register_4_q[4]), .out(data_bus_out[4]), .gate(not_13_out));
  Transistor transistor_182 (.in(register_4_q[5]), .out(data_bus_out[5]), .gate(not_13_out));
  Transistor transistor_183 (.in(register_4_q[6]), .out(data_bus_out[6]), .gate(not_13_out));
  Transistor transistor_184 (.in(register_4_q[7]), .out(data_bus_out[7]), .gate(not_13_out));
  and and_15 (and_15_out, pull_resistor_74_node, io_out);
  and and_16 (and_16_out, pull_resistor_74_node, io_in);
  not not_14 (not_14_out, and_16_out);
  Transistor transistor_185 (.in(s_r_ff_11_q[0]), .out(data_bus_out[0]), .gate(not_14_out));
  Transistor transistor_186 (.in(s_r_ff_11_q[1]), .out(data_bus_out[1]), .gate(not_14_out));
  Transistor transistor_187 (.in(s_r_ff_11_q[2]), .out(data_bus_out[2]), .gate(not_14_out));
  Transistor transistor_188 (.in(s_r_ff_11_q[3]), .out(data_bus_out[3]), .gate(not_14_out));
  Transistor transistor_189 (.in(s_r_ff_11_q[4]), .out(data_bus_out[4]), .gate(not_14_out));
  Transistor transistor_190 (.in(s_r_ff_11_q[5]), .out(data_bus_out[5]), .gate(not_14_out));
  Transistor transistor_191 (.in(s_r_ff_11_q[6]), .out(data_bus_out[6]), .gate(not_14_out));
  Transistor transistor_192 (.in(s_r_ff_11_q[7]), .out(data_bus_out[7]), .gate(not_14_out));
  and and_17 (and_17_out, d_ff_6_q, PC_FLUSH_COND);
  Transistor transistor_193 (.in(alua_q[0]), .out(transistor_193_out[0]), .gate(not_15_out));
  Transistor transistor_194 (.in(alua_q[1]), .out(transistor_193_out[1]), .gate(not_15_out));
  Transistor transistor_195 (.in(alua_q[2]), .out(transistor_193_out[2]), .gate(not_15_out));
  Transistor transistor_196 (.in(alua_q[3]), .out(transistor_193_out[3]), .gate(not_15_out));
  Transistor transistor_197 (.in(alua_q[4]), .out(transistor_193_out[4]), .gate(not_15_out));
  Transistor transistor_198 (.in(alua_q[5]), .out(transistor_193_out[5]), .gate(not_15_out));
  Transistor transistor_199 (.in(alua_q[6]), .out(transistor_193_out[6]), .gate(not_15_out));
  Transistor transistor_200 (.in(alua_q[7]), .out(transistor_193_out[7]), .gate(not_15_out));
  not not_15 (not_15_out, or_10_out);
  or or_10 (or_10_out, and_25_out, and_22_out);
  or or_11 (or_11_out, CLEAR_FG, reset);
  Register #(.trigger("falling")) register_4 (
    .D(data_bus_out), .en(and_13_out), .clk(clk_out), .Q(register_4_q), .clr(reset));
  not not_16 (not_16_out, clk_out);
  buf buffer_7 (PC_FLUSH, and_17_out);
  Register #(.trigger("falling")) register_5 (
    .D(data_bus_out), .en(and_15_out), .clk(clk_out), .Q(register_5_q), .clr(reset));
  D_Flip_Flop #(.trigger("falling")) d_ff_7 (
    .D(data_bus_out[3]), .clk(and_18_out), .Q(fg[3]), .preset(halt), .reset(or_11_out));  // open: Qn
  and and_18 (and_18_out, PUT_DB_FG, clk_out);
  xnor xnor_49 (xnor_49_out, address_bus[0], 1'b0);
  Transistor transistor_201 (.in(1'b1), .out(transistor_201_out), .gate(xnor_49_out));
  xnor xnor_50 (xnor_50_out, address_bus[1], 1'b0);
  Transistor transistor_202 (.in(transistor_201_out), .out(transistor_202_out), .gate(xnor_50_out));
  xnor xnor_51 (xnor_51_out, address_bus[2], 1'b1);
  Transistor transistor_203 (.in(transistor_202_out), .out(transistor_203_out), .gate(xnor_51_out));
  xnor xnor_52 (xnor_52_out, address_bus[3], 1'b1);
  Transistor transistor_204 (.in(transistor_203_out), .out(transistor_204_out), .gate(xnor_52_out));
  xnor xnor_53 (xnor_53_out, address_bus[4], 1'b1);
  Transistor transistor_205 (.in(transistor_204_out), .out(transistor_205_out), .gate(xnor_53_out));
  xnor xnor_54 (xnor_54_out, address_bus[5], 1'b1);
  Transistor transistor_206 (.in(transistor_205_out), .out(transistor_206_out), .gate(xnor_54_out));
  xnor xnor_55 (xnor_55_out, address_bus[6], 1'b1);
  Transistor transistor_207 (.in(transistor_206_out), .out(transistor_207_out), .gate(xnor_55_out));
  xnor xnor_56 (xnor_56_out, address_bus[7], 1'b1);
  Transistor transistor_208 (.in(transistor_207_out), .out(transistor_208_out), .gate(xnor_56_out));
  xnor xnor_57 (xnor_57_out, address_bus[8], 1'b0);
  Transistor transistor_209 (.in(transistor_208_out), .out(transistor_209_out), .gate(xnor_57_out));
  xnor xnor_58 (xnor_58_out, address_bus[9], 1'b0);
  Transistor transistor_210 (.in(transistor_209_out), .out(transistor_210_out), .gate(xnor_58_out));
  xnor xnor_59 (xnor_59_out, address_bus[10], 1'b0);
  Transistor transistor_211 (.in(transistor_210_out), .out(transistor_211_out), .gate(xnor_59_out));
  xnor xnor_60 (xnor_60_out, address_bus[11], 1'b0);
  Transistor transistor_212 (.in(transistor_211_out), .out(transistor_212_out), .gate(xnor_60_out));
  xnor xnor_61 (xnor_61_out, address_bus[12], 1'b0);
  Transistor transistor_213 (.in(transistor_212_out), .out(transistor_213_out), .gate(xnor_61_out));
  xnor xnor_62 (xnor_62_out, address_bus[13], 1'b0);
  Transistor transistor_214 (.in(transistor_213_out), .out(transistor_214_out), .gate(xnor_62_out));
  xnor xnor_63 (xnor_63_out, address_bus[14], 1'b0);
  Transistor transistor_215 (.in(transistor_214_out), .out(transistor_215_out), .gate(xnor_63_out));
  xnor xnor_64 (xnor_64_out, address_bus[15], 1'b0);
  Pull_Resistor pull_resistor_75 (.node(pull_resistor_75_node));
  Transistor transistor_216 (.in(transistor_215_out), .out(pull_resistor_75_node), .gate(xnor_64_out));
  and and_19 (and_19_out, register_6_q[0], not_16_out);
  Multiplexer multiplexer_1 (.in0(and_19_out), .in1(comparator_1_eq), .out(multiplexer_1_out), .sel(register_6_q[1]));
  nand nand_1 (nand_1_out, alub_q[0], alua_q[0]);
  nand nand_2 (nand_2_out, alub_q[1], alua_q[1]);
  nand nand_3 (nand_3_out, alub_q[2], alua_q[2]);
  nand nand_4 (nand_4_out, alub_q[3], alua_q[3]);
  nand nand_5 (nand_5_out, alub_q[4], alua_q[4]);
  nand nand_6 (nand_6_out, alub_q[5], alua_q[5]);
  nand nand_7 (nand_7_out, alub_q[6], alua_q[6]);
  nand nand_8 (nand_8_out, alub_q[7], alua_q[7]);
  not not_17 (not_17_out, ALU_NAND);
  Adder adder_1 (.a(alua_q), .b(alub_q), .out(adder_1_out), .cout(adder_1_cout));  // open: cin
  and and_20 (and_20_out, adder_1_cout, ALU_ADD);
  and and_21 (and_21_out, ALU_ADO, fg[2]);
  and and_22 (and_22_out, ALU_ADO, not_18_out);
  not not_18 (not_18_out, and_21_out);
  Subtractor subtractor_1 (.a(alua_q), .b(alub_q), .out(subtractor_1_out), .bout(subtractor_1_bout));  // open: bin
  and and_23 (and_23_out, subtractor_1_bout, ALU_SUB);
  and and_24 (and_24_out, ALU_SBO, fg[2]);
  and and_25 (and_25_out, ALU_SBO, not_19_out);
  not not_19 (not_19_out, and_24_out);
  and and_26 (and_26_out, pull_resistor_75_node, io_out);
  and and_27 (and_27_out, pull_resistor_75_node, io_in);
  not not_20 (not_20_out, and_27_out);
  Transistor transistor_217 (.in(register_6_q[0]), .out(data_bus_out[0]), .gate(not_20_out));
  Transistor transistor_218 (.in(register_6_q[1]), .out(data_bus_out[1]), .gate(not_20_out));
  Transistor transistor_219 (.in(register_6_q[2]), .out(data_bus_out[2]), .gate(not_20_out));
  Transistor transistor_220 (.in(register_6_q[3]), .out(data_bus_out[3]), .gate(not_20_out));
  Transistor transistor_221 (.in(register_6_q[4]), .out(data_bus_out[4]), .gate(not_20_out));
  Transistor transistor_222 (.in(register_6_q[5]), .out(data_bus_out[5]), .gate(not_20_out));
  Transistor transistor_223 (.in(register_6_q[6]), .out(data_bus_out[6]), .gate(not_20_out));
  Transistor transistor_224 (.in(register_6_q[7]), .out(data_bus_out[7]), .gate(not_20_out));
  Counter tpsc (.clr(or_12_out), .clk(and_19_out), .Q(tpsc_q));  // open: load, up, count, D, carry
  or or_12 (or_12_out, reset, comparator_1_eq);
  Counter tcnt (.clr(or_13_out), .clk(multiplexer_1_out), .Q(tcnt_q));  // open: load, up, count, D, carry
  or or_13 (or_13_out, reset, comparator_2_eq);
  D_Flip_Flop d_ff_8 (.D(d_ff_8_qn), .clk(and_28_out), .Qn(d_ff_8_qn), .reset(reset));  // open: Q, preset
  Transistor transistor_225 (.in(nand_1_out), .out(transistor_193_out[0]), .gate(not_17_out));
  Transistor transistor_226 (.in(nand_2_out), .out(transistor_193_out[1]), .gate(not_17_out));
  Transistor transistor_227 (.in(nand_3_out), .out(transistor_193_out[2]), .gate(not_17_out));
  Transistor transistor_228 (.in(nand_4_out), .out(transistor_193_out[3]), .gate(not_17_out));
  Transistor transistor_229 (.in(nand_5_out), .out(transistor_193_out[4]), .gate(not_17_out));
  Transistor transistor_230 (.in(nand_6_out), .out(transistor_193_out[5]), .gate(not_17_out));
  Transistor transistor_231 (.in(nand_7_out), .out(transistor_193_out[6]), .gate(not_17_out));
  Transistor transistor_232 (.in(nand_8_out), .out(transistor_193_out[7]), .gate(not_17_out));
  or or_14 (or_14_out, ALU_ADD, and_21_out);
  buf buffer_8 (buffer_8_out, and_20_out);
  Pull_Resistor pull_resistor_76 (.node(buffer_8_out));
  or or_15 (or_15_out, ALU_SUB, and_24_out);
  buf buffer_9 (buffer_8_out, and_23_out);
  D_Flip_Flop #(.trigger("falling")) d_ff_9 (
    .D(data_bus_out[2]), .clk(and_18_out), .Q(fg[2]), .preset(buffer_8_out), .reset(or_11_out));  // open: Qn
  and and_28 (and_28_out, comparator_2_eq, register_6_q[0]);
  S_R_Flip_Flop #(.trigger("high")) s_r_ff_2 (
    .S(INT_LOCK), .R(or_16_out), .clk(1'b1), .Qn(s_r_ff_2_qn));  // open: Q, reset, preset
  or or_16 (or_16_out, reset, INT_RET_TO_ADDR);
  not not_21 (not_21_out, instruction_reg0[0]);
  not not_22 (not_22_out, instruction_reg0[1]);
  not not_23 (not_23_out, instruction_reg0[2]);
  not not_24 (not_24_out, instruction_reg0[3]);
  not not_25 (not_25_out, instruction_reg1[0]);
  not not_26 (not_26_out, instruction_reg1[1]);
  not not_27 (not_27_out, instruction_reg1[2]);
  not not_28 (not_28_out, instruction_reg1[3]);
  not not_29 (not_29_out, instruction_reg0[1]);
  not not_30 (not_30_out, instruction_reg0[2]);
  not not_31 (not_31_out, instruction_reg0[3]);
  not not_32 (not_32_out, instruction_reg1[1]);
  not not_33 (not_33_out, instruction_reg1[2]);
  not not_34 (not_34_out, instruction_reg1[3]);
  Transistor transistor_233 (.in(adder_1_out[0]), .out(transistor_193_out[0]), .gate(not_35_out));
  Transistor transistor_234 (.in(adder_1_out[1]), .out(transistor_193_out[1]), .gate(not_35_out));
  Transistor transistor_235 (.in(adder_1_out[2]), .out(transistor_193_out[2]), .gate(not_35_out));
  Transistor transistor_236 (.in(adder_1_out[3]), .out(transistor_193_out[3]), .gate(not_35_out));
  Transistor transistor_237 (.in(adder_1_out[4]), .out(transistor_193_out[4]), .gate(not_35_out));
  Transistor transistor_238 (.in(adder_1_out[5]), .out(transistor_193_out[5]), .gate(not_35_out));
  Transistor transistor_239 (.in(adder_1_out[6]), .out(transistor_193_out[6]), .gate(not_35_out));
  Transistor transistor_240 (.in(adder_1_out[7]), .out(transistor_193_out[7]), .gate(not_35_out));
  not not_35 (not_35_out, or_14_out);
  Transistor transistor_241 (.in(subtractor_1_out[0]), .out(transistor_193_out[0]), .gate(not_36_out));
  Transistor transistor_242 (.in(subtractor_1_out[1]), .out(transistor_193_out[1]), .gate(not_36_out));
  Transistor transistor_243 (.in(subtractor_1_out[2]), .out(transistor_193_out[2]), .gate(not_36_out));
  Transistor transistor_244 (.in(subtractor_1_out[3]), .out(transistor_193_out[3]), .gate(not_36_out));
  Transistor transistor_245 (.in(subtractor_1_out[4]), .out(transistor_193_out[4]), .gate(not_36_out));
  Transistor transistor_246 (.in(subtractor_1_out[5]), .out(transistor_193_out[5]), .gate(not_36_out));
  Transistor transistor_247 (.in(subtractor_1_out[6]), .out(transistor_193_out[6]), .gate(not_36_out));
  Transistor transistor_248 (.in(subtractor_1_out[7]), .out(transistor_193_out[7]), .gate(not_36_out));
  not not_36 (not_36_out, or_15_out);
  and and_29 (and_29_out, transistor_268_out, ALU_CMP);
  D_Flip_Flop #(.trigger("falling")) d_ff_10 (
    .D(data_bus_out[1]), .clk(and_18_out), .Q(fg[1]), .preset(and_29_out), .reset(or_11_out));  // open: Qn
  Register #(.trigger("falling")) register_6 (
    .D(data_bus_out), .en(and_26_out), .clk(clk_out), .Q(register_6_q), .clr(reset));
  Pull_Resistor pull_resistor_77 (.node(int0));
  or or_17 (or_17_out, reset, INT_LOCK);
  Pull_Resistor pull_resistor_78 (.node(int1));
  or or_18 (or_18_out, reset, INT_LOCK);
  Pull_Resistor pull_resistor_79 (.node(int2));
  or or_19 (or_19_out, reset, INT_LOCK);
  Pull_Resistor pull_resistor_80 (.node(int3));
  or or_20 (or_20_out, reset, INT_LOCK);
  Pull_Resistor pull_resistor_81 (.node(int4));
  or or_21 (or_21_out, reset, INT_LOCK);
  Pull_Resistor pull_resistor_82 (.node(int5));
  or or_22 (or_22_out, reset, INT_LOCK);
  Pull_Resistor pull_resistor_83 (.node(INT6));
  or or_23 (or_23_out, reset, INT_LOCK);
  Pull_Resistor pull_resistor_84 (.node(INT7));
  or or_24 (or_24_out, reset, INT_LOCK);
  and and_30 (and_30_out, not_21_out, not_22_out);
  and and_31 (and_31_out, not_23_out, not_24_out);
  and and_32 (and_32_out, not_25_out, not_26_out);
  and and_33 (and_33_out, not_27_out, not_28_out);
  and and_34 (and_34_out, instruction_reg0[0], not_29_out);
  and and_35 (and_35_out, not_30_out, not_31_out);
  and and_36 (and_36_out, instruction_reg1[0], not_32_out);
  and and_37 (and_37_out, not_33_out, not_34_out);
  D_Flip_Flop #(.trigger("falling")) d_ff_11 (
    .D(data_bus_out[0]), .clk(and_18_out), .Q(fg[0]), .preset(and_52_out), .reset(or_11_out));  // open: Qn
  not not_37 (not_37_out, PUT_FG_DB);
  Comparator comparator_1 (.a(tpsc_q), .b(register_3_q), .eq(comparator_1_eq));  // open: gt, lt
  Comparator comparator_2 (.a(tcnt_q), .b(register_4_q), .eq(comparator_2_eq));  // open: gt, lt
  and and_38 (and_38_out, and_28_out, register_6_q[3]);
  or or_25 (timer_out, and_38_out, and_39_out);
  and and_39 (and_39_out, d_ff_8_qn, register_6_q[4]);
  S_R_Flip_Flop #(.trigger("high")) s_r_ff_3 (
    .S(and_40_out), .R(or_17_out), .clk(1'b1), .Q(s_r_ff_3_q));  // open: reset, Qn, preset
  and and_40 (and_40_out, register_5_q[0], s_r_ff_2_qn, int0);
  S_R_Flip_Flop #(.trigger("high")) s_r_ff_4 (
    .S(and_41_out), .R(or_18_out), .clk(1'b1), .Q(s_r_ff_4_q));  // open: reset, Qn, preset
  and and_41 (and_41_out, register_5_q[1], s_r_ff_2_qn, int1);
  S_R_Flip_Flop #(.trigger("high")) s_r_ff_5 (
    .S(and_42_out), .R(or_19_out), .clk(1'b1), .Q(s_r_ff_5_q));  // open: reset, Qn, preset
  and and_42 (and_42_out, register_5_q[2], s_r_ff_2_qn, int2);
  S_R_Flip_Flop #(.trigger("high")) s_r_ff_6 (
    .S(and_43_out), .R(or_20_out), .clk(1'b1), .Q(s_r_ff_6_q));  // open: reset, Qn, preset
  and and_43 (and_43_out, register_5_q[3], s_r_ff_2_qn, int3);
  S_R_Flip_Flop #(.trigger("high")) s_r_ff_7 (
    .S(and_44_out), .R(or_21_out), .clk(1'b1), .Q(s_r_ff_7_q));  // open: reset, Qn, preset
  and and_44 (and_44_out, register_5_q[4], s_r_ff_2_qn, int4);
  S_R_Flip_Flop #(.trigger("high")) s_r_ff_8 (
    .S(and_45_out), .R(or_22_out), .clk(1'b1), .Q(s_r_ff_8_q));  // open: reset, Qn, preset
  and and_45 (and_45_out, register_5_q[5], s_r_ff_2_qn, int5);
  S_R_Flip_Flop #(.trigger("high")) s_r_ff_9 (
    .S(and_46_out), .R(or_23_out), .clk(1'b1), .Q(s_r_ff_9_q));  // open: reset, Qn, preset
  and and_46 (and_46_out, register_5_q[6], s_r_ff_2_qn, INT6);
  S_R_Flip_Flop #(.trigger("high")) s_r_ff_10 (
    .S(and_47_out), .R(or_24_out), .clk(1'b1), .Q(s_r_ff_10_q));  // open: reset, Qn, preset
  and and_47 (and_47_out, register_5_q[7], s_r_ff_2_qn, INT7);
  and and_48 (and_48_out, and_30_out, and_31_out);
  and and_49 (and_49_out, and_32_out, and_33_out);
  and and_50 (and_50_out, and_34_out, and_35_out);
  and and_51 (and_51_out, and_36_out, and_37_out);
  Pull_Resistor pull_resistor_85 (.node(transistor_193_out[0]));
  Pull_Resistor pull_resistor_86 (.node(transistor_193_out[1]));
  Pull_Resistor pull_resistor_87 (.node(transistor_193_out[2]));
  Pull_Resistor pull_resistor_88 (.node(transistor_193_out[3]));
  Pull_Resistor pull_resistor_89 (.node(transistor_193_out[4]));
  Pull_Resistor pull_resistor_90 (.node(transistor_193_out[5]));
  Pull_Resistor pull_resistor_91 (.node(transistor_193_out[6]));
  Pull_Resistor pull_resistor_92 (.node(transistor_193_out[7]));
  or or_26 (or_26_out, ALU_ADD, ALU_ADO, ALU_SUB, ALU_SBO, ALU_NAND, ALU_NOR);
  and and_52 (and_52_out, ALU_CMP, transistor_300_out);
  Transistor transistor_249 (.in(fg[0]), .out(data_bus_out[0]), .gate(not_37_out));
  Transistor transistor_250 (.in(fg[1]), .out(data_bus_out[1]), .gate(not_37_out));
  Transistor transistor_251 (.in(fg[2]), .out(data_bus_out[2]), .gate(not_37_out));
  Transistor transistor_252 (.in(fg[3]), .out(data_bus_out[3]), .gate(not_37_out));
  and and_53 (INT6, and_28_out, register_6_q[2]);
  Transistor transistor_253 (.in(nor_1_out), .out(transistor_193_out[0]), .gate(not_38_out));
  nor nor_1 (nor_1_out, alub_q[0], alua_q[0]);
  Transistor transistor_254 (.in(nor_2_out), .out(transistor_193_out[1]), .gate(not_38_out));
  nor nor_2 (nor_2_out, alub_q[1], alua_q[1]);
  Transistor transistor_255 (.in(nor_3_out), .out(transistor_193_out[2]), .gate(not_38_out));
  nor nor_3 (nor_3_out, alub_q[2], alua_q[2]);
  Transistor transistor_256 (.in(nor_4_out), .out(transistor_193_out[3]), .gate(not_38_out));
  nor nor_4 (nor_4_out, alub_q[3], alua_q[3]);
  Transistor transistor_257 (.in(nor_5_out), .out(transistor_193_out[4]), .gate(not_38_out));
  nor nor_5 (nor_5_out, alub_q[4], alua_q[4]);
  Transistor transistor_258 (.in(nor_6_out), .out(transistor_193_out[5]), .gate(not_38_out));
  nor nor_6 (nor_6_out, alub_q[5], alua_q[5]);
  Transistor transistor_259 (.in(nor_7_out), .out(transistor_193_out[6]), .gate(not_38_out));
  nor nor_7 (nor_7_out, alub_q[6], alua_q[6]);
  Transistor transistor_260 (.in(nor_8_out), .out(transistor_193_out[7]), .gate(not_38_out));
  nor nor_8 (nor_8_out, alub_q[7], alua_q[7]);
  not not_38 (not_38_out, ALU_NOR);
  Register #(.trigger("falling")) aluout (
    .D(transistor_193_out), .en(or_26_out), .clk(clk_out), .Q(aluout_q), .clr(reset));
  // Probe on fg
  buf buffer_10 (INT_TRIGGER, s_r_ff_3_q);
  buf buffer_11 (INT_TRIGGER, s_r_ff_4_q);
  buf buffer_12 (INT_TRIGGER, s_r_ff_5_q);
  buf buffer_13 (INT_TRIGGER, s_r_ff_6_q);
  buf buffer_14 (INT_TRIGGER, s_r_ff_7_q);
  buf buffer_15 (INT_TRIGGER, s_r_ff_8_q);
  buf buffer_16 (INT_TRIGGER, s_r_ff_9_q);
  buf buffer_17 (INT_TRIGGER, s_r_ff_10_q);
  Pull_Resistor pull_resistor_93 (.node(pull_resistor_93_node[0]));
  Pull_Resistor pull_resistor_94 (.node(pull_resistor_93_node[1]));
  Pull_Resistor pull_resistor_95 (.node(pull_resistor_93_node[2]));
  Pull_Resistor pull_resistor_96 (.node(pull_resistor_93_node[3]));
  Pull_Resistor pull_resistor_97 (.node(pull_resistor_93_node[4]));
  Pull_Resistor pull_resistor_98 (.node(pull_resistor_93_node[5]));
  Pull_Resistor pull_resistor_99 (.node(pull_resistor_93_node[6]));
  Pull_Resistor pull_resistor_100 (.node(pull_resistor_93_node[7]));
  Pull_Resistor pull_resistor_101 (.node(pull_resistor_101_node[0]));
  Pull_Resistor pull_resistor_102 (.node(pull_resistor_101_node[1]));
  Pull_Resistor pull_resistor_103 (.node(pull_resistor_101_node[2]));
  Pull_Resistor pull_resistor_104 (.node(pull_resistor_101_node[3]));
  Pull_Resistor pull_resistor_105 (.node(pull_resistor_101_node[4]));
  Pull_Resistor pull_resistor_106 (.node(pull_resistor_101_node[5]));
  Pull_Resistor pull_resistor_107 (.node(pull_resistor_101_node[6]));
  Pull_Resistor pull_resistor_108 (.node(pull_resistor_101_node[7]));
  Transistor transistor_261 (.in(1'b1), .out(transistor_261_out), .gate(alua_q[0]));
  Transistor transistor_262 (.in(transistor_261_out), .out(transistor_262_out), .gate(alua_q[1]));
  Transistor transistor_263 (.in(transistor_262_out), .out(transistor_263_out), .gate(alua_q[2]));
  Transistor transistor_264 (.in(transistor_263_out), .out(transistor_264_out), .gate(alua_q[3]));
  Transistor transistor_265 (.in(transistor_264_out), .out(transistor_265_out), .gate(alua_q[4]));
  Transistor transistor_266 (.in(transistor_265_out), .out(transistor_266_out), .gate(alua_q[5]));
  Transistor transistor_267 (.in(transistor_266_out), .out(transistor_267_out), .gate(alua_q[6]));
  Transistor transistor_268 (.in(transistor_267_out), .out(transistor_268_out), .gate(alua_q[7]));
  Pull_Resistor pull_resistor_109 (.node(transistor_268_out));
  Transistor transistor_269 (.in(address_bus[0]), .out(pull_resistor_93_node[0]), .gate(not_39_out));
  Transistor transistor_270 (.in(address_bus[1]), .out(pull_resistor_93_node[1]), .gate(not_39_out));
  Transistor transistor_271 (.in(address_bus[2]), .out(pull_resistor_93_node[2]), .gate(not_39_out));
  Transistor transistor_272 (.in(address_bus[3]), .out(pull_resistor_93_node[3]), .gate(not_39_out));
  Transistor transistor_273 (.in(address_bus[4]), .out(pull_resistor_93_node[4]), .gate(not_39_out));
  Transistor transistor_274 (.in(address_bus[5]), .out(pull_resistor_93_node[5]), .gate(not_39_out));
  Transistor transistor_275 (.in(address_bus[6]), .out(pull_resistor_93_node[6]), .gate(not_39_out));
  Transistor transistor_276 (.in(address_bus[7]), .out(pull_resistor_93_node[7]), .gate(not_39_out));
  Transistor transistor_277 (.in(address_bus[8]), .out(pull_resistor_101_node[0]), .gate(not_39_out));
  Transistor transistor_278 (.in(address_bus[9]), .out(pull_resistor_101_node[1]), .gate(not_39_out));
  Transistor transistor_279 (.in(address_bus[10]), .out(pull_resistor_101_node[2]), .gate(not_39_out));
  Transistor transistor_280 (.in(address_bus[11]), .out(pull_resistor_101_node[3]), .gate(not_39_out));
  Transistor transistor_281 (.in(address_bus[12]), .out(pull_resistor_101_node[4]), .gate(not_39_out));
  Transistor transistor_282 (.in(address_bus[13]), .out(pull_resistor_101_node[5]), .gate(not_39_out));
  Transistor transistor_283 (.in(address_bus[14]), .out(pull_resistor_101_node[6]), .gate(not_39_out));
  Transistor transistor_284 (.in(address_bus[15]), .out(pull_resistor_101_node[7]), .gate(not_39_out));
  not not_39 (not_39_out, SAVE_ADDR_A);
  and and_54 (and_54_out, SAVE_DB_IR0, and_48_out);
  and and_55 (and_55_out, SAVE_DB_IR1, and_49_out);
  and and_56 (and_56_out, SAVE_DB_IR0, and_50_out);
  or or_27 (or_27_out, and_56_out, SAVE_ADDR_A, and_57_out);
  and and_57 (and_57_out, SAVE_DB_IR1, and_51_out);
  Transistor transistor_285 (.in(aluout_q[0]), .out(data_bus_out[0]), .gate(not_40_out));
  Transistor transistor_286 (.in(aluout_q[1]), .out(data_bus_out[1]), .gate(not_40_out));
  Transistor transistor_287 (.in(aluout_q[2]), .out(data_bus_out[2]), .gate(not_40_out));
  Transistor transistor_288 (.in(aluout_q[3]), .out(data_bus_out[3]), .gate(not_40_out));
  Transistor transistor_289 (.in(aluout_q[4]), .out(data_bus_out[4]), .gate(not_40_out));
  Transistor transistor_290 (.in(aluout_q[5]), .out(data_bus_out[5]), .gate(not_40_out));
  Transistor transistor_291 (.in(aluout_q[6]), .out(data_bus_out[6]), .gate(not_40_out));
  Transistor transistor_292 (.in(aluout_q[7]), .out(data_bus_out[7]), .gate(not_40_out));
  not not_40 (not_40_out, PUT_ALUOUT_DB);
  or or_28 (or_28_out, and_54_out, SAVE_ADDR_A, and_55_out);
  xor xor_7 (xor_7_out, alua_q[0], alub_q[0]);
  xor xor_8 (xor_8_out, alua_q[1], alub_q[1]);
  xor xor_9 (xor_9_out, alua_q[2], alub_q[2]);
  xor xor_10 (xor_10_out, alua_q[3], alub_q[3]);
  xor xor_11 (xor_11_out, alua_q[4], alub_q[4]);
  xor xor_12 (xor_12_out, alua_q[5], alub_q[5]);
  xor xor_13 (xor_13_out, alua_q[6], alub_q[6]);
  xor xor_14 (xor_14_out, alua_q[7], alub_q[7]);
  S_R_Flip_Flop #(.trigger("high")) s_r_ff_11 (
    .S(s_r_ff_3_q), .R(or_29_out), .clk(1'b1), .Q(s_r_ff_11_q[0]));  // open: reset, Qn, preset
  or or_29 (or_29_out, reset, INT_RET_TO_ADDR);
  S_R_Flip_Flop #(.trigger("high")) s_r_ff_12 (
    .S(s_r_ff_4_q), .R(or_30_out), .clk(1'b1), .Q(s_r_ff_11_q[1]));  // open: reset, Qn, preset
  or or_30 (or_30_out, reset, INT_RET_TO_ADDR);
  S_R_Flip_Flop #(.trigger("high")) s_r_ff_13 (
    .S(s_r_ff_5_q), .R(or_31_out), .clk(1'b1), .Q(s_r_ff_11_q[2]));  // open: reset, Qn, preset
  or or_31 (or_31_out, reset, INT_RET_TO_ADDR);
  S_R_Flip_Flop #(.trigger("high")) s_r_ff_14 (
    .S(s_r_ff_6_q), .R(or_32_out), .clk(1'b1), .Q(s_r_ff_11_q[3]));  // open: reset, Qn, preset
  or or_32 (or_32_out, reset, INT_RET_TO_ADDR);
  S_R_Flip_Flop #(.trigger("high")) s_r_ff_15 (
    .S(s_r_ff_7_q), .R(or_33_out), .clk(1'b1), .Q(s_r_ff_11_q[4]));  // open: reset, Qn, preset
  or or_33 (or_33_out, reset, INT_RET_TO_ADDR);
  S_R_Flip_Flop #(.trigger("high")) s_r_ff_16 (
    .S(s_r_ff_8_q), .R(or_34_out), .clk(1'b1), .Q(s_r_ff_11_q[5]));  // open: reset, Qn, preset
  or or_34 (or_34_out, reset, INT_RET_TO_ADDR);
  S_R_Flip_Flop #(.trigger("high")) s_r_ff_17 (
    .S(s_r_ff_9_q), .R(or_35_out), .clk(1'b1), .Q(s_r_ff_11_q[6]));  // open: reset, Qn, preset
  or or_35 (or_35_out, reset, INT_RET_TO_ADDR);
  S_R_Flip_Flop #(.trigger("high")) s_r_ff_18 (
    .S(s_r_ff_10_q), .R(or_36_out), .clk(1'b1), .Q(s_r_ff_11_q[7]));  // open: reset, Qn, preset
  or or_36 (or_36_out, reset, INT_RET_TO_ADDR);
  assign or_37_out = pull_resistor_93_node | data_bus_out;  // OR_Gate or_37, 8 bits wide
  assign or_38_out = pull_resistor_101_node | data_bus_out;  // OR_Gate or_38, 8 bits wide
  Register #(.trigger("falling")) r0 (.D(or_37_out), .en(or_28_out), .clk(clk_out), .Q(r0_q), .clr(reset));
  and and_58 (and_58_out, PUT_IR0_DB, and_48_out);
  and and_59 (and_59_out, PUT_IR1_DB, and_49_out);
  Register #(.trigger("falling")) r1 (.D(or_38_out), .en(or_27_out), .clk(clk_out), .Q(r1_q), .clr(reset));
  and and_60 (and_60_out, PUT_IR0_DB, and_50_out);
  and and_61 (and_61_out, PUT_IR1_DB, and_51_out);
  Transistor transistor_293 (.in(1'b1), .out(transistor_293_out), .gate(xor_7_out));
  Transistor transistor_294 (.in(transistor_293_out), .out(transistor_294_out), .gate(xor_8_out));
  Transistor transistor_295 (.in(transistor_294_out), .out(transistor_295_out), .gate(xor_9_out));
  Transistor transistor_296 (.in(transistor_295_out), .out(transistor_296_out), .gate(xor_10_out));
  Transistor transistor_297 (.in(transistor_296_out), .out(transistor_297_out), .gate(xor_11_out));
  Transistor transistor_298 (.in(transistor_297_out), .out(transistor_298_out), .gate(xor_12_out));
  Transistor transistor_299 (.in(transistor_298_out), .out(transistor_299_out), .gate(xor_13_out));
  Transistor transistor_300 (.in(transistor_299_out), .out(transistor_300_out), .gate(xor_14_out));
  Pull_Resistor pull_resistor_110 (.node(transistor_300_out));
  or or_39 (or_39_out, and_58_out, and_59_out);
  or or_40 (or_40_out, and_60_out, and_61_out);
  Transistor transistor_301 (.in(r0_q[0]), .out(data_bus_out[0]), .gate(not_41_out));
  Transistor transistor_302 (.in(r0_q[1]), .out(data_bus_out[1]), .gate(not_41_out));
  Transistor transistor_303 (.in(r0_q[2]), .out(data_bus_out[2]), .gate(not_41_out));
  Transistor transistor_304 (.in(r0_q[3]), .out(data_bus_out[3]), .gate(not_41_out));
  Transistor transistor_305 (.in(r0_q[4]), .out(data_bus_out[4]), .gate(not_41_out));
  Transistor transistor_306 (.in(r0_q[5]), .out(data_bus_out[5]), .gate(not_41_out));
  Transistor transistor_307 (.in(r0_q[6]), .out(data_bus_out[6]), .gate(not_41_out));
  Transistor transistor_308 (.in(r0_q[7]), .out(data_bus_out[7]), .gate(not_41_out));
  not not_41 (not_41_out, or_39_out);
  Transistor transistor_309 (.in(r1_q[0]), .out(data_bus_out[0]), .gate(not_42_out));
  Transistor transistor_310 (.in(r1_q[1]), .out(data_bus_out[1]), .gate(not_42_out));
  Transistor transistor_311 (.in(r1_q[2]), .out(data_bus_out[2]), .gate(not_42_out));
  Transistor transistor_312 (.in(r1_q[3]), .out(data_bus_out[3]), .gate(not_42_out));
  Transistor transistor_313 (.in(r1_q[4]), .out(data_bus_out[4]), .gate(not_42_out));
  Transistor transistor_314 (.in(r1_q[5]), .out(data_bus_out[5]), .gate(not_42_out));
  Transistor transistor_315 (.in(r1_q[6]), .out(data_bus_out[6]), .gate(not_42_out));
  Transistor transistor_316 (.in(r1_q[7]), .out(data_bus_out[7]), .gate(not_42_out));
  not not_42 (not_42_out, or_40_out);
  not not_43 (not_43_out, PUT_A_ADDR);
  Transistor transistor_317 (.in(r0_q[0]), .out(address_bus[0]), .gate(not_43_out));
  Transistor transistor_318 (.in(r0_q[1]), .out(address_bus[1]), .gate(not_43_out));
  Transistor transistor_319 (.in(r0_q[2]), .out(address_bus[2]), .gate(not_43_out));
  Transistor transistor_320 (.in(r0_q[3]), .out(address_bus[3]), .gate(not_43_out));
  Transistor transistor_321 (.in(r0_q[4]), .out(address_bus[4]), .gate(not_43_out));
  Transistor transistor_322 (.in(r0_q[5]), .out(address_bus[5]), .gate(not_43_out));
  Transistor transistor_323 (.in(r0_q[6]), .out(address_bus[6]), .gate(not_43_out));
  Transistor transistor_324 (.in(r0_q[7]), .out(address_bus[7]), .gate(not_43_out));
  Transistor transistor_325 (.in(r1_q[0]), .out(address_bus[8]), .gate(not_43_out));
  Transistor transistor_326 (.in(r1_q[1]), .out(address_bus[9]), .gate(not_43_out));
  Transistor transistor_327 (.in(r1_q[2]), .out(address_bus[10]), .gate(not_43_out));
  Transistor transistor_328 (.in(r1_q[3]), .out(address_bus[11]), .gate(not_43_out));
  Transistor transistor_329 (.in(r1_q[4]), .out(address_bus[12]), .gate(not_43_out));
  Transistor transistor_330 (.in(r1_q[5]), .out(address_bus[13]), .gate(not_43_out));
  Transistor transistor_331 (.in(r1_q[6]), .out(address_bus[14]), .gate(not_43_out));
  Transistor transistor_332 (.in(r1_q[7]), .out(address_bus[15]), .gate(not_43_out));
  not not_44 (not_44_out, instruction_reg0[0]);
  not not_45 (not_45_out, instruction_reg0[1]);
  not not_46 (not_46_out, instruction_reg0[3]);
  not not_47 (not_47_out, instruction_reg1[0]);
  not not_48 (not_48_out, instruction_reg1[1]);
  not not_49 (not_49_out, instruction_reg1[3]);
  not not_50 (not_50_out, instruction_reg0[1]);
  not not_51 (not_51_out, instruction_reg0[3]);
  not not_52 (not_52_out, instruction_reg1[1]);
  not not_53 (not_53_out, instruction_reg1[3]);
  not not_54 (not_54_out, instruction_reg0[0]);
  not not_55 (not_55_out, instruction_reg0[3]);
  not not_56 (not_56_out, instruction_reg1[0]);
  not not_57 (not_57_out, instruction_reg1[3]);
  not not_58 (not_58_out, instruction_reg0[3]);
  not not_59 (not_59_out, instruction_reg1[3]);
  not not_60 (not_60_out, instruction_reg0[0]);
  not not_61 (not_61_out, instruction_reg0[1]);
  not not_62 (not_62_out, instruction_reg0[2]);
  not not_63 (not_63_out, instruction_reg1[0]);
  not not_64 (not_64_out, instruction_reg1[1]);
  not not_65 (not_65_out, instruction_reg1[2]);
  not not_66 (not_66_out, instruction_reg0[1]);
  not not_67 (not_67_out, instruction_reg0[2]);
  not not_68 (not_68_out, instruction_reg1[1]);
  not not_69 (not_69_out, instruction_reg1[2]);
  not not_70 (not_70_out, instruction_reg0[0]);
  not not_71 (not_71_out, instruction_reg0[2]);
  not not_72 (not_72_out, instruction_reg1[0]);
  not not_73 (not_73_out, instruction_reg1[2]);
  not not_74 (not_74_out, instruction_reg0[2]);
  not not_75 (not_75_out, instruction_reg1[2]);
  not not_76 (not_76_out, instruction_reg0[0]);
  not not_77 (not_77_out, instruction_reg0[1]);
  not not_78 (not_78_out, instruction_reg1[0]);
  not not_79 (not_79_out, instruction_reg1[1]);
  not not_80 (not_80_out, instruction_reg0[1]);
  not not_81 (not_81_out, instruction_reg1[1]);
  not not_82 (not_82_out, instruction_reg0[0]);
  not not_83 (not_83_out, instruction_reg1[0]);
  not not_84 (not_84_out, instruction_reg0[0]);
  not not_85 (not_85_out, instruction_reg0[2]);
  not not_86 (not_86_out, instruction_reg0[3]);
  not not_87 (not_87_out, instruction_reg1[0]);
  not not_88 (not_88_out, instruction_reg1[2]);
  not not_89 (not_89_out, instruction_reg1[3]);
  and and_62 (and_62_out, instruction_reg0[0], instruction_reg0[1]);
  not not_90 (not_90_out, instruction_reg0[2]);
  and and_63 (and_63_out, not_90_out, not_91_out);
  not not_91 (not_91_out, instruction_reg0[3]);
  and and_64 (and_64_out, instruction_reg1[0], instruction_reg1[1]);
  not not_92 (not_92_out, instruction_reg1[2]);
  and and_65 (and_65_out, not_92_out, not_93_out);
  not not_93 (not_93_out, instruction_reg1[3]);
  and and_66 (and_66_out, not_44_out, not_45_out);
  and and_67 (and_67_out, instruction_reg0[2], not_46_out);
  and and_68 (and_68_out, not_47_out, not_48_out);
  and and_69 (and_69_out, instruction_reg1[2], not_49_out);
  and and_70 (and_70_out, instruction_reg0[0], not_50_out);
  and and_71 (and_71_out, instruction_reg0[2], not_51_out);
  and and_72 (and_72_out, instruction_reg1[0], not_52_out);
  and and_73 (and_73_out, instruction_reg1[2], not_53_out);
  and and_74 (and_74_out, not_54_out, instruction_reg0[1]);
  and and_75 (and_75_out, instruction_reg0[2], not_55_out);
  and and_76 (and_76_out, not_56_out, instruction_reg1[1]);
  and and_77 (and_77_out, instruction_reg1[2], not_57_out);
  and and_78 (and_78_out, instruction_reg0[0], instruction_reg0[1]);
  and and_79 (and_79_out, instruction_reg0[2], not_58_out);
  and and_80 (and_80_out, instruction_reg1[0], instruction_reg1[1]);
  and and_81 (and_81_out, instruction_reg1[2], not_59_out);
  and and_82 (and_82_out, not_60_out, not_61_out);
  and and_83 (and_83_out, not_62_out, instruction_reg0[3]);
  and and_84 (and_84_out, not_63_out, not_64_out);
  and and_85 (and_85_out, not_65_out, instruction_reg1[3]);
  and and_86 (and_86_out, instruction_reg0[0], not_66_out);
  and and_87 (and_87_out, not_67_out, instruction_reg0[3]);
  and and_88 (and_88_out, instruction_reg1[0], not_68_out);
  and and_89 (and_89_out, not_69_out, instruction_reg1[3]);
  and and_90 (and_90_out, not_70_out, instruction_reg0[1]);
  and and_91 (and_91_out, not_71_out, instruction_reg0[3]);
  and and_92 (and_92_out, not_72_out, instruction_reg1[1]);
  and and_93 (and_93_out, not_73_out, instruction_reg1[3]);
  and and_94 (and_94_out, instruction_reg0[0], instruction_reg0[1]);
  and and_95 (and_95_out, not_74_out, instruction_reg0[3]);
  and and_96 (and_96_out, instruction_reg1[0], instruction_reg1[1]);
  and and_97 (and_97_out, not_75_out, instruction_reg1[3]);
  and and_98 (and_98_out, not_76_out, not_77_out);
  and and_99 (and_99_out, instruction_reg0[2], instruction_reg0[3]);
  and and_100 (and_100_out, not_78_out, not_79_out);
  and and_101 (and_101_out, instruction_reg1[2], instruction_reg1[3]);
  and and_102 (and_102_out, instruction_reg0[0], not_80_out);
  and and_103 (and_103_out, instruction_reg0[2], instruction_reg0[3]);
  and and_104 (and_104_out, instruction_reg1[0], not_81_out);
  and and_105 (and_105_out, instruction_reg1[2], instruction_reg1[3]);
  and and_106 (and_106_out, not_82_out, instruction_reg0[1]);
  and and_107 (and_107_out, instruction_reg0[2], instruction_reg0[3]);
  and and_108 (and_108_out, not_83_out, instruction_reg1[1]);
  and and_109 (and_109_out, instruction_reg1[2], instruction_reg1[3]);
  and and_110 (and_110_out, instruction_reg0[0], instruction_reg0[1]);
  and and_111 (and_111_out, instruction_reg0[2], instruction_reg0[3]);
  and and_112 (and_112_out, instruction_reg1[0], instruction_reg1[1]);
  and and_113 (and_113_out, instruction_reg1[2], instruction_reg1[3]);
  and and_114 (and_114_out, not_84_out, instruction_reg0[1]);
  and and_115 (and_115_out, not_85_out, not_86_out);
  and and_116 (and_116_out, not_87_out, instruction_reg1[1]);
  and and_117 (and_117_out, not_88_out, not_89_out);
  and and_118 (and_118_out, and_62_out, and_63_out);
  and and_119 (and_119_out, and_64_out, and_65_out);
  and and_120 (and_120_out, and_66_out, and_67_out);
  and and_121 (and_121_out, and_68_out, and_69_out);
  and and_122 (and_122_out, and_70_out, and_71_out);
  and and_123 (and_123_out, and_72_out, and_73_out);
  and and_124 (and_124_out, and_74_out, and_75_out);
  and and_125 (and_125_out, and_76_out, and_77_out);
  and and_126 (and_126_out, and_78_out, and_79_out);
  and and_127 (and_127_out, and_80_out, and_81_out);
  and and_128 (and_128_out, and_82_out, and_83_out);
  and and_129 (and_129_out, and_84_out, and_85_out);
  and and_130 (and_130_out, and_86_out, and_87_out);
  and and_131 (and_131_out, and_88_out, and_89_out);
  and and_132 (and_132_out, and_90_out, and_91_out);
  and and_133 (and_133_out, and_92_out, and_93_out);
  and and_134 (and_134_out, and_94_out, and_95_out);
  and and_135 (and_135_out, and_96_out, and_97_out);
  and and_136 (and_136_out, and_98_out, and_99_out);
  and and_137 (and_137_out, and_100_out, and_101_out);
  and and_138 (and_138_out, and_102_out, and_103_out);
  and and_139 (and_139_out, and_104_out, and_105_out);
  and and_140 (and_140_out, and_106_out, and_107_out);
  and and_141 (and_141_out, and_108_out, and_109_out);
  and and_142 (and_142_out, and_110_out, and_111_out);
  and and_143 (and_143_out, and_112_out, and_113_out);
  and and_144 (and_144_out, and_114_out, and_115_out);
  and and_145 (and_145_out, and_116_out, and_117_out);
  Pull_Resistor pull_resistor_111 (.node(pull_resistor_111_node[0]));
  Pull_Resistor pull_resistor_112 (.node(pull_resistor_111_node[1]));
  Pull_Resistor pull_resistor_113 (.node(pull_resistor_111_node[2]));
  Pull_Resistor pull_resistor_114 (.node(pull_resistor_111_node[3]));
  Pull_Resistor pull_resistor_115 (.node(pull_resistor_111_node[4]));
  Pull_Resistor pull_resistor_116 (.node(pull_resistor_111_node[5]));
  Pull_Resistor pull_resistor_117 (.node(pull_resistor_111_node[6]));
  Pull_Resistor pull_resistor_118 (.node(pull_resistor_111_node[7]));
  Pull_Resistor pull_resistor_119 (.node(pull_resistor_119_node[0]));
  Pull_Resistor pull_resistor_120 (.node(pull_resistor_119_node[1]));
  Pull_Resistor pull_resistor_121 (.node(pull_resistor_119_node[2]));
  Pull_Resistor pull_resistor_122 (.node(pull_resistor_119_node[3]));
  Pull_Resistor pull_resistor_123 (.node(pull_resistor_119_node[4]));
  Pull_Resistor pull_resistor_124 (.node(pull_resistor_119_node[5]));
  Pull_Resistor pull_resistor_125 (.node(pull_resistor_119_node[6]));
  Pull_Resistor pull_resistor_126 (.node(pull_resistor_119_node[7]));
  not not_94 (not_94_out, SAVE_ADDR_B);
  and and_146 (and_146_out, SAVE_DB_IR0, and_118_out);
  and and_147 (and_147_out, SAVE_DB_IR1, and_119_out);
  and and_148 (and_148_out, SAVE_DB_IR0, and_120_out);
  and and_149 (and_149_out, SAVE_DB_IR1, and_121_out);
  and and_150 (and_150_out, SAVE_DB_IR0, and_122_out);
  and and_151 (and_151_out, SAVE_DB_IR1, and_123_out);
  and and_152 (and_152_out, SAVE_DB_IR0, and_124_out);
  and and_153 (and_153_out, SAVE_DB_IR1, and_125_out);
  and and_154 (and_154_out, SAVE_DB_IR0, and_126_out);
  and and_155 (and_155_out, SAVE_DB_IR1, and_127_out);
  and and_156 (and_156_out, SAVE_DB_IR0, and_128_out);
  and and_157 (and_157_out, SAVE_DB_IR1, and_129_out);
  and and_158 (and_158_out, SAVE_DB_IR0, and_130_out);
  and and_159 (and_159_out, SAVE_DB_IR1, and_131_out);
  and and_160 (and_160_out, SAVE_DB_IR0, and_132_out);
  and and_161 (and_161_out, SAVE_DB_IR1, and_133_out);
  and and_162 (and_162_out, SAVE_DB_IR0, and_134_out);
  and and_163 (and_163_out, SAVE_DB_IR1, and_135_out);
  and and_164 (and_164_out, SAVE_DB_IR0, and_136_out);
  and and_165 (and_165_out, SAVE_DB_IR1, and_137_out);
  and and_166 (and_166_out, SAVE_DB_IR0, and_138_out);
  and and_167 (and_167_out, SAVE_DB_IR1, and_139_out);
  and and_168 (and_168_out, SAVE_DB_IR0, and_140_out);
  and and_169 (and_169_out, SAVE_DB_IR1, and_141_out);
  and and_170 (and_170_out, SAVE_DB_IR0, and_142_out);
  and and_171 (and_171_out, SAVE_DB_IR1, and_143_out);
  Transistor transistor_333 (.in(address_bus[0]), .out(pull_resistor_111_node[0]), .gate(not_94_out));
  Transistor transistor_334 (.in(address_bus[1]), .out(pull_resistor_111_node[1]), .gate(not_94_out));
  Transistor transistor_335 (.in(address_bus[2]), .out(pull_resistor_111_node[2]), .gate(not_94_out));
  Transistor transistor_336 (.in(address_bus[3]), .out(pull_resistor_111_node[3]), .gate(not_94_out));
  Transistor transistor_337 (.in(address_bus[4]), .out(pull_resistor_111_node[4]), .gate(not_94_out));
  Transistor transistor_338 (.in(address_bus[5]), .out(pull_resistor_111_node[5]), .gate(not_94_out));
  Transistor transistor_339 (.in(address_bus[6]), .out(pull_resistor_111_node[6]), .gate(not_94_out));
  Transistor transistor_340 (.in(address_bus[7]), .out(pull_resistor_111_node[7]), .gate(not_94_out));
  Transistor transistor_341 (.in(address_bus[8]), .out(pull_resistor_119_node[0]), .gate(not_94_out));
  Transistor transistor_342 (.in(address_bus[9]), .out(pull_resistor_119_node[1]), .gate(not_94_out));
  Transistor transistor_343 (.in(address_bus[10]), .out(pull_resistor_119_node[2]), .gate(not_94_out));
  Transistor transistor_344 (.in(address_bus[11]), .out(pull_resistor_119_node[3]), .gate(not_94_out));
  Transistor transistor_345 (.in(address_bus[12]), .out(pull_resistor_119_node[4]), .gate(not_94_out));
  Transistor transistor_346 (.in(address_bus[13]), .out(pull_resistor_119_node[5]), .gate(not_94_out));
  Transistor transistor_347 (.in(address_bus[14]), .out(pull_resistor_119_node[6]), .gate(not_94_out));
  Transistor transistor_348 (.in(address_bus[15]), .out(pull_resistor_119_node[7]), .gate(not_94_out));
  and and_172 (and_172_out, SAVE_DB_IR0, and_144_out);
  or or_41 (or_41_out, and_172_out, SAVE_ADDR_B, and_173_out);
  and and_173 (and_173_out, SAVE_DB_IR1, and_145_out);
  or or_42 (or_42_out, and_146_out, SAVE_ADDR_B, and_147_out);
  or or_43 (or_43_out, and_148_out, and_149_out);
  or or_44 (or_44_out, and_150_out, and_151_out);
  or or_45 (or_45_out, and_152_out, and_153_out);
  or or_46 (or_46_out, and_154_out, and_155_out);
  or or_47 (or_47_out, and_156_out, and_157_out);
  or or_48 (or_48_out, and_158_out, and_159_out);
  or or_49 (or_49_out, and_160_out, and_161_out);
  or or_50 (or_50_out, and_162_out, and_163_out);
  or or_51 (or_51_out, and_164_out, and_165_out);
  or or_52 (or_52_out, and_166_out, and_167_out);
  or or_53 (or_53_out, and_168_out, and_169_out);
  or or_54 (or_54_out, and_170_out, and_171_out);
  Register #(.trigger("falling")) r3 (.D(or_56_out), .en(or_42_out), .clk(clk_out), .Q(r3_q), .clr(reset));
  Register #(.trigger("falling")) r4 (.D(data_bus_out), .en(or_43_out), .clk(clk_out), .Q(r4_q), .clr(reset));
  and and_174 (and_174_out, PUT_IR0_DB, and_120_out);
  and and_175 (and_175_out, PUT_IR1_DB, and_121_out);
  Register #(.trigger("falling")) r5 (.D(data_bus_out), .en(or_44_out), .clk(clk_out), .Q(r5_q), .clr(reset));
  and and_176 (and_176_out, PUT_IR0_DB, and_122_out);
  and and_177 (and_177_out, PUT_IR1_DB, and_123_out);
  Register #(.trigger("falling")) r6 (.D(data_bus_out), .en(or_45_out), .clk(clk_out), .Q(r6_q), .clr(reset));
  and and_178 (and_178_out, PUT_IR0_DB, and_124_out);
  and and_179 (and_179_out, PUT_IR1_DB, and_125_out);
  Register #(.trigger("falling")) r7 (.D(data_bus_out), .en(or_46_out), .clk(clk_out), .Q(r7_q), .clr(reset));
  and and_180 (and_180_out, PUT_IR0_DB, and_126_out);
  and and_181 (and_181_out, PUT_IR1_DB, and_127_out);
  Register #(.trigger("falling")) r8 (.D(data_bus_out), .en(or_47_out), .clk(clk_out), .Q(r8_q), .clr(reset));
  and and_182 (and_182_out, PUT_IR0_DB, and_128_out);
  and and_183 (and_183_out, PUT_IR1_DB, and_129_out);
  Register #(.trigger("falling")) r9 (.D(data_bus_out), .en(or_48_out), .clk(clk_out), .Q(r9_q), .clr(reset));
  Register #(.trigger("falling")) r10 (.D(data_bus_out), .en(or_49_out), .clk(clk_out), .Q(r10_q), .clr(reset));
  and and_184 (and_184_out, PUT_IR0_DB, and_132_out);
  and and_185 (and_185_out, PUT_IR1_DB, and_133_out);
  Register #(.trigger("falling")) r11 (.D(data_bus_out), .en(or_50_out), .clk(clk_out), .Q(r11_q), .clr(reset));
  Register #(.trigger("falling")) r12 (.D(data_bus_out), .en(or_51_out), .clk(clk_out), .Q(r12_q), .clr(reset));
  and and_186 (and_186_out, PUT_IR0_DB, and_136_out);
  and and_187 (and_187_out, PUT_IR1_DB, and_137_out);
  Register #(.trigger("falling")) r13 (.D(data_bus_out), .en(or_52_out), .clk(clk_out), .Q(r13_q), .clr(reset));
  and and_188 (and_188_out, PUT_IR0_DB, and_138_out);
  and and_189 (and_189_out, PUT_IR1_DB, and_139_out);
  Register #(.trigger("falling")) r14 (.D(data_bus_out), .en(or_53_out), .clk(clk_out), .Q(r14_q), .clr(reset));
  and and_190 (and_190_out, PUT_IR0_DB, and_140_out);
  and and_191 (and_191_out, PUT_IR1_DB, and_141_out);
  Register #(.trigger("falling")) r15 (.D(data_bus_out), .en(or_54_out), .clk(clk_out), .Q(r15_q), .clr(reset));
  and and_192 (and_192_out, PUT_IR0_DB, and_142_out);
  and and_193 (and_193_out, PUT_IR1_DB, and_143_out);
  assign or_55_out = pull_resistor_111_node | data_bus_out;  // OR_Gate or_55, 8 bits wide
  assign or_56_out = pull_resistor_119_node | data_bus_out;  // OR_Gate or_56, 8 bits wide
  Register #(.trigger("falling")) r2 (.D(or_55_out), .en(or_41_out), .clk(clk_out), .Q(r2_q), .clr(reset));
  and and_194 (and_194_out, PUT_IR0_DB, and_144_out);
  and and_195 (and_195_out, PUT_IR1_DB, and_145_out);
  and and_196 (and_196_out, PUT_IR0_DB, and_118_out);
  and and_197 (and_197_out, PUT_IR1_DB, and_119_out);
  and and_198 (and_198_out, PUT_IR0_DB, and_130_out);
  and and_199 (and_199_out, PUT_IR1_DB, and_131_out);
  and and_200 (and_200_out, PUT_IR0_DB, and_134_out);
  and and_201 (and_201_out, PUT_IR1_DB, and_135_out);
  or or_57 (or_57_out, and_194_out, and_195_out);
  or or_58 (or_58_out, and_196_out, and_197_out);
  not not_95 (not_95_out, or_58_out);
  or or_59 (or_59_out, and_174_out, and_175_out);
  not not_96 (not_96_out, or_59_out);
  or or_60 (or_60_out, and_176_out, and_177_out);
  not not_97 (not_97_out, or_60_out);
  or or_61 (or_61_out, and_178_out, and_179_out);
  not not_98 (not_98_out, or_61_out);
  or or_62 (or_62_out, and_180_out, and_181_out);
  not not_99 (not_99_out, or_62_out);
  or or_63 (or_63_out, and_182_out, and_183_out);
  not not_100 (not_100_out, or_63_out);
  or or_64 (or_64_out, and_198_out, and_199_out);
  not not_101 (not_101_out, or_64_out);
  or or_65 (or_65_out, and_184_out, and_185_out);
  not not_102 (not_102_out, or_65_out);
  or or_66 (or_66_out, and_200_out, and_201_out);
  not not_103 (not_103_out, or_66_out);
  or or_67 (or_67_out, and_186_out, and_187_out);
  not not_104 (not_104_out, or_67_out);
  or or_68 (or_68_out, and_188_out, and_189_out);
  not not_105 (not_105_out, or_68_out);
  or or_69 (or_69_out, and_190_out, and_191_out);
  not not_106 (not_106_out, or_69_out);
  or or_70 (or_70_out, and_192_out, and_193_out);
  not not_107 (not_107_out, or_70_out);
  Transistor transistor_349 (.in(r2_q[0]), .out(data_bus_out[0]), .gate(not_108_out));
  Transistor transistor_350 (.in(r2_q[1]), .out(data_bus_out[1]), .gate(not_108_out));
  Transistor transistor_351 (.in(r2_q[2]), .out(data_bus_out[2]), .gate(not_108_out));
  Transistor transistor_352 (.in(r2_q[3]), .out(data_bus_out[3]), .gate(not_108_out));
  Transistor transistor_353 (.in(r2_q[4]), .out(data_bus_out[4]), .gate(not_108_out));
  Transistor transistor_354 (.in(r2_q[5]), .out(data_bus_out[5]), .gate(not_108_out));
  Transistor transistor_355 (.in(r2_q[6]), .out(data_bus_out[6]), .gate(not_108_out));
  Transistor transistor_356 (.in(r2_q[7]), .out(data_bus_out[7]), .gate(not_108_out));
  not not_108 (not_108_out, or_57_out);
  Transistor transistor_357 (.in(r3_q[0]), .out(data_bus_out[0]), .gate(not_95_out));
  Transistor transistor_358 (.in(r3_q[1]), .out(data_bus_out[1]), .gate(not_95_out));
  Transistor transistor_359 (.in(r3_q[2]), .out(data_bus_out[2]), .gate(not_95_out));
  Transistor transistor_360 (.in(r3_q[3]), .out(data_bus_out[3]), .gate(not_95_out));
  Transistor transistor_361 (.in(r3_q[4]), .out(data_bus_out[4]), .gate(not_95_out));
  Transistor transistor_362 (.in(r3_q[5]), .out(data_bus_out[5]), .gate(not_95_out));
  Transistor transistor_363 (.in(r3_q[6]), .out(data_bus_out[6]), .gate(not_95_out));
  Transistor transistor_364 (.in(r3_q[7]), .out(data_bus_out[7]), .gate(not_95_out));
  Transistor transistor_365 (.in(r4_q[0]), .out(data_bus_out[0]), .gate(not_96_out));
  Transistor transistor_366 (.in(r4_q[1]), .out(data_bus_out[1]), .gate(not_96_out));
  Transistor transistor_367 (.in(r4_q[2]), .out(data_bus_out[2]), .gate(not_96_out));
  Transistor transistor_368 (.in(r4_q[3]), .out(data_bus_out[3]), .gate(not_96_out));
  Transistor transistor_369 (.in(r4_q[4]), .out(data_bus_out[4]), .gate(not_96_out));
  Transistor transistor_370 (.in(r4_q[5]), .out(data_bus_out[5]), .gate(not_96_out));
  Transistor transistor_371 (.in(r4_q[6]), .out(data_bus_out[6]), .gate(not_96_out));
  Transistor transistor_372 (.in(r4_q[7]), .out(data_bus_out[7]), .gate(not_96_out));
  Transistor transistor_373 (.in(r5_q[0]), .out(data_bus_out[0]), .gate(not_97_out));
  Transistor transistor_374 (.in(r5_q[1]), .out(data_bus_out[1]), .gate(not_97_out));
  Transistor transistor_375 (.in(r5_q[2]), .out(data_bus_out[2]), .gate(not_97_out));
  Transistor transistor_376 (.in(r5_q[3]), .out(data_bus_out[3]), .gate(not_97_out));
  Transistor transistor_377 (.in(r5_q[4]), .out(data_bus_out[4]), .gate(not_97_out));
  Transistor transistor_378 (.in(r5_q[5]), .out(data_bus_out[5]), .gate(not_97_out));
  Transistor transistor_379 (.in(r5_q[6]), .out(data_bus_out[6]), .gate(not_97_out));
  Transistor transistor_380 (.in(r5_q[7]), .out(data_bus_out[7]), .gate(not_97_out));
  Transistor transistor_381 (.in(r6_q[0]), .out(data_bus_out[0]), .gate(not_98_out));
  Transistor transistor_382 (.in(r6_q[1]), .out(data_bus_out[1]), .gate(not_98_out));
  Transistor transistor_383 (.in(r6_q[2]), .out(data_bus_out[2]), .gate(not_98_out));
  Transistor transistor_384 (.in(r6_q[3]), .out(data_bus_out[3]), .gate(not_98_out));
  Transistor transistor_385 (.in(r6_q[4]), .out(data_bus_out[4]), .gate(not_98_out));
  Transistor transistor_386 (.in(r6_q[5]), .out(data_bus_out[5]), .gate(not_98_out));
  Transistor transistor_387 (.in(r6_q[6]), .out(data_bus_out[6]), .gate(not_98_out));
  Transistor transistor_388 (.in(r6_q[7]), .out(data_bus_out[7]), .gate(not_98_out));
  Transistor transistor_389 (.in(r7_q[0]), .out(data_bus_out[0]), .gate(not_99_out));
  Transistor transistor_390 (.in(r7_q[1]), .out(data_bus_out[1]), .gate(not_99_out));
  Transistor transistor_391 (.in(r7_q[2]), .out(data_bus_out[2]), .gate(not_99_out));
  Transistor transistor_392 (.in(r7_q[3]), .out(data_bus_out[3]), .gate(not_99_out));
  Transistor transistor_393 (.in(r7_q[4]), .out(data_bus_out[4]), .gate(not_99_out));
  Transistor transistor_394 (.in(r7_q[5]), .out(data_bus_out[5]), .gate(not_99_out));
  Transistor transistor_395 (.in(r7_q[6]), .out(data_bus_out[6]), .gate(not_99_out));
  Transistor transistor_396 (.in(r7_q[7]), .out(data_bus_out[7]), .gate(not_99_out));
  Transistor transistor_397 (.in(r8_q[0]), .out(data_bus_out[0]), .gate(not_100_out));
  Transistor transistor_398 (.in(r8_q[1]), .out(data_bus_out[1]), .gate(not_100_out));
  Transistor transistor_399 (.in(r8_q[2]), .out(data_bus_out[2]), .gate(not_100_out));
  Transistor transistor_400 (.in(r8_q[3]), .out(data_bus_out[3]), .gate(not_100_out));
  Transistor transistor_401 (.in(r8_q[4]), .out(data_bus_out[4]), .gate(not_100_out));
  Transistor transistor_402 (.in(r8_q[5]), .out(data_bus_out[5]), .gate(not_100_out));
  Transistor transistor_403 (.in(r8_q[6]), .out(data_bus_out[6]), .gate(not_100_out));
  Transistor transistor_404 (.in(r8_q[7]), .out(data_bus_out[7]), .gate(not_100_out));
  Transistor transistor_405 (.in(r9_q[0]), .out(data_bus_out[0]), .gate(not_101_out));
  Transistor transistor_406 (.in(r9_q[1]), .out(data_bus_out[1]), .gate(not_101_out));
  Transistor transistor_407 (.in(r9_q[2]), .out(data_bus_out[2]), .gate(not_101_out));
  Transistor transistor_408 (.in(r9_q[3]), .out(data_bus_out[3]), .gate(not_101_out));
  Transistor transistor_409 (.in(r9_q[4]), .out(data_bus_out[4]), .gate(not_101_out));
  Transistor transistor_410 (.in(r9_q[5]), .out(data_bus_out[5]), .gate(not_101_out));
  Transistor transistor_411 (.in(r9_q[6]), .out(data_bus_out[6]), .gate(not_101_out));
  Transistor transistor_412 (.in(r9_q[7]), .out(data_bus_out[7]), .gate(not_101_out));
  Transistor transistor_413 (.in(r10_q[0]), .out(data_bus_out[0]), .gate(not_102_out));
  Transistor transistor_414 (.in(r10_q[1]), .out(data_bus_out[1]), .gate(not_102_out));
  Transistor transistor_415 (.in(r10_q[2]), .out(data_bus_out[2]), .gate(not_102_out));
  Transistor transistor_416 (.in(r10_q[3]), .out(data_bus_out[3]), .gate(not_102_out));
  Transistor transistor_417 (.in(r10_q[4]), .out(data_bus_out[4]), .gate(not_102_out));
  Transistor transistor_418 (.in(r10_q[5]), .out(data_bus_out[5]), .gate(not_102_out));
  Transistor transistor_419 (.in(r10_q[6]), .out(data_bus_out[6]), .gate(not_102_out));
  Transistor transistor_420 (.in(r10_q[7]), .out(data_bus_out[7]), .gate(not_102_out));
  Transistor transistor_421 (.in(r11_q[0]), .out(data_bus_out[0]), .gate(not_103_out));
  Transistor transistor_422 (.in(r11_q[1]), .out(data_bus_out[1]), .gate(not_103_out));
  Transistor transistor_423 (.in(r11_q[2]), .out(data_bus_out[2]), .gate(not_103_out));
  Transistor transistor_424 (.in(r11_q[3]), .out(data_bus_out[3]), .gate(not_103_out));
  Transistor transistor_425 (.in(r11_q[4]), .out(data_bus_out[4]), .gate(not_103_out));
  Transistor transistor_426 (.in(r11_q[5]), .out(data_bus_out[5]), .gate(not_103_out));
  Transistor transistor_427 (.in(r11_q[6]), .out(data_bus_out[6]), .gate(not_103_out));
  Transistor transistor_428 (.in(r11_q[7]), .out(data_bus_out[7]), .gate(not_103_out));
  Transistor transistor_429 (.in(r12_q[0]), .out(data_bus_out[0]), .gate(not_104_out));
  Transistor transistor_430 (.in(r12_q[1]), .out(data_bus_out[1]), .gate(not_104_out));
  Transistor transistor_431 (.in(r12_q[2]), .out(data_bus_out[2]), .gate(not_104_out));
  Transistor transistor_432 (.in(r12_q[3]), .out(data_bus_out[3]), .gate(not_104_out));
  Transistor transistor_433 (.in(r12_q[4]), .out(data_bus_out[4]), .gate(not_104_out));
  Transistor transistor_434 (.in(r12_q[5]), .out(data_bus_out[5]), .gate(not_104_out));
  Transistor transistor_435 (.in(r12_q[6]), .out(data_bus_out[6]), .gate(not_104_out));
  Transistor transistor_436 (.in(r12_q[7]), .out(data_bus_out[7]), .gate(not_104_out));
  Transistor transistor_437 (.in(r13_q[0]), .out(data_bus_out[0]), .gate(not_105_out));
  Transistor transistor_438 (.in(r13_q[1]), .out(data_bus_out[1]), .gate(not_105_out));
  Transistor transistor_439 (.in(r13_q[2]), .out(data_bus_out[2]), .gate(not_105_out));
  Transistor transistor_440 (.in(r13_q[3]), .out(data_bus_out[3]), .gate(not_105_out));
  Transistor transistor_441 (.in(r13_q[4]), .out(data_bus_out[4]), .gate(not_105_out));
  Transistor transistor_442 (.in(r13_q[5]), .out(data_bus_out[5]), .gate(not_105_out));
  Transistor transistor_443 (.in(r13_q[6]), .out(data_bus_out[6]), .gate(not_105_out));
  Transistor transistor_444 (.in(r13_q[7]), .out(data_bus_out[7]), .gate(not_105_out));
  Transistor transistor_445 (.in(r14_q[0]), .out(data_bus_out[0]), .gate(not_106_out));
  Transistor transistor_446 (.in(r14_q[1]), .out(data_bus_out[1]), .gate(not_106_out));
  Transistor transistor_447 (.in(r14_q[2]), .out(data_bus_out[2]), .gate(not_106_out));
  Transistor transistor_448 (.in(r14_q[3]), .out(data_bus_out[3]), .gate(not_106_out));
  Transistor transistor_449 (.in(r14_q[4]), .out(data_bus_out[4]), .gate(not_106_out));
  Transistor transistor_450 (.in(r14_q[5]), .out(data_bus_out[5]), .gate(not_106_out));
  Transistor transistor_451 (.in(r14_q[6]), .out(data_bus_out[6]), .gate(not_106_out));
  Transistor transistor_452 (.in(r14_q[7]), .out(data_bus_out[7]), .gate(not_106_out));
  Transistor transistor_453 (.in(r15_q[0]), .out(data_bus_out[0]), .gate(not_107_out));
  Transistor transistor_454 (.in(r15_q[1]), .out(data_bus_out[1]), .gate(not_107_out));
  Transistor transistor_455 (.in(r15_q[2]), .out(data_bus_out[2]), .gate(not_107_out));
  Transistor transistor_456 (.in(r15_q[3]), .out(data_bus_out[3]), .gate(not_107_out));
  Transistor transistor_457 (.in(r15_q[4]), .out(data_bus_out[4]), .gate(not_107_out));
  Transistor transistor_458 (.in(r15_q[5]), .out(data_bus_out[5]), .gate(not_107_out));
  Transistor transistor_459 (.in(r15_q[6]), .out(data_bus_out[6]), .gate(not_107_out));
  Transistor transistor_460 (.in(r15_q[7]), .out(data_bus_out[7]), .gate(not_107_out));
  not not_109 (not_109_out, PUT_B_ADDR);
  Transistor transistor_461 (.in(r2_q[0]), .out(address_bus[0]), .gate(not_109_out));
  Transistor transistor_462 (.in(r2_q[1]), .out(address_bus[1]), .gate(not_109_out));
  Transistor transistor_463 (.in(r2_q[2]), .out(address_bus[2]), .gate(not_109_out));
  Transistor transistor_464 (.in(r2_q[3]), .out(address_bus[3]), .gate(not_109_out));
  Transistor transistor_465 (.in(r2_q[4]), .out(address_bus[4]), .gate(not_109_out));
  Transistor transistor_466 (.in(r2_q[5]), .out(address_bus[5]), .gate(not_109_out));
  Transistor transistor_467 (.in(r2_q[6]), .out(address_bus[6]), .gate(not_109_out));
  Transistor transistor_468 (.in(r2_q[7]), .out(address_bus[7]), .gate(not_109_out));
  Transistor transistor_469 (.in(r3_q[0]), .out(address_bus[8]), .gate(not_109_out));
  Transistor transistor_470 (.in(r3_q[1]), .out(address_bus[9]), .gate(not_109_out));
  Transistor transistor_471 (.in(r3_q[2]), .out(address_bus[10]), .gate(not_109_out));
  Transistor transistor_472 (.in(r3_q[3]), .out(address_bus[11]), .gate(not_109_out));
  Transistor transistor_473 (.in(r3_q[4]), .out(address_bus[12]), .gate(not_109_out));
  Transistor transistor_474 (.in(r3_q[5]), .out(address_bus[13]), .gate(not_109_out));
  Transistor transistor_475 (.in(r3_q[6]), .out(address_bus[14]), .gate(not_109_out));
  Transistor transistor_476 (.in(r3_q[7]), .out(address_bus[15]), .gate(not_109_out));
  or or_71 (or_71_out, SP_UP, SP_DOWN, SAVE_ADDR_SP);
  Counter #(.max('hffff), .trigger("falling"), .width(16)) sp (
    .clr(reset), .load(SAVE_ADDR_SP), .up(SP_UP), .count(or_71_out), .clk(clk_out), .D(address_bus), .Q(sp_q));  // open: carry
  not not_110 (not_110_out, PUT_SP_ADDR);
  Transistor transistor_477 (.in(sp_q[0]), .out(address_bus[0]), .gate(not_110_out));
  Transistor transistor_478 (.in(sp_q[1]), .out(address_bus[1]), .gate(not_110_out));
  Transistor transistor_479 (.in(sp_q[2]), .out(address_bus[2]), .gate(not_110_out));
  Transistor transistor_480 (.in(sp_q[3]), .out(address_bus[3]), .gate(not_110_out));
  Transistor transistor_481 (.in(sp_q[4]), .out(address_bus[4]), .gate(not_110_out));
  Transistor transistor_482 (.in(sp_q[5]), .out(address_bus[5]), .gate(not_110_out));
  Transistor transistor_483 (.in(sp_q[6]), .out(address_bus[6]), .gate(not_110_out));
  Transistor transistor_484 (.in(sp_q[7]), .out(address_bus[7]), .gate(not_110_out));
  Transistor transistor_485 (.in(sp_q[8]), .out(address_bus[8]), .gate(not_110_out));
  Transistor transistor_486 (.in(sp_q[9]), .out(address_bus[9]), .gate(not_110_out));
  Transistor transistor_487 (.in(sp_q[10]), .out(address_bus[10]), .gate(not_110_out));
  Transistor transistor_488 (.in(sp_q[11]), .out(address_bus[11]), .gate(not_110_out));
  Transistor transistor_489 (.in(sp_q[12]), .out(address_bus[12]), .gate(not_110_out));
  Transistor transistor_490 (.in(sp_q[13]), .out(address_bus[13]), .gate(not_110_out));
  Transistor transistor_491 (.in(sp_q[14]), .out(address_bus[14]), .gate(not_110_out));
  Transistor transistor_492 (.in(sp_q[15]), .out(address_bus[15]), .gate(not_110_out));

  // Other names for the same wires on the sheet: clk_t = clk_out; data_bus[7:0] = data_bus_out; INT_RESET = INT_LOCK;
  //   memory_read = mem_read; PUT_MEM_DB = mem_read; memory_write = mem_write; SAVE_DB_MEM = mem_write

  // Notes on the sheet:
  //   contents of MC1 (hex, n*v repeats v):
  //   0 80000000 7*0 c 80000000 6*0 28 80000000 6*0 800003 80000000 6*0 400009 80000000 6*0 1801 40000
  //   80000000 5*0 42 84 100 408 80000000 0 0 0 42 a0 100 408 80000000 0 0 0 42 84 80000 408 80000000 0 0
  //   0 42 a0 80000 408 80000000 0 0 0 42 84 100000 408 80000000 0 0 0 42 a0 100000 408 80000000 0 0 0 42
  //   84 200000 408 80000000 0 0 0 42 a0 200000 408 80000000 0 0 0 42 84 200 80000000 4*0 42 a0 200
  //   80000000 4*0 1001 40000 80000000 5*0 10009 80000000 6*0 8003 80000000 6*0 4001 20000 0 80000000 4*0
  //   2001 40000 80000000 5*0 2801 40000 80000000 5*0 1001800 40000 80000000 5*0 1001000 40000 80000000
  //   5*0 1004000 20000 0 80000000 4*0 1002000 40000 80000000 5*0 1002800 40000 80000000 5*0 1010008
  //   80000000 6*0 1008002 80000000 6*0 2004000 20000 0 80000000 4*0 2002000 40000 80000000 5*0 2002800
  //   40000 80000000 13*0 2001800 40000 80000000 5*0 6000000 80000000 6*0 a000000 80000000 6*0 1800002
  //   80000000 6*0 1400008 80000000 6*0 10004000 20000 80000000 5*0 20000000 80000000 6*0 1 40000 80000000
  //   5*0 1000000 40000 80000000 5*0 2000000 40000 80000000 5*0 801 40000 6*0 1000800 40000 80000000 5*0
  //   2000800 80000000 80000000 5*0 42 84 0 408 80000000 0 0 0 42 a0 0 408 80000000 0 0 0 42 84 0 408
  //   80000000 0 0 0 42 a0 0 408 80000000 11*0 1 80000000 6*0 1000000 80000000 6*0 2000000 80000000 6*0 2
  //   80000000 6*0 8 80000000 6*0 1 80000000 6*0 1000000 80000000 6*0 2000000 80000000 6*0 4000000
  //   80000000 6*0 8000000 80000000 6*0 8020 0 80000000 5*0 8002 0 80000000 6*0 10008 80000000
  //   contents of MC2 (hex, n*v repeats v):
  //   114*0 2 206*0 1 7*0 1 7*0 1 7*0 1 7*0 1 7*0 1 9*0 4 7*0 4 7*0 8 7*0 8 5*0 2 7*0 10 7*0 10 7*0 10 7*0
  //   40 7*0 20 7*0 200 7*0 200 7*0 200 7*0 400 7*0 400 7*0 400 100 6*0 400 100 6*0 80 400
  //   buffer_1 drives only 1 and floats otherwise
  //   buffer_2 drives only 1 and floats otherwise
  //   buffer_3 drives only 1 and floats otherwise
  //   buffer_4 drives only 1 and floats otherwise
  //   buffer_5 drives only 1 and floats otherwise
  //   buffer_6 drives only 1 and floats otherwise
  //   buffer_7 drives only 1 and floats otherwise
  //   buffer_8 drives only 1 and floats otherwise
  //   buffer_9 drives only 1 and floats otherwise
  //   buffer_10 drives only 1 and floats otherwise
  //   buffer_11 drives only 1 and floats otherwise
  //   buffer_12 drives only 1 and floats otherwise
  //   buffer_13 drives only 1 and floats otherwise
  //   buffer_14 drives only 1 and floats otherwise
  //   buffer_15 drives only 1 and floats otherwise
  //   buffer_16 drives only 1 and floats otherwise
  //   buffer_17 drives only 1 and floats otherwise
endmodule
module io (
  input  [15:0] address_bus,
  input  [15:0] address_config,
  input  [7:0] data_bus_in,
  input  io_out,
  input  clk,
  input  reset,
  input  io_in,
  input  [7:0] data_bus_out,
  input  [7:0] port_in,
  output [7:0] port_out
);

  wire and_1_out, and_2_out, not_2_out, pull_resistor_1_node, transistor_1_out, transistor_2_out,
       transistor_3_out, transistor_4_out, transistor_5_out, transistor_6_out, transistor_7_out,
       transistor_8_out, transistor_9_out, transistor_10_out, transistor_11_out, transistor_12_out,
       transistor_13_out, transistor_14_out, transistor_15_out, xnor_1_out, xnor_2_out, xnor_3_out,
       xnor_4_out, xnor_5_out, xnor_6_out, xnor_7_out, xnor_8_out, xnor_9_out, xnor_10_out, xnor_11_out,
       xnor_12_out, xnor_13_out, xnor_14_out, xnor_15_out, xnor_16_out;
  wire [15:0] not_1_out;

  assign not_1_out = ~address_config;  // NOT_Gate not_1, 16 bits wide
  xnor xnor_1 (xnor_1_out, address_bus[0], not_1_out[0]);
  Transistor transistor_1 (.in(1'b1), .out(transistor_1_out), .gate(xnor_1_out));
  xnor xnor_2 (xnor_2_out, address_bus[1], not_1_out[1]);
  Transistor transistor_2 (.in(transistor_1_out), .out(transistor_2_out), .gate(xnor_2_out));
  xnor xnor_3 (xnor_3_out, address_bus[2], not_1_out[2]);
  Transistor transistor_3 (.in(transistor_2_out), .out(transistor_3_out), .gate(xnor_3_out));
  xnor xnor_4 (xnor_4_out, address_bus[3], not_1_out[3]);
  Transistor transistor_4 (.in(transistor_3_out), .out(transistor_4_out), .gate(xnor_4_out));
  xnor xnor_5 (xnor_5_out, address_bus[4], not_1_out[4]);
  Transistor transistor_5 (.in(transistor_4_out), .out(transistor_5_out), .gate(xnor_5_out));
  xnor xnor_6 (xnor_6_out, address_bus[5], not_1_out[5]);
  Transistor transistor_6 (.in(transistor_5_out), .out(transistor_6_out), .gate(xnor_6_out));
  xnor xnor_7 (xnor_7_out, address_bus[6], not_1_out[6]);
  Transistor transistor_7 (.in(transistor_6_out), .out(transistor_7_out), .gate(xnor_7_out));
  xnor xnor_8 (xnor_8_out, address_bus[7], not_1_out[7]);
  Transistor transistor_8 (.in(transistor_7_out), .out(transistor_8_out), .gate(xnor_8_out));
  xnor xnor_9 (xnor_9_out, address_bus[8], not_1_out[8]);
  Transistor transistor_9 (.in(transistor_8_out), .out(transistor_9_out), .gate(xnor_9_out));
  xnor xnor_10 (xnor_10_out, address_bus[9], not_1_out[9]);
  Transistor transistor_10 (.in(transistor_9_out), .out(transistor_10_out), .gate(xnor_10_out));
  xnor xnor_11 (xnor_11_out, address_bus[10], not_1_out[10]);
  Transistor transistor_11 (.in(transistor_10_out), .out(transistor_11_out), .gate(xnor_11_out));
  xnor xnor_12 (xnor_12_out, address_bus[11], not_1_out[11]);
  Transistor transistor_12 (.in(transistor_11_out), .out(transistor_12_out), .gate(xnor_12_out));
  xnor xnor_13 (xnor_13_out, address_bus[12], not_1_out[12]);
  Transistor transistor_13 (.in(transistor_12_out), .out(transistor_13_out), .gate(xnor_13_out));
  xnor xnor_14 (xnor_14_out, address_bus[13], not_1_out[13]);
  Transistor transistor_14 (.in(transistor_13_out), .out(transistor_14_out), .gate(xnor_14_out));
  xnor xnor_15 (xnor_15_out, address_bus[14], not_1_out[14]);
  Transistor transistor_15 (.in(transistor_14_out), .out(transistor_15_out), .gate(xnor_15_out));
  xnor xnor_16 (xnor_16_out, address_bus[15], not_1_out[15]);
  Pull_Resistor pull_resistor_1 (.node(pull_resistor_1_node));
  Transistor transistor_16 (.in(transistor_15_out), .out(pull_resistor_1_node), .gate(xnor_16_out));
  Pull_Resistor pull_resistor_2 (.node(port_in[0]));
  Pull_Resistor pull_resistor_3 (.node(port_in[1]));
  Pull_Resistor pull_resistor_4 (.node(port_in[2]));
  Pull_Resistor pull_resistor_5 (.node(port_in[3]));
  Pull_Resistor pull_resistor_6 (.node(port_in[4]));
  Pull_Resistor pull_resistor_7 (.node(port_in[5]));
  Pull_Resistor pull_resistor_8 (.node(port_in[6]));
  Pull_Resistor pull_resistor_9 (.node(port_in[7]));
  and and_1 (and_1_out, pull_resistor_1_node, io_out);
  and and_2 (and_2_out, pull_resistor_1_node, io_in);
  not not_2 (not_2_out, and_2_out);
  Transistor transistor_17 (.in(port_in[0]), .out(data_bus_out[0]), .gate(not_2_out));
  Transistor transistor_18 (.in(port_in[1]), .out(data_bus_out[1]), .gate(not_2_out));
  Transistor transistor_19 (.in(port_in[2]), .out(data_bus_out[2]), .gate(not_2_out));
  Transistor transistor_20 (.in(port_in[3]), .out(data_bus_out[3]), .gate(not_2_out));
  Transistor transistor_21 (.in(port_in[4]), .out(data_bus_out[4]), .gate(not_2_out));
  Transistor transistor_22 (.in(port_in[5]), .out(data_bus_out[5]), .gate(not_2_out));
  Transistor transistor_23 (.in(port_in[6]), .out(data_bus_out[6]), .gate(not_2_out));
  Transistor transistor_24 (.in(port_in[7]), .out(data_bus_out[7]), .gate(not_2_out));
  Register #(.trigger("falling")) register_1 (.D(data_bus_in), .en(and_1_out), .clk(clk), .Q(port_out), .clr(reset));
endmodule

module main (
);

  wire and_1_out, and_2_out, and_3_out, and_4_out, and_5_out, button_1_out, clock_1_out, core_1_clk_out,
       core_1_io_in, core_1_io_out, core_1_mem_read, core_1_mem_write, core_1_timer_out, not_1_out,
       not_2_out, not_3_out, not_4_out;
  wire [7:0] core_1_data_bus_out, dipswitch_1_sw8, io_1_port_out, or_1_out, pull_resistor_1_node, ram_1_dout,
       rom_1_data, transistor_1_out;
  wire [15:0] core_1_address_bus;

  Button button_1 (.out(button_1_out));
  not not_1 (not_1_out, button_1_out);
  Clock clock_1 (.out(clock_1_out));
  and and_1 (and_1_out, not_1_out, clock_1_out);
  assign or_1_out = transistor_1_out | pull_resistor_1_node;  // OR_Gate or_1, 8 bits wide
  Pull_Resistor pull_resistor_1 (.node(pull_resistor_1_node));
  DipSwitch dipswitch_1 (
    .sw1(dipswitch_1_sw8[7]), .sw2(dipswitch_1_sw8[6]), .sw3(dipswitch_1_sw8[5]), .sw4(dipswitch_1_sw8[4]),
    .sw5(dipswitch_1_sw8[3]), .sw6(dipswitch_1_sw8[2]), .sw7(dipswitch_1_sw8[1]), .sw8(dipswitch_1_sw8[0]));
  core core_1 (
    .data_bus_in(or_1_out), .reset(button_1_out), .clk(and_1_out), .mem_write(core_1_mem_write),
    .mem_read(core_1_mem_read), .data_bus_out(core_1_data_bus_out), .address_bus(core_1_address_bus),
    .clk_out(core_1_clk_out), .io_in(core_1_io_in), .io_out(core_1_io_out), .timer_out(core_1_timer_out));  // open: int0, int1, int2, int3, int4, int5
  LED led_1 (.in(core_1_timer_out));
  io io_1 (
    .address_bus(core_1_address_bus), .address_config({16{1'b0}}), .data_bus_in(core_1_data_bus_out),
    .io_out(core_1_io_out), .clk(core_1_clk_out), .reset(button_1_out), .io_in(core_1_io_in),
    .data_bus_out(pull_resistor_1_node), .port_in(dipswitch_1_sw8), .port_out(io_1_port_out));
  LedBar ledbar_1 (
    .led0(io_1_port_out[7]), .led1(io_1_port_out[6]), .led2(io_1_port_out[5]), .led3(io_1_port_out[4]),
    .led4(io_1_port_out[3]), .led5(io_1_port_out[2]), .led6(io_1_port_out[1]), .led7(io_1_port_out[0]));
  ROM #(.addrWidth(15)) rom_1 (.addr(core_1_address_bus[14:0]), .data(rom_1_data));
  RAM #(.addrWidth(15), .enables("line"), .trigger("falling")) ram_1 (
    .addr(core_1_address_bus[14:0]), .we(and_4_out), .clk(and_5_out), .din(core_1_data_bus_out),
    .dout(ram_1_dout));
  not not_2 (not_2_out, core_1_address_bus[15]);
  and and_2 (and_2_out, not_2_out, core_1_mem_read);
  and and_3 (and_3_out, core_1_address_bus[15], core_1_mem_read);
  and and_4 (and_4_out, core_1_address_bus[15], core_1_mem_write);
  not not_3 (not_3_out, and_2_out);
  not not_4 (not_4_out, and_3_out);
  and and_5 (and_5_out, and_4_out, core_1_clk_out);
  Transistor transistor_1 (.in(rom_1_data[0]), .out(transistor_1_out[0]), .gate(not_3_out));
  Transistor transistor_2 (.in(rom_1_data[1]), .out(transistor_1_out[1]), .gate(not_3_out));
  Transistor transistor_3 (.in(rom_1_data[2]), .out(transistor_1_out[2]), .gate(not_3_out));
  Transistor transistor_4 (.in(rom_1_data[3]), .out(transistor_1_out[3]), .gate(not_3_out));
  Transistor transistor_5 (.in(rom_1_data[4]), .out(transistor_1_out[4]), .gate(not_3_out));
  Transistor transistor_6 (.in(rom_1_data[5]), .out(transistor_1_out[5]), .gate(not_3_out));
  Transistor transistor_7 (.in(rom_1_data[6]), .out(transistor_1_out[6]), .gate(not_3_out));
  Transistor transistor_8 (.in(rom_1_data[7]), .out(transistor_1_out[7]), .gate(not_3_out));
  Transistor transistor_9 (.in(ram_1_dout[0]), .out(transistor_1_out[0]), .gate(not_4_out));
  Transistor transistor_10 (.in(ram_1_dout[1]), .out(transistor_1_out[1]), .gate(not_4_out));
  Transistor transistor_11 (.in(ram_1_dout[2]), .out(transistor_1_out[2]), .gate(not_4_out));
  Transistor transistor_12 (.in(ram_1_dout[3]), .out(transistor_1_out[3]), .gate(not_4_out));
  Transistor transistor_13 (.in(ram_1_dout[4]), .out(transistor_1_out[4]), .gate(not_4_out));
  Transistor transistor_14 (.in(ram_1_dout[5]), .out(transistor_1_out[5]), .gate(not_4_out));
  Transistor transistor_15 (.in(ram_1_dout[6]), .out(transistor_1_out[6]), .gate(not_4_out));
  Transistor transistor_16 (.in(ram_1_dout[7]), .out(transistor_1_out[7]), .gate(not_4_out));
  Pull_Resistor pull_resistor_2 (.node(transistor_1_out));

  // Notes on the sheet:
  //   contents of rom_1 (hex, n*v repeats v):
  //   2 f 0 23 0 0 3a ff ff 35 3c 0 22 0 ff 2 4 40 3 4 0 22 1 ff 2 4 f 3 4 0 22 2 ff 2 4 1f 3 4 0 22 3 ff
  //   2 4 7 3 4 0 7 0 1 7 1 2 7 e 2 1d 30 0 3e f 0 37 f 0 3e 0 0 3e 1 0 3e e 0 22 0 80 11 e 0 d e 0 12 e 0
  //   22 0 0 3 e 0 3f e 0 3f 1 0 3f 0 0 36 f 0 3f f 0 26
endmodule
